// Logisim project cpu21-riscv.circ as structural Verilog: 28 circuits, main circuit ◇单周期RISC-V
module \单周期RISC_V  (
  input  IR1,
  input  IR2,
  input  IR3,
  output RegWrite,
  output MemWrite,
  output [31:0] PC,
  output [31:0] IR,
  output [31:0] RDin,
  output [31:0] MDin,
  output [31:0] LedData
);

  wire and_1_out, and_2_out, and_3_out, and_4_out, and_5_out, Beq, BGE, Bne, Branch, CLK, clock_1_out,
       comparator_1_eq, comparator_2_eq, comparator_2_lt, d_ff_1_q, ecall, Go, halt, IR1_t, IR2_t, IR3_t,
       IRA, IRB, IRC, JAL, JALR, LB, MemToReg, nand_1_out, not_1_out, not_2_out, or_5_out, RST, tunnel,
       tunnel_t, tunnel_t_t, URET, W1, W2, W3, \单周期硬布线控制器_1_alu_src , \单周期硬布线控制器_1_s_type ;
  wire [1:0] Addr, priority_encoder_1_out, priority_encoder_2_out;
  wire [3:0] \单周期硬布线控制器_1_alu_op ;
  wire [4:0] multiplexer_2_out, multiplexer_3_out;
  wire [12:0] CNT_num;
  wire [15:0] \总周期数 ;
  wire [31:0] B_Addr, bit_extender_1_out, bit_extender_2_out, bit_extender_3_out, bit_extender_4_out,
       bit_extender_5_out, bit_extender_6_out, bit_extender_7_out, bit_extender_8_out, \byte , Dout, J_Addr,
       multiplexer_1_out, multiplexer_4_out, multiplexer_5_out, PC_4, R1, shifter_1_out, shifter_2_out, word;
  wire [31:2] R;

  Button \u_总复位  (.out(RST));
  Button _1 (.out(IRA));
  Button _2 (.out(IRB));
  Button _3 (.out(IRC));
  Button \u_继续运行  (.out(Go));
  LED #(.active("true")) led_1 (.in(W1));
  LED #(.active("true")) led_2 (.in(W2));
  LED #(.active("true")) led_3 (.in(W3));
  and and_1 (and_1_out, Beq, tunnel_t);
  and and_2 (and_2_out, ~tunnel_t, Bne);  // AND_Gate
  and and_3 (and_3_out, tunnel_t_t, BGE);
  Hex_Digit_Display hex_digit_display_1 (.value(LedData[31:28]));  // open: dp
  or or_1 (Branch, and_1_out, and_2_out, and_3_out);
  Comparator #(.width(32), .mode("twosComplement")) comparator_1 (
    .a(R1), .b(32'ha), .eq(comparator_1_eq));  // open: gt, lt
  Hex_Digit_Display hex_digit_display_2 (.value(LedData[27:24]));  // open: dp
  Hex_Digit_Display hex_digit_display_3 (.value(LedData[23:20]));  // open: dp
  and and_4 (and_4_out, ecall, ~comparator_1_eq);  // AND_Gate
  and and_5 (and_5_out, ecall, comparator_1_eq);
  Hex_Digit_Display hex_digit_display_4 (.value(LedData[19:16]));  // open: dp
  Hex_Digit_Display hex_digit_display_5 (.value(LedData[15:12]));  // open: dp
  Priority_Encoder #(.select(2), .disabled("Z")) priority_encoder_1 (
    .in0(1'b1), .in1(Branch), .in2(JAL), .in3(JALR), .out(priority_encoder_1_out));  // open: gs, en_out, en_in
  Register #(.width(32), .trigger("rising"), .Select("low")) u_PC (
    .D(MDin), .en(and_4_out), .Q(LedData), .clk(CLK));  // open: clr
  and and_6 (halt, and_5_out, ~Go);  // AND_Gate
  Hex_Digit_Display hex_digit_display_6 (.value(LedData[7:4]));  // open: dp
  Hex_Digit_Display hex_digit_display_7 (.value(LedData[11:8]));  // open: dp
  // Probe on \总周期数 
  Multiplexer #(.select(2), .width(32), .disabled("Z"), .enable("false")) multiplexer_1 (
    .in0(PC_4), .in1(B_Addr), .in2(J_Addr), .in3({R, Addr}), .out(multiplexer_1_out),
    .sel(priority_encoder_1_out));
  not not_1 (not_1_out, halt);
  Hex_Digit_Display hex_digit_display_8 (.value(LedData[3:0]));  // open: dp
  Register #(.width(32), .trigger("rising"), .Select("low")) PC_2 (
    .D(multiplexer_1_out), .en(not_1_out), .Q(PC), .clk(CLK), .clr(RST));
  not not_2 (not_2_out, halt);
  Counter #(.width(16), .max('hffff), .ongoal("stay"), .trigger("rising"), .behavior("old")) counter_1 (
    .count(not_2_out), .Q(\总周期数 ), .clk(CLK), .clr(RST));  // open: load, D, carry, preset
  or or_2 (IR1_t, IR1, IRA);
  // RiscV_Probe riscv_probe_1: pin names not known; wires that end beside it: IR
  ROM #(.addrWidth(10), .dataWidth(32), .Select("high")) rom_1 (.addr(PC[11:2]), .data(IR));
  Adder #(.width(32)) adder_1 (.a(PC), .b(32'h4), .out(PC_4));  // open: cin, cout
  or or_3 (IR2_t, IR2, IRB);
  \单周期硬布线控制器  \u_单周期硬布线控制器_1  (
    .Funct({IR[30], IR[25], IR[14:12]}), .OP(IR[6:2]), .ALU_OP(\单周期硬布线控制器_1_alu_op ), .MemToReg(MemToReg),
    .MemWrite(MemWrite), .ALU_SRC(\单周期硬布线控制器_1_alu_src ), .RegWrite(RegWrite), .ecall(ecall),
    .S_type(\单周期硬布线控制器_1_s_type ), .Jalr(JALR), .Beq(Beq), .JAL(JAL), .Bne(Bne), .in_3(IR[21]), .uret(URET),
    .LB(LB), .BGE(BGE));  // open: CSRRSI, CSRRCI
  Multiplexer #(.select(1), .width(5), .disabled("Z"), .enable("false")) multiplexer_2 (
    .in0(IR[19:15]), .in1(5'b10001), .out(multiplexer_2_out), .sel(ecall));
  Multiplexer #(.select(1), .width(5), .disabled("Z"), .enable("false")) multiplexer_3 (
    .in0(IR[24:20]), .in1(5'b01010), .out(multiplexer_3_out), .sel(ecall));
  assign bit_extender_1_out = {{20{IR[31]}}, IR[31:20]};  // Bit_Extender bit_extender_1
  assign bit_extender_2_out = {{20{IR[31]}}, {IR[31:25], IR[11:7]}};  // Bit_Extender bit_extender_2
  or or_4 (IR3_t, IR3, IRC);
  Multiplexer #(.select(1), .width(32), .disabled("Z"), .enable("false")) multiplexer_4 (
    .in0(bit_extender_1_out), .in1(bit_extender_2_out), .out(multiplexer_4_out), .sel(\单周期硬布线控制器_1_s_type ));
  assign bit_extender_3_out = {{20{IR[31]}}, {IR[31], IR[7], IR[30:25], IR[11:8]}};  // Bit_Extender bit_extender_3
  assign bit_extender_4_out = {{12{IR[31]}}, {IR[31], IR[19:12], IR[20], IR[30:21]}};  // Bit_Extender bit_extender_4
  Shifter #(.width(32), .shift("ll")) shifter_1 (.in(bit_extender_3_out), .\dist (5'b00001), .out(shifter_1_out));
  Shifter #(.width(32), .shift("ll")) shifter_2 (.in(bit_extender_4_out), .\dist (5'b00001), .out(shifter_2_out));
  Regifile regifile_1 (
    .Din(RDin), .Clk(CLK), .R1(R1), .R2(MDin), .WE(RegWrite), .W_num(IR[11:7]), .R1_num(multiplexer_2_out),
    .R2_num(multiplexer_3_out));
  Adder #(.width(32)) adder_2 (.a(shifter_1_out), .b(PC), .out(B_Addr));  // open: cin, cout
  Adder #(.width(32)) adder_3 (.a(shifter_2_out), .b(PC), .out(J_Addr));  // open: cin, cout
  Multiplexer #(.select(1), .width(32), .disabled("Z"), .enable("false")) multiplexer_5 (
    .in0(MDin), .in1(multiplexer_4_out), .out(multiplexer_5_out), .sel(\单周期硬布线控制器_1_alu_src ));
  ALU alu_1 (
    .X(R1), .Y(multiplexer_5_out), .AluOP(\单周期硬布线控制器_1_alu_op ), .Equal(tunnel_t), .Result({R, Addr}),
    .out_4(tunnel_t_t), .out_6(tunnel));  // open: Result_2
  D_Flip_Flop #(.trigger("high"), .Pre_Clr_Positions("LEGACY"), .NegatePresetClear("false"), .enable("true"), .NewFFLayout("false")) d_ff_1 (.Q(d_ff_1_q));  // open: clk, D, Qn, preset, en, reset
  // Probe on 13'hc
  or or_5 (or_5_out, JAL, JALR);
  RAM #(.addrWidth(10), .dataWidth(32), .bus("separate"), .Select("high")) ram_1 (
    .addr(R[11:2]), .din(MDin), .data(Dout), .str(MemWrite), .clk(CLK), .clr(RST));  // open: sel, ld
  Comparator #(.width(13), .mode("twosComplement")) comparator_2 (
    .a(CNT_num), .b(13'hc), .eq(comparator_2_eq), .lt(comparator_2_lt));  // open: gt
  Clock #(.highDuration(1), .lowDuration(1)) clock_1 (.out(clock_1_out));
  Priority_Encoder #(.select(2), .disabled("Z")) priority_encoder_2 (
    .in0(1'b1), .in1(MemToReg), .in2(or_5_out), .out(priority_encoder_2_out));  // open: in3, gs, en_out, en_in
  Counter #(.width(13), .max('h1fff), .ongoal("stay"), .trigger("rising"), .behavior("old")) counter_2 (
    .count(comparator_2_lt), .Q(CNT_num), .clk(clock_1_out));  // open: load, D, carry, clr, preset
  Multiplexer #(.select(2), .width(32), .disabled("Z"), .enable("false")) multiplexer_6 (
    .in0({R, Addr}), .in1(Dout), .in2(PC_4), .out(word), .sel(priority_encoder_2_out));  // open: in3
  nand nand_1 (nand_1_out, d_ff_1_q, comparator_2_eq);
  Multiplexer #(.select(1), .width(32), .disabled("Z"), .enable("false")) multiplexer_7 (
    .in0(word), .in1(\byte ), .out(RDin), .sel(LB));
  assign CLK = nand_1_out ? clock_1_out : 1'bz;  // Controlled_Buffer controlled_buffer_1
  Pull_Resistor #(.pull(1)) pull_resistor_1 (.node(CLK));
  assign bit_extender_5_out = {{24{word[7]}}, word[7:0]};  // Bit_Extender bit_extender_5
  assign bit_extender_6_out = {{24{word[15]}}, word[15:8]};  // Bit_Extender bit_extender_6
  assign bit_extender_7_out = {{24{word[23]}}, word[23:16]};  // Bit_Extender bit_extender_7
  assign bit_extender_8_out = {{24{word[31]}}, word[31:24]};  // Bit_Extender bit_extender_8
  Multiplexer #(.select(2), .width(32), .disabled("Z"), .enable("false")) multiplexer_8 (
    .in0(bit_extender_5_out), .in1(bit_extender_6_out), .in2(bit_extender_7_out), .in3(bit_extender_8_out),
    .out(\byte ), .sel(Addr));

  // Other names for the same wires on the sheet: R[1:0] = Addr

  // Notes on the sheet:
  //   中断源
  //   中断等待指示
  //   数码管输出应该用寄存器锁存，否则显示数据只能一闪而过
  //   数码管输出
  //   指令探针
  //   指令存储器
  //   contents of rom_1 (hex, n*v repeats v):
  //   100493 100006f 100493 200913 300993 100006f 100493 200913 300993 100006f 100493 200913 300993
  //   100006f 100493 200913 300993 3d0000ef 100413 100493 1f49493 900533 2200893 73 24d493 48463 fedff06f
  //   900533 2200893 73 100493 249493 900533 2200893 73 48463 fedff06f 100493 1f49493 900533 2200893 73
  //   4034d493 900533 2200893 73 4044d493 900533 2200893 73 4044d493 900533 2200893 73 4044d493 900533
  //   2200893 73 4044d493 900533 2200893 73 4044d493 900533 2200893 73 4044d493 900533 2200893 73 4044d493
  //   900533 2200893 73 100413 1f41993 41f9d993 433 c00913 300b13 140413 f47413 800293 100313 499993
  //   89e9b3 1300533 2200893 73 406282b3 fe0294e3 140413 f00f93 1f47433 1c41413 800293 100313 49d993
  //   89e9b3 1300533 2200893 73 406282b3 fe0294e3 1c45413 406b0b33 b0463 f95ff06f 2b3 fff2c293 829293
  //   ff2e293 500533 2200893 73 fff00413 493 84a023 140413 448493 84a023 140413 448493 84a023 140413
  //   448493 84a023 140413 448493 84a023 140413 448493 84a023 140413 448493 84a023 140413 448493 84a023
  //   140413 448493 84a023 140413 448493 84a023 140413 448493 84a023 140413 448493 84a023 140413 448493
  //   84a023 140413 448493 84a023 140413 448493 84a023 140413 448493 84a023 140413 448493 140413 433
  //   3c00493 42983 4aa03 149a2b3 28663 134a023 1442023 ffc48493 fe9412e3 800533 2200893 73 440413 3c00493
  //   fc9416e3 a00893 73 100293 300313 800493 849493 7648493 900533 2200893 73 800e13 5494b3 6494b3 900533
  //   2200893 73 fffe0e13 fe0e14e3 a00893 73 100293 300313 800493 849493 7648493 1449493 900533 2200893 73
  //   800e13 54d4b3 64d4b3 900533 2200893 73 fffe0e13 fe0e14e3 a00893 73 313 1000e13 8400493 849493
  //   8348493 400913 891913 490913 849493 8248493 849493 8148493 891913 490913 891913 490913 932023
  //   12484b3 430313 fffe0e13 fe0e18e3 2000e13 313 30483 900533 2200893 73 130313 fffe0e13 fe0e14e3 a00893
  //   73 f00493 900533 2200893 73 fff48493 fe04d8e3 a00893 73 413 140413 800533 2200893 73 240413 800533
  //   2200893 73 340413 800533 2200893 73 440413 800533 2200893 73 540413 800533 2200893 73 640413 800533
  //   2200893 73 740413 800533 2200893 73 840413 800533 2200893 2200893 73 8067
  //   指令字
  //   JAL
  //   JALR
  //   URET
  //   Beq
  //   Bne
  //   MemToReg
  //   MemWrite
  //   AluOP
  //   AluSrcB
  //   RegWrite
  //   S_Type
  //   为方便自动评测，需要输出PC，IR，寄存器堆写如数据RDin
  //   RAM写使能MemWrite、RAM写入数据MDin等信号
  //   数据存储器
  //   控制位
  //   暂停节拍，不能为0
  //   戳工具置1进入计数暂停模式，ctrl+k时钟自动运行到对应节拍暂停
  //   ctrl+k关闭时钟连续运行，将控制位置零，进入单步调试模式调试
  //   用这个时钟源需要去掉电路中的其他时钟源
  //   可计数暂停的时钟源
endmodule

// 单周期硬布线控制器
module \单周期硬布线控制器  (
  input  [4:0] OP,
  input  [4:0] Funct,
  input  in_3,
  output [3:0] ALU_OP,
  output uret,
  output MemToReg,
  output ecall,
  output MemWrite,
  output ALU_SRC,
  output RegWrite,
  output S_type,
  output Beq,
  output Bne,
  output Jalr,
  output JAL,
  output LB,
  output BGE,
  output CSRRSI,
  output CSRRCI
);

  wire \控制信号自动生成_1_ecall ;

  \运算控制器自动生成  \u_运算控制器自动生成_1  (
    .OP2(OP[0]), .OP3(OP[1]), .OP4(OP[2]), .OP5(OP[3]), .OP6(OP[4]), .F12(Funct[0]), .F13(Funct[1]),
    .F14(Funct[2]), .F25(Funct[3]), .F30(Funct[4]), .S0(ALU_OP[0]), .S1(ALU_OP[1]), .S2(ALU_OP[2]),
    .S3(ALU_OP[3]));
  \控制信号自动生成  \u_控制信号自动生成_1  (
    .OP2(OP[0]), .OP3(OP[1]), .MemToReg(MemToReg), .OP4(OP[2]), .OP5(OP[3]), .OP6(OP[4]), .F12(Funct[0]),
    .MemWrite(MemWrite), .F13(Funct[1]), .F14(Funct[2]), .F25(Funct[3]), .F30(Funct[4]), .ALU_SRC(ALU_SRC),
    .CSRRSI(CSRRSI), .CSRRCI(CSRRCI), .RegWrite(RegWrite), .ecall(\控制信号自动生成_1_ecall ), .S_Type(S_type),
    .BEQ(Beq), .BNE(Bne), .JALR(Jalr), .JAL(JAL), .LB(LB), .BGE(BGE));
  and and_1 (uret, in_3, \控制信号自动生成_1_ecall );
  and and_2 (ecall, ~in_3, \控制信号自动生成_1_ecall );  // AND_Gate

  // Other names for the same wires on the sheet: IR21 = in_3; OP_CODE[4:0] = OP

  // Notes on the sheet:
  //   控制信号生成，产生数据通路需要的其他控制信号
  //   运算器控制器，根据指令生成运算器功能选择信号
endmodule

// 运算器控制器
module \运算控制器自动生成  (
  input  OP2,
  input  OP3,
  input  OP4,
  input  OP5,
  input  OP6,
  input  F12,
  input  F13,
  input  F14,
  input  F25,
  input  F30,
  output S0,
  output S1,
  output S2,
  output S3
);

  wire and_1_out, and_2_out, and_3_out, and_4_out, and_5_out, and_6_out, and_7_out, and_8_out, and_9_out,
       and_10_out, and_11_out, and_12_out, and_13_out, and_14_out, and_15_out, and_16_out, and_17_out,
       and_18_out, and_19_out, and_20_out, and_21_out, and_22_out, and_23_out, and_24_out, and_25_out,
       and_26_out, and_27_out, not_1_out, not_2_out, not_3_out, not_4_out, not_5_out, not_6_out, not_7_out,
       not_8_out, not_9_out, not_10_out, not_11_out, not_12_out, not_13_out, not_14_out, not_15_out,
       not_16_out, not_17_out, not_18_out, not_19_out, not_20_out, not_21_out, not_22_out, not_23_out,
       not_24_out, not_25_out, not_26_out, not_27_out, not_28_out, not_29_out, not_30_out, not_31_out,
       not_32_out, not_33_out, not_34_out, not_35_out, not_36_out, not_37_out, not_38_out, not_39_out,
       not_40_out, not_41_out, not_42_out, not_43_out, not_44_out, not_45_out, not_46_out, not_47_out,
       not_48_out, not_49_out, not_50_out, not_51_out, not_52_out, not_53_out, not_54_out, not_55_out,
       not_56_out, not_57_out, not_58_out, not_59_out, not_60_out, not_61_out, not_62_out, not_63_out,
       not_64_out, not_65_out, not_66_out, not_67_out, not_68_out, not_69_out, not_70_out, not_71_out,
       not_72_out, not_73_out, not_74_out, not_75_out, not_76_out, not_77_out, not_78_out, not_79_out,
       not_80_out, not_81_out, not_82_out, not_83_out, not_84_out, not_85_out, not_86_out, not_87_out,
       not_88_out, not_89_out, not_90_out, not_91_out, not_92_out, not_93_out, not_94_out, not_95_out,
       not_96_out, not_97_out, not_98_out, not_99_out, not_100_out, not_101_out, not_102_out, not_103_out,
       not_104_out, not_105_out, not_106_out, not_107_out, not_108_out, not_109_out, not_110_out,
       not_111_out, not_112_out, not_113_out, not_114_out, not_115_out, not_116_out, not_117_out,
       not_118_out, not_119_out, not_120_out, not_121_out, not_122_out, not_123_out, not_124_out,
       not_125_out, not_126_out, not_127_out, not_128_out, not_129_out, not_130_out, not_131_out,
       not_132_out, not_133_out, not_134_out, not_135_out, not_136_out, not_137_out, not_138_out,
       not_139_out, not_140_out, not_141_out, not_142_out, not_143_out, not_144_out, not_145_out,
       not_146_out, not_147_out, not_148_out, not_149_out, not_150_out;

  not not_1 (not_1_out, F30);
  not not_2 (not_2_out, F25);
  not not_3 (not_3_out, F14);
  not not_4 (not_4_out, F13);
  not not_5 (not_5_out, F12);
  not not_6 (not_6_out, OP6);
  not not_7 (not_7_out, OP3);
  not not_8 (not_8_out, OP2);
  not not_9 (not_9_out, F30);
  not not_10 (not_10_out, F25);
  not not_11 (not_11_out, OP6);
  not not_12 (not_12_out, OP3);
  not not_13 (not_13_out, OP2);
  not not_14 (not_14_out, F30);
  not not_15 (not_15_out, F25);
  not not_16 (not_16_out, F14);
  not not_17 (not_17_out, F12);
  not not_18 (not_18_out, OP6);
  not not_19 (not_19_out, OP3);
  not not_20 (not_20_out, OP2);
  not not_21 (not_21_out, F14);
  not not_22 (not_22_out, F13);
  not not_23 (not_23_out, F12);
  not not_24 (not_24_out, OP6);
  not not_25 (not_25_out, OP5);
  not not_26 (not_26_out, OP3);
  not not_27 (not_27_out, OP2);
  not not_28 (not_28_out, OP6);
  not not_29 (not_29_out, OP5);
  not not_30 (not_30_out, OP3);
  not not_31 (not_31_out, OP2);
  not not_32 (not_32_out, F13);
  not not_33 (not_33_out, F12);
  not not_34 (not_34_out, OP6);
  not not_35 (not_35_out, OP5);
  not not_36 (not_36_out, OP3);
  not not_37 (not_37_out, OP2);
  not not_38 (not_38_out, F14);
  not not_39 (not_39_out, F12);
  not not_40 (not_40_out, OP6);
  not not_41 (not_41_out, OP5);
  not not_42 (not_42_out, OP3);
  not not_43 (not_43_out, OP2);
  not not_44 (not_44_out, F25);
  not not_45 (not_45_out, F13);
  not not_46 (not_46_out, OP6);
  not not_47 (not_47_out, OP5);
  not not_48 (not_48_out, OP3);
  not not_49 (not_49_out, OP2);
  not not_50 (not_50_out, F13);
  not not_51 (not_51_out, OP4);
  not not_52 (not_52_out, OP3);
  not not_53 (not_53_out, OP2);
  not not_54 (not_54_out, OP3);
  not not_55 (not_55_out, OP4);
  not not_56 (not_56_out, F12);
  not not_57 (not_57_out, F13);
  not not_58 (not_58_out, F14);
  not not_59 (not_59_out, OP2);
  not not_60 (not_60_out, OP3);
  not not_61 (not_61_out, OP4);
  not not_62 (not_62_out, F13);
  not not_63 (not_63_out, OP2);
  not not_64 (not_64_out, OP3);
  not not_65 (not_65_out, OP5);
  not not_66 (not_66_out, OP6);
  not not_67 (not_67_out, F12);
  not not_68 (not_68_out, F14);
  not not_69 (not_69_out, OP2);
  not not_70 (not_70_out, OP3);
  not not_71 (not_71_out, OP6);
  not not_72 (not_72_out, F12);
  not not_73 (not_73_out, F14);
  not not_74 (not_74_out, F25);
  not not_75 (not_75_out, F30);
  not not_76 (not_76_out, OP2);
  not not_77 (not_77_out, OP3);
  not not_78 (not_78_out, OP6);
  not not_79 (not_79_out, F25);
  not not_80 (not_80_out, F30);
  not not_81 (not_81_out, OP2);
  not not_82 (not_82_out, OP3);
  not not_83 (not_83_out, OP5);
  not not_84 (not_84_out, OP6);
  not not_85 (not_85_out, OP2);
  not not_86 (not_86_out, OP3);
  not not_87 (not_87_out, OP6);
  not not_88 (not_88_out, F12);
  not not_89 (not_89_out, F13);
  not not_90 (not_90_out, F14);
  not not_91 (not_91_out, F25);
  not not_92 (not_92_out, OP2);
  not not_93 (not_93_out, OP3);
  not not_94 (not_94_out, OP4);
  not not_95 (not_95_out, F13);
  not not_96 (not_96_out, F14);
  not not_97 (not_97_out, OP3);
  not not_98 (not_98_out, OP4);
  not not_99 (not_99_out, F12);
  not not_100 (not_100_out, F13);
  not not_101 (not_101_out, F14);
  not not_102 (not_102_out, OP2);
  not not_103 (not_103_out, OP3);
  not not_104 (not_104_out, OP5);
  not not_105 (not_105_out, OP6);
  not not_106 (not_106_out, F12);
  not not_107 (not_107_out, F13);
  not not_108 (not_108_out, F14);
  not not_109 (not_109_out, OP2);
  not not_110 (not_110_out, OP3);
  not not_111 (not_111_out, OP6);
  not not_112 (not_112_out, F12);
  not not_113 (not_113_out, F13);
  not not_114 (not_114_out, F14);
  not not_115 (not_115_out, F25);
  not not_116 (not_116_out, OP2);
  not not_117 (not_117_out, OP3);
  not not_118 (not_118_out, OP5);
  not not_119 (not_119_out, OP6);
  not not_120 (not_120_out, OP2);
  not not_121 (not_121_out, OP3);
  not not_122 (not_122_out, OP6);
  not not_123 (not_123_out, F25);
  not not_124 (not_124_out, F30);
  not not_125 (not_125_out, OP2);
  not not_126 (not_126_out, OP3);
  not not_127 (not_127_out, OP4);
  not not_128 (not_128_out, F13);
  not not_129 (not_129_out, OP2);
  not not_130 (not_130_out, OP3);
  not not_131 (not_131_out, OP5);
  not not_132 (not_132_out, OP6);
  not not_133 (not_133_out, F12);
  not not_134 (not_134_out, OP2);
  not not_135 (not_135_out, OP3);
  not not_136 (not_136_out, OP5);
  not not_137 (not_137_out, OP6);
  not not_138 (not_138_out, F12);
  not not_139 (not_139_out, OP2);
  not not_140 (not_140_out, OP3);
  not not_141 (not_141_out, OP6);
  not not_142 (not_142_out, F12);
  not not_143 (not_143_out, F25);
  not not_144 (not_144_out, F30);
  not not_145 (not_145_out, OP2);
  not not_146 (not_146_out, OP3);
  not not_147 (not_147_out, OP6);
  not not_148 (not_148_out, F14);
  not not_149 (not_149_out, F25);
  not not_150 (not_150_out, F30);
  and and_1 (and_1_out, not_1_out, not_2_out, not_3_out, not_4_out, not_5_out, not_6_out, OP5, OP4, not_7_out, not_8_out);
  and and_2 (and_2_out, not_9_out, not_10_out, F14, F13, F12, not_11_out, OP5, OP4, not_12_out, not_13_out);
  and and_3 (and_3_out, not_14_out, not_15_out, not_16_out, F13, not_17_out, not_18_out, OP5, OP4, not_19_out, not_20_out);
  and and_4 (and_4_out, not_21_out, not_22_out, not_23_out, not_24_out, not_25_out, OP4, not_26_out, not_27_out);
  and and_5 (and_5_out, F14, F13, F12, not_28_out, not_29_out, OP4, not_30_out, not_31_out);
  and and_6 (and_6_out, F14, not_32_out, not_33_out, not_34_out, not_35_out, OP4, not_36_out, not_37_out);
  and and_7 (and_7_out, not_38_out, F13, not_39_out, not_40_out, not_41_out, OP4, not_42_out, not_43_out);
  and and_8 (and_8_out, F30, not_44_out, F14, not_45_out, F12, not_46_out, not_47_out, OP4, not_48_out, not_49_out);
  and and_9 (and_9_out, F14, not_50_out, F12, OP6, OP5, not_51_out, not_52_out, not_53_out);
  and and_10 (and_10_out, not_54_out, not_55_out, OP5, OP6, not_56_out, not_57_out, not_58_out);
  and and_11 (and_11_out, not_59_out, not_60_out, not_61_out, OP5, OP6, F12, not_62_out);
  and and_12 (and_12_out, not_63_out, not_64_out, OP4, not_65_out, not_66_out, not_67_out, F13, not_68_out);
  and and_13 (and_13_out, not_69_out, not_70_out, OP4, not_71_out, not_72_out, F13, not_73_out, not_74_out, not_75_out);
  and and_14 (and_14_out, not_76_out, not_77_out, OP4, not_78_out, F12, F14, not_79_out, not_80_out);
  and and_15 (and_15_out, not_81_out, not_82_out, OP4, not_83_out, not_84_out, F12, F13, F14);
  and and_16 (and_16_out, not_85_out, not_86_out, OP4, OP5, not_87_out, not_88_out, not_89_out, not_90_out, not_91_out, F30);
  and and_17 (and_17_out, not_92_out, not_93_out, not_94_out, OP5, OP6, not_95_out, not_96_out);
  and and_18 (and_18_out, not_97_out, not_98_out, OP5, OP6, not_99_out, not_100_out, not_101_out);
  and and_19 (and_19_out, not_102_out, not_103_out, OP4, not_104_out, not_105_out, not_106_out, not_107_out, not_108_out);
  and and_20 (and_20_out, not_109_out, not_110_out, OP4, not_111_out, not_112_out, not_113_out, not_114_out, not_115_out);
  and and_21 (and_21_out, not_116_out, not_117_out, OP4, not_118_out, not_119_out, F12, F13, F14);
  and and_22 (and_22_out, not_120_out, not_121_out, OP4, OP5, not_122_out, F12, F13, not_123_out, not_124_out);
  and and_23 (and_23_out, not_125_out, not_126_out, not_127_out, OP5, OP6, F12, not_128_out, F14);
  and and_24 (and_24_out, not_129_out, not_130_out, OP4, not_131_out, not_132_out, not_133_out, F14);
  and and_25 (and_25_out, not_134_out, not_135_out, OP4, not_136_out, not_137_out, not_138_out, F13);
  and and_26 (and_26_out, not_139_out, not_140_out, OP4, not_141_out, not_142_out, F13, not_143_out, not_144_out);
  and and_27 (and_27_out, not_145_out, not_146_out, OP4, OP5, not_147_out, F13, not_148_out, not_149_out, not_150_out);
  or or_1 (S2, and_17_out, and_18_out, and_19_out, and_20_out, and_21_out, and_22_out);
  or or_2 (S3, and_23_out, and_24_out, and_25_out, and_26_out, and_27_out);
  or or_3 (S0, and_1_out, and_2_out, and_3_out, and_4_out, and_5_out, and_6_out, and_7_out, and_8_out, and_9_out);
  or or_4 (S1, and_10_out, and_11_out, and_12_out, and_13_out, and_14_out, and_15_out, and_16_out);
endmodule

// 控制信号生成
module \控制信号自动生成  (
  input  OP2,
  input  OP3,
  input  OP4,
  input  OP5,
  input  OP6,
  input  F12,
  input  F13,
  input  F14,
  input  F25,
  input  F30,
  output MemToReg,
  output MemWrite,
  output ALU_SRC,
  output CSRRSI,
  output CSRRCI,
  output RegWrite,
  output ecall,
  output S_Type,
  output BEQ,
  output BNE,
  output JALR,
  output JAL,
  output LB,
  output BGE
);

  wire and_3_out, and_4_out, and_5_out, and_6_out, and_7_out, and_8_out, and_9_out, and_12_out, and_13_out,
       and_14_out, and_15_out, and_16_out, and_17_out, and_18_out, and_19_out, and_20_out, and_21_out,
       not_1_out, not_2_out, not_3_out, not_4_out, not_5_out, not_6_out, not_7_out, not_8_out, not_9_out,
       not_10_out, not_11_out, not_12_out, not_13_out, not_14_out, not_15_out, not_16_out, not_17_out,
       not_18_out, not_19_out, not_20_out, not_21_out, not_22_out, not_23_out, not_24_out, not_25_out,
       not_26_out, not_27_out, not_28_out, not_29_out, not_30_out, not_31_out, not_32_out, not_33_out,
       not_34_out, not_35_out, not_36_out, not_37_out, not_38_out, not_39_out, not_40_out, not_41_out,
       not_42_out, not_43_out, not_44_out, not_45_out, not_46_out, not_47_out, not_48_out, not_49_out,
       not_50_out, not_51_out, not_52_out, not_53_out, not_54_out, not_55_out, not_56_out, not_57_out,
       not_58_out, not_59_out, not_60_out, not_61_out, not_62_out, not_63_out, not_64_out, not_65_out,
       not_66_out, not_67_out, not_68_out, not_69_out, not_70_out, not_71_out, not_72_out, not_73_out,
       not_74_out, not_75_out, not_76_out, not_77_out, not_78_out, not_79_out, not_80_out, not_81_out,
       not_82_out, not_83_out, not_84_out, not_85_out, not_86_out, not_87_out, not_88_out, not_89_out,
       not_90_out, not_91_out, not_92_out, not_93_out, not_94_out, not_95_out, not_96_out, not_97_out,
       not_98_out, not_99_out, not_100_out, not_101_out, not_102_out, not_103_out, not_104_out, not_105_out,
       not_106_out, not_107_out, not_108_out, not_109_out, not_110_out, not_111_out, not_112_out,
       not_113_out, not_114_out, not_115_out, not_116_out, not_117_out, not_118_out, not_119_out,
       not_120_out, not_121_out, not_122_out, not_123_out, not_124_out, not_125_out, not_126_out,
       not_127_out, not_128_out, not_129_out, not_130_out, not_131_out, not_132_out, not_133_out,
       not_134_out, not_135_out, not_136_out, not_137_out, not_138_out, not_139_out, not_140_out,
       not_141_out, not_142_out, not_143_out, not_144_out, not_145_out, not_146_out, not_147_out, not_148_out;

  not not_1 (not_1_out, OP2);
  not not_2 (not_2_out, OP3);
  not not_3 (not_3_out, OP4);
  not not_4 (not_4_out, OP5);
  not not_5 (not_5_out, OP6);
  not not_6 (not_6_out, F12);
  not not_7 (not_7_out, F14);
  not not_8 (not_8_out, OP2);
  not not_9 (not_9_out, OP3);
  not not_10 (not_10_out, OP4);
  not not_11 (not_11_out, OP6);
  not not_12 (not_12_out, F12);
  not not_13 (not_13_out, F14);
  not not_14 (not_14_out, OP2);
  not not_15 (not_15_out, OP3);
  not not_16 (not_16_out, OP5);
  not not_17 (not_17_out, OP6);
  not not_18 (not_18_out, F12);
  not not_19 (not_19_out, F14);
  not not_20 (not_20_out, OP2);
  not not_21 (not_21_out, OP3);
  not not_22 (not_22_out, OP4);
  not not_23 (not_23_out, OP6);
  not not_24 (not_24_out, F12);
  not not_25 (not_25_out, F14);
  not not_26 (not_26_out, OP2);
  not not_27 (not_27_out, OP3);
  not not_28 (not_28_out, OP5);
  not not_29 (not_29_out, OP6);
  not not_30 (not_30_out, F12);
  not not_31 (not_31_out, OP2);
  not not_32 (not_32_out, OP3);
  not not_33 (not_33_out, OP5);
  not not_34 (not_34_out, OP6);
  not not_35 (not_35_out, F13);
  not not_36 (not_36_out, F25);
  not not_37 (not_37_out, F30);
  not not_38 (not_38_out, OP2);
  not not_39 (not_39_out, OP3);
  not not_40 (not_40_out, OP5);
  not not_41 (not_41_out, OP6);
  not not_42 (not_42_out, F25);
  not not_43 (not_43_out, OP2);
  not not_44 (not_44_out, OP3);
  not not_45 (not_45_out, OP5);
  not not_46 (not_46_out, OP6);
  not not_47 (not_47_out, OP3);
  not not_48 (not_48_out, OP4);
  not not_49 (not_49_out, F12);
  not not_50 (not_50_out, F13);
  not not_51 (not_51_out, F14);
  not not_52 (not_52_out, F12);
  not not_53 (not_53_out, OP3);
  not not_54 (not_54_out, OP2);
  not not_55 (not_55_out, OP3);
  not not_56 (not_56_out, OP2);
  not not_57 (not_57_out, OP2);
  not not_58 (not_58_out, OP3);
  not not_59 (not_59_out, OP5);
  not not_60 (not_60_out, OP6);
  not not_61 (not_61_out, F12);
  not not_62 (not_62_out, F14);
  not not_63 (not_63_out, OP2);
  not not_64 (not_64_out, OP3);
  not not_65 (not_65_out, OP5);
  not not_66 (not_66_out, OP6);
  not not_67 (not_67_out, F12);
  not not_68 (not_68_out, OP2);
  not not_69 (not_69_out, OP3);
  not not_70 (not_70_out, OP6);
  not not_71 (not_71_out, F12);
  not not_72 (not_72_out, F13);
  not not_73 (not_73_out, F14);
  not not_74 (not_74_out, F25);
  not not_75 (not_75_out, OP2);
  not not_76 (not_76_out, OP3);
  not not_77 (not_77_out, OP6);
  not not_78 (not_78_out, F13);
  not not_79 (not_79_out, F14);
  not not_80 (not_80_out, F25);
  not not_81 (not_81_out, F30);
  not not_82 (not_82_out, OP2);
  not not_83 (not_83_out, OP3);
  not not_84 (not_84_out, OP5);
  not not_85 (not_85_out, OP6);
  not not_86 (not_86_out, F25);
  not not_87 (not_87_out, OP2);
  not not_88 (not_88_out, OP3);
  not not_89 (not_89_out, OP6);
  not not_90 (not_90_out, F12);
  not not_91 (not_91_out, F25);
  not not_92 (not_92_out, F30);
  not not_93 (not_93_out, OP2);
  not not_94 (not_94_out, OP3);
  not not_95 (not_95_out, OP5);
  not not_96 (not_96_out, OP6);
  not not_97 (not_97_out, OP2);
  not not_98 (not_98_out, OP3);
  not not_99 (not_99_out, OP6);
  not not_100 (not_100_out, F25);
  not not_101 (not_101_out, F30);
  not not_102 (not_102_out, OP4);
  not not_103 (not_103_out, F12);
  not not_104 (not_104_out, F13);
  not not_105 (not_105_out, F14);
  not not_106 (not_106_out, OP4);
  not not_107 (not_107_out, OP2);
  not not_108 (not_108_out, OP3);
  not not_109 (not_109_out, F12);
  not not_110 (not_110_out, F13);
  not not_111 (not_111_out, F14);
  not not_112 (not_112_out, F25);
  not not_113 (not_113_out, F30);
  not not_114 (not_114_out, OP2);
  not not_115 (not_115_out, OP3);
  not not_116 (not_116_out, OP4);
  not not_117 (not_117_out, OP6);
  not not_118 (not_118_out, F12);
  not not_119 (not_119_out, F14);
  not not_120 (not_120_out, OP2);
  not not_121 (not_121_out, OP3);
  not not_122 (not_122_out, OP4);
  not not_123 (not_123_out, F12);
  not not_124 (not_124_out, F13);
  not not_125 (not_125_out, F14);
  not not_126 (not_126_out, OP2);
  not not_127 (not_127_out, OP3);
  not not_128 (not_128_out, OP4);
  not not_129 (not_129_out, F13);
  not not_130 (not_130_out, F14);
  not not_131 (not_131_out, OP3);
  not not_132 (not_132_out, OP4);
  not not_133 (not_133_out, F12);
  not not_134 (not_134_out, F13);
  not not_135 (not_135_out, F14);
  not not_136 (not_136_out, OP4);
  not not_137 (not_137_out, OP2);
  not not_138 (not_138_out, OP3);
  not not_139 (not_139_out, OP4);
  not not_140 (not_140_out, OP5);
  not not_141 (not_141_out, OP6);
  not not_142 (not_142_out, F12);
  not not_143 (not_143_out, F13);
  not not_144 (not_144_out, F14);
  not not_145 (not_145_out, OP2);
  not not_146 (not_146_out, OP3);
  not not_147 (not_147_out, OP4);
  not not_148 (not_148_out, F13);
  and and_1 (MemToReg, not_1_out, not_2_out, not_3_out, not_4_out, not_5_out, not_6_out, not_7_out);
  and and_2 (MemWrite, not_8_out, not_9_out, not_10_out, OP5, not_11_out, not_12_out, F13, not_13_out);
  and and_3 (and_3_out, not_14_out, not_15_out, not_16_out, not_17_out, not_18_out, not_19_out);
  and and_4 (and_4_out, not_20_out, not_21_out, not_22_out, not_23_out, not_24_out, F13, not_25_out);
  and and_5 (and_5_out, not_26_out, not_27_out, OP4, not_28_out, not_29_out, not_30_out);
  and and_6 (and_6_out, not_31_out, not_32_out, OP4, not_33_out, not_34_out, not_35_out, not_36_out, not_37_out);
  and and_7 (and_7_out, not_38_out, not_39_out, OP4, not_40_out, not_41_out, F14, not_42_out);
  and and_8 (and_8_out, not_43_out, not_44_out, OP4, not_45_out, not_46_out, F13, F14);
  and and_9 (and_9_out, OP2, not_47_out, not_48_out, OP5, OP6, not_49_out, not_50_out, not_51_out);
  and and_10 (CSRRSI, F14, F13, not_52_out, OP6, OP5, OP4, not_53_out, not_54_out);
  and and_11 (CSRRCI, F14, F13, F12, OP6, OP5, OP4, not_55_out, not_56_out);
  and and_12 (and_12_out, not_57_out, not_58_out, not_59_out, not_60_out, not_61_out, not_62_out);
  and and_13 (and_13_out, not_63_out, not_64_out, OP4, not_65_out, not_66_out, not_67_out);
  and and_14 (and_14_out, not_68_out, not_69_out, OP4, not_70_out, not_71_out, not_72_out, not_73_out, not_74_out);
  and and_15 (and_15_out, not_75_out, not_76_out, OP4, not_77_out, not_78_out, not_79_out, not_80_out, not_81_out);
  and and_16 (and_16_out, not_82_out, not_83_out, OP4, not_84_out, not_85_out, F14, not_86_out);
  and and_17 (and_17_out, not_87_out, not_88_out, OP4, not_89_out, not_90_out, F13, not_91_out, not_92_out);
  and and_18 (and_18_out, not_93_out, not_94_out, OP4, not_95_out, not_96_out, F13, F14);
  and and_19 (and_19_out, not_97_out, not_98_out, OP4, OP5, not_99_out, F12, not_100_out, not_101_out);
  and and_20 (and_20_out, OP2, not_102_out, OP5, OP6, not_103_out, not_104_out, not_105_out);
  and and_21 (and_21_out, OP2, OP3, not_106_out, OP5, OP6);
  and and_22 (ecall, not_107_out, not_108_out, OP4, OP5, OP6, not_109_out, not_110_out, not_111_out, not_112_out, not_113_out);
  and and_23 (S_Type, not_114_out, not_115_out, not_116_out, OP5, not_117_out, not_118_out, F13, not_119_out);
  and and_24 (BEQ, not_120_out, not_121_out, not_122_out, OP5, OP6, not_123_out, not_124_out, not_125_out);
  and and_25 (BNE, not_126_out, not_127_out, not_128_out, OP5, OP6, F12, not_129_out, not_130_out);
  and and_26 (JALR, OP2, not_131_out, not_132_out, OP5, OP6, not_133_out, not_134_out, not_135_out);
  and and_27 (JAL, OP2, OP3, not_136_out, OP5, OP6);
  and and_28 (LB, not_137_out, not_138_out, not_139_out, not_140_out, not_141_out, not_142_out, not_143_out, not_144_out);
  and and_29 (BGE, not_145_out, not_146_out, not_147_out, OP5, OP6, F12, not_148_out, F14);
  or or_1 (ALU_SRC, and_3_out, and_4_out, and_5_out, and_6_out, and_7_out, and_8_out, and_9_out);
  or or_2 (RegWrite, and_12_out, and_13_out, and_14_out, and_15_out, and_16_out, and_17_out, and_18_out, and_19_out, and_20_out, and_21_out);
endmodule

// ALU
module ALU (
  input  [31:0] X,
  input  [31:0] Y,
  input  [3:0] AluOP,
  output out_4,
  output Equal,
  output out_6,
  output [31:0] Result,
  output [31:0] Result_2
);

  wire [0:0] comparator_1_lt, comparator_2_lt;
  wire [31:0] adder_1_out, AND_out, divider_1_out, divider_1_rem, multiplier_1_cout, multiplier_1_out,
       NOR_out, OR_out, shifter_1_out, shifter_2_out, shifter_3_out, subtractor_1_out, XOR_out;

  assign AND_out = X & Y;  // AND_Gate AND, 32 bits wide
  assign OR_out = X | Y;  // OR_Gate OR, 32 bits wide
  Shifter #(.width(32), .shift("ll")) shifter_1 (.in(X), .\dist (Y[4:0]), .out(shifter_1_out));
  Shifter #(.width(32), .shift("ar")) shifter_2 (.in(X), .\dist (Y[4:0]), .out(shifter_2_out));
  Shifter #(.width(32), .shift("lr")) shifter_3 (.in(X), .\dist (Y[4:0]), .out(shifter_3_out));
  Multiplier #(.width(32)) multiplier_1 (.a(X), .b(Y), .out(multiplier_1_out), .cout(multiplier_1_cout));  // open: cin
  Divider #(.width(32)) divider_1 (.a(X), .b(Y), .out(divider_1_out), .rem(divider_1_rem));  // open: upper
  Adder #(.width(32)) adder_1 (.a(X), .b(Y), .out(adder_1_out));  // open: cin, cout
  Subtractor #(.width(32)) subtractor_1 (.a(X), .b(Y), .out(subtractor_1_out));  // open: bin, bout
  assign XOR_out = X ^ Y;  // XOR_Gate XOR, 32 bits wide
  assign NOR_out = ~(X | Y);  // NOR_Gate NOR, 32 bits wide
  Comparator #(.width(32), .mode("twosComplement")) comparator_1 (
    .a(X), .b(Y), .eq(Equal), .lt(comparator_1_lt[0]));  // open: gt
  Comparator #(.width(32), .mode("unsigned")) comparator_2 (.a(X), .b(Y), .lt(comparator_2_lt[0]));  // open: gt, eq
  Multiplexer #(.select(4), .width(32), .disabled("Z"), .enable("false")) multiplexer_1 (
    .in0(shifter_1_out), .in1(shifter_2_out), .in2(shifter_3_out), .in3(multiplier_1_out),
    .in4(divider_1_out), .in5(adder_1_out), .in6(subtractor_1_out), .in7(AND_out), .in8(OR_out),
    .in9(XOR_out), .in10(NOR_out), .in11({{31{1'b0}}, comparator_1_lt[0]}),
    .in12({{31{1'b0}}, comparator_2_lt[0]}), .in13({32{1'b0}}), .in14({32{1'b0}}), .in15({32{1'b0}}),
    .out(Result), .sel(AluOP));
  Multiplexer #(.select(4), .width(32), .disabled("Z"), .enable("false")) multiplexer_2 (
    .in0({32{1'b0}}), .in1({32{1'b0}}), .in2({32{1'b0}}), .in3(multiplier_1_cout), .in4(divider_1_rem),
    .in5({32{1'b0}}), .in6({32{1'b0}}), .in7({32{1'b0}}), .in8({32{1'b0}}), .in9({32{1'b0}}),
    .in10({32{1'b0}}), .in11({32{1'b0}}), .in12({32{1'b0}}), .in13({32{1'b0}}), .in14({32{1'b0}}),
    .in15({32{1'b0}}), .out(Result_2), .sel(AluOP));
  Multiplexer #(.select(4), .width(1), .disabled("Z"), .enable("false")) multiplexer_3 (
    .in0(1'b0), .in1(1'b0), .in2(1'b0), .in3(1'b0), .in4(1'b0), .in5(1'b0), .in6(1'b0), .in7(1'b0),
    .in8(1'b0), .in9(1'b0), .in10(1'b0), .in11(comparator_1_lt[0]), .in12(comparator_2_lt[0]), .in13(1'b0),
    .in14(1'b0), .in15(1'b0), .out(out_6), .sel(AluOP));
  not not_1 (out_4, out_6);

  // Other names for the same wires on the sheet: Result2[31:0] = Result_2; S[3:0] = AluOP; tunnel = out_6;
  //   tunnel_t = out_4

  // Notes on the sheet:
  //   不要改变此引脚区域内容，也不要改变ALU封装形式
  //   输入引脚
  //   输出引脚
endmodule

module Regifile (
  input  [31:0] Din,
  input  Clk,
  input  WE,
  input  [4:0] R1_num,
  input  [4:0] W_num,
  input  [4:0] R2_num,
  output [31:0] R1,
  output [31:0] R2
);

  // RegisterFile registerfile_1: pin names not known; wires that end beside it: Din, Clk, WE, W_num, R1_num, R2_num, R1, R2
endmodule

module \理想流水线  (
  output RegWrite,
  output MemWrite,
  output [31:0] IF_PC,
  output [31:0] ID_PC,
  output [31:0] EX_PC,
  output [31:0] M_PC,
  output [31:0] WB_PC,
  output [31:0] RDin,
  output [31:0] MDin,
  output [31:0] LedData
);

  wire and_1_out, and_2_out, and_3_out, and_4_out, and_5_out, Beq, BGE, Bne, Branch, CLK, clock_1_out,
       clock_2_out, comparator_1_eq, comparator_2_eq, comparator_2_lt, d_ff_1_q, EX_ecall, ex_mem_1_jal_2,
       ex_mem_1_jalr_2, ex_mem_1_lb_2, ex_mem_1_memtoreg_2, ex_mem_1_regwrite_2, Go, halt, ID_ecall,
       id_ex_1_alusrcb_2, id_ex_1_lb_2, id_ex_1_memtoreg_2, id_ex_1_memwrite_2, id_ex_1_regwrite_2, IR1, IR2,
       IR3, JAL, JALR, LB, MEM_ecall, MemToReg, nand_1_out, not_1_out, not_2_out, not_3_out, or_2_out,
       or_3_out, RST, tunnel, tunnel_t, tunnel_t_t, W1, W2, W3, WB_ecall, WB_JAL, WB_JALR,
       \单周期硬布线控制器_1_alu_src , \单周期硬布线控制器_1_beq , \单周期硬布线控制器_1_bge , \单周期硬布线控制器_1_bne , \单周期硬布线控制器_1_jal ,
       \单周期硬布线控制器_1_jalr , \单周期硬布线控制器_1_lb , \单周期硬布线控制器_1_memtoreg , \单周期硬布线控制器_1_memwrite ,
       \单周期硬布线控制器_1_regwrite , \单周期硬布线控制器_1_s_type ;
  wire [1:0] Addr, priority_encoder_1_out, priority_encoder_2_out;
  wire [3:0] id_ex_1_aluop_2, \单周期硬布线控制器_1_alu_op ;
  wire [4:0] ex_mem_1_rd_2, id_ex_1_rd_2, multiplexer_2_out, multiplexer_3_out, WB_rd;
  wire [12:0] CNT_num;
  wire [15:0] \LoadUse次数 , \总周期数 , \插入气泡数 , \无条件分支数 , \条件分支成功数 ;
  wire [31:0] B_Addr, bit_extender_1_out, bit_extender_2_out, bit_extender_3_out, bit_extender_4_out,
       bit_extender_5_out, bit_extender_6_out, bit_extender_7_out, bit_extender_8_out, \byte , EX_IR,
       ex_mem_1_pc_4_2, ex_mem_1_r_2, EX_R1, EX_R2, id_ex_1_imm_2, id_ex_1_imm_b_2, id_ex_1_imm_j_2,
       id_ex_1_pc_4_2, ID_IR, if_id_1_pc_4_2, IF_IR, IF_PC_4, J_Addr, MEM_IR, MEM_R1, mem_wb_1_dataout_2,
       mem_wb_1_r_2, multiplexer_1_out, multiplexer_4_out, multiplexer_5_out, R, ram_1_data, regifile_1_r1,
       regifile_1_r2, shifter_1_out, shifter_2_out, WB_IR, WB_PC_4, WB_R1, WB_R2, word;

  Button \u_总复位  (.out(RST));
  Button _1 (.out(IR1));
  Button _2 (.out(IR2));
  Button _3 (.out(IR3));
  // Probe on \总周期数 
  // Probe on \总周期数 
  Button \u_继续运行  (.out(Go));
  LED #(.active("true")) led_1 (.in(W1));
  LED #(.active("true")) led_2 (.in(W2));
  LED #(.active("true")) led_3 (.in(W3));
  Hex_Digit_Display hex_digit_display_1 (.value(LedData[31:28]));  // open: dp
  // Probe on IF_PC[19:0]
  // RiscV_Probe riscv_probe_1: pin names not known; wires that end beside it: IF_IR
  and and_1 (and_1_out, Beq, tunnel_t);
  and and_2 (and_2_out, ~tunnel_t, Bne);  // AND_Gate
  or or_1 (Branch, and_1_out, and_2_out, and_3_out);
  and and_3 (and_3_out, tunnel_t_t, BGE);
  Comparator #(.width(32), .mode("twosComplement")) comparator_1 (
    .a(WB_R1), .b(32'ha), .eq(comparator_1_eq));  // open: gt, lt
  Priority_Encoder #(.select(2), .disabled("Z")) priority_encoder_1 (
    .in0(1'b1), .in1(Branch), .in2(JAL), .in3(JALR), .out(priority_encoder_1_out));  // open: gs, en_out, en_in
  Multiplexer #(.select(2), .width(32), .disabled("Z"), .enable("false")) multiplexer_1 (
    .in0(IF_PC_4), .in1(B_Addr), .in2(J_Addr), .in3(R), .out(multiplexer_1_out), .sel(priority_encoder_1_out));
  not not_1 (not_1_out, halt);
  Hex_Digit_Display hex_digit_display_2 (.value(LedData[27:24]));  // open: dp
  Hex_Digit_Display hex_digit_display_3 (.value(LedData[23:20]));  // open: dp
  // Probe on ID_PC[19:0]
  // RiscV_Probe riscv_probe_2: pin names not known; wires that end beside it: ID_IR
  Register #(.width(32), .trigger("rising"), .Select("low")) PC (
    .D(WB_R2), .en(and_4_out), .Q(LedData), .clk(CLK));  // open: clr
  and and_4 (and_4_out, WB_ecall, ~comparator_1_eq);  // AND_Gate
  and and_5 (and_5_out, WB_ecall, comparator_1_eq);
  Register #(.width(32), .trigger("rising"), .Select("low")) PC_2 (
    .D(multiplexer_1_out), .en(not_1_out), .Q(IF_PC), .clk(CLK), .clr(RST));
  Hex_Digit_Display hex_digit_display_4 (.value(LedData[19:16]));  // open: dp
  Hex_Digit_Display hex_digit_display_5 (.value(LedData[15:12]));  // open: dp
  and and_6 (halt, and_5_out, ~Go);  // AND_Gate
  Hex_Digit_Display hex_digit_display_6 (.value(LedData[7:4]));  // open: dp
  Hex_Digit_Display hex_digit_display_7 (.value(LedData[11:8]));  // open: dp
  Clock #(.highDuration(1), .lowDuration(1)) clock_1 (.out(clock_1_out));
  // Probe on EX_PC[19:0]
  // RiscV_Probe riscv_probe_3: pin names not known; wires that end beside it: clock_1_out, EX_IR, CLK
  not not_2 (not_2_out, halt);
  ROM #(.addrWidth(10), .dataWidth(32), .Select("high")) rom_1 (.addr(IF_PC[11:2]), .data(IF_IR));
  Adder #(.width(32)) adder_1 (.a(IF_PC), .b(32'h4), .out(IF_PC_4));  // open: cin, cout
  Hex_Digit_Display hex_digit_display_8 (.value(LedData[3:0]));  // open: dp
  Counter #(.width(16), .max('hffff), .ongoal("stay"), .trigger("rising"), .behavior("old")) counter_1 (
    .count(not_2_out), .Q(\总周期数 ), .clk(CLK), .clr(RST));  // open: load, D, carry, preset
  // Probe on \总周期数 
  // Probe on M_PC[19:0]
  // RiscV_Probe riscv_probe_4: pin names not known; wires that end beside it: MEM_IR
  IF__ID if_id_1 (
    .IR(IF_IR), .PC(IF_PC), .PC_4(IF_PC_4), .IR_2(ID_IR), .PC_2(ID_PC), .PC_4_2(if_id_1_pc_4_2), .RST(RST),
    .CLK(CLK), .en(not_3_out), .BranchTaken(1'b0));  // open: PredictJump, PredictJump_2
  not not_3 (not_3_out, halt);
  // Probe on \总周期数 
  // Probe on \无条件分支数 
  // Probe on \条件分支成功数 
  // Probe on \插入气泡数 
  // Probe on \LoadUse次数 
  // Probe on IF_PC[11:0]
  // Probe on WB_PC[19:0]
  // RiscV_Probe riscv_probe_5: pin names not known; wires that end beside it: WB_IR
  \单周期硬布线控制器  \u_单周期硬布线控制器_1  (
    .Funct({ID_IR[30], ID_IR[25], ID_IR[14:12]}), .OP(ID_IR[6:2]), .ALU_OP(\单周期硬布线控制器_1_alu_op ),
    .MemToReg(\单周期硬布线控制器_1_memtoreg ), .MemWrite(\单周期硬布线控制器_1_memwrite ), .ALU_SRC(\单周期硬布线控制器_1_alu_src ),
    .RegWrite(\单周期硬布线控制器_1_regwrite ), .ecall(ID_ecall), .S_type(\单周期硬布线控制器_1_s_type ),
    .Jalr(\单周期硬布线控制器_1_jalr ), .Beq(\单周期硬布线控制器_1_beq ), .JAL(\单周期硬布线控制器_1_jal ), .Bne(\单周期硬布线控制器_1_bne ),
    .in_3(ID_IR[21]), .LB(\单周期硬布线控制器_1_lb ), .BGE(\单周期硬布线控制器_1_bge ));  // open: uret, CSRRSI, CSRRCI
  Multiplexer #(.select(1), .width(5), .disabled("Z"), .enable("false")) multiplexer_2 (
    .in0(ID_IR[19:15]), .in1(5'b10001), .out(multiplexer_2_out), .sel(ID_ecall));
  Multiplexer #(.select(1), .width(5), .disabled("Z"), .enable("false")) multiplexer_3 (
    .in0(ID_IR[24:20]), .in1(5'b01010), .out(multiplexer_3_out), .sel(ID_ecall));
  assign bit_extender_1_out = {{20{ID_IR[31]}}, ID_IR[31:20]};  // Bit_Extender bit_extender_1
  assign bit_extender_2_out = {{20{ID_IR[31]}}, {ID_IR[31:25], ID_IR[11:7]}};  // Bit_Extender bit_extender_2
  // Probe on ID_PC[11:0]
  // Probe on EX_PC[11:0]
  Multiplexer #(.select(1), .width(32), .disabled("Z"), .enable("false")) multiplexer_4 (
    .in0(bit_extender_1_out), .in1(bit_extender_2_out), .out(multiplexer_4_out), .sel(\单周期硬布线控制器_1_s_type ));
  assign bit_extender_3_out = {{20{ID_IR[31]}}, {ID_IR[31], ID_IR[7], ID_IR[30:25], ID_IR[11:8]}};  // Bit_Extender bit_extender_3
  assign bit_extender_4_out = {{12{ID_IR[31]}}, {ID_IR[31], ID_IR[19:12], ID_IR[20], ID_IR[30:21]}};  // Bit_Extender bit_extender_4
  // Probe on M_PC[11:0]
  D_Flip_Flop #(.trigger("high"), .Pre_Clr_Positions("LEGACY"), .NegatePresetClear("false"), .enable("true"), .NewFFLayout("false")) d_ff_1 (.Q(d_ff_1_q));  // open: clk, D, Qn, preset, en, reset
  // Probe on 13'hc
  Regifile regifile_1 (
    .Din(RDin), .Clk(CLK), .R1(regifile_1_r1), .R2(regifile_1_r2), .WE(RegWrite), .W_num(WB_rd),
    .R1_num(multiplexer_2_out), .R2_num(multiplexer_3_out));
  // Probe on WB_PC[11:0]
  Comparator #(.width(13), .mode("twosComplement")) comparator_2 (
    .a(CNT_num), .b(13'hc), .eq(comparator_2_eq), .lt(comparator_2_lt));  // open: gt
  Clock #(.highDuration(1), .lowDuration(1)) clock_2 (.out(clock_2_out));
  ID__EX id_ex_1 (
    .R1(regifile_1_r1), .R2(regifile_1_r2), .imm(multiplexer_4_out), .imm_b(bit_extender_3_out), .PC(ID_PC),
    .PC_4(if_id_1_pc_4_2), .IR(ID_IR), .R1_2(EX_R1), .R2_2(EX_R2), .imm_2(id_ex_1_imm_2),
    .imm_b_2(id_ex_1_imm_b_2), .PC_2(EX_PC), .PC_4_2(id_ex_1_pc_4_2), .IR_2(EX_IR), .RST_2(RST),
    .imm_j(bit_extender_4_out), .imm_j_2(id_ex_1_imm_j_2), .BGE_2(\单周期硬布线控制器_1_bge ), .LB(\单周期硬布线控制器_1_lb ),
    .JALR(\单周期硬布线控制器_1_jalr ), .JAL(\单周期硬布线控制器_1_jal ), .Beq(\单周期硬布线控制器_1_beq ), .Bne(\单周期硬布线控制器_1_bne ),
    .MemToReg(\单周期硬布线控制器_1_memtoreg ), .MemWrite(\单周期硬布线控制器_1_memwrite ), .AluSrcB(\单周期硬布线控制器_1_alu_src ),
    .RegWrite(\单周期硬布线控制器_1_regwrite ), .ecall(ID_ecall), .AluOP(\单周期硬布线控制器_1_alu_op ), .rd(ID_IR[11:7]),
    .BGE_4(BGE), .LB_2(id_ex_1_lb_2), .JALR_2(JALR), .JAL_2(JAL), .Beq_2(Beq), .Bne_2(Bne),
    .MemToReg_2(id_ex_1_memtoreg_2), .MemWrite_2(id_ex_1_memwrite_2), .AluSrcB_2(id_ex_1_alusrcb_2),
    .RegWrite_2(id_ex_1_regwrite_2), .ecall_2(EX_ecall), .AluOP_2(id_ex_1_aluop_2), .rd_2(id_ex_1_rd_2),
    .CLK(CLK), .en(not_3_out), .flush(1'b0));  // open: rs1Forward, rs2Forward, rs1Forward_2, rs2Forward_2, BGE, BGE_3, RST
  nand nand_1 (nand_1_out, d_ff_1_q, comparator_2_eq);
  Counter #(.width(13), .max('h1fff), .ongoal("stay"), .trigger("rising"), .behavior("old")) counter_2 (
    .count(comparator_2_lt), .Q(CNT_num), .clk(clock_2_out));  // open: load, D, carry, clr, preset
  assign CLK = nand_1_out ? clock_2_out : 1'bz;  // Controlled_Buffer controlled_buffer_1
  Multiplexer #(.select(1), .width(32), .disabled("Z"), .enable("false")) multiplexer_5 (
    .in0(EX_R2), .in1(id_ex_1_imm_2), .out(multiplexer_5_out), .sel(id_ex_1_alusrcb_2));
  Shifter #(.width(32), .shift("ll")) shifter_1 (.in(id_ex_1_imm_b_2), .\dist (5'b00001), .out(shifter_1_out));
  Adder #(.width(32)) adder_2 (.a(shifter_1_out), .b(EX_PC), .out(B_Addr));  // open: cin, cout
  Shifter #(.width(32), .shift("ll")) shifter_2 (.in(id_ex_1_imm_j_2), .\dist (5'b00001), .out(shifter_2_out));
  Adder #(.width(32)) adder_3 (.a(shifter_2_out), .b(EX_PC), .out(J_Addr));  // open: cin, cout
  Pull_Resistor #(.pull(1)) pull_resistor_1 (.node(CLK));
  ALU alu_1 (
    .X(EX_R1), .Y(multiplexer_5_out), .AluOP(id_ex_1_aluop_2), .Equal(tunnel_t), .Result(R),
    .out_4(tunnel_t_t), .out_6(tunnel));  // open: Result_2
  EX__MEM ex_mem_1 (
    .LB(id_ex_1_lb_2), .JALR(JALR), .MemToReg(id_ex_1_memtoreg_2), .MemWrite(id_ex_1_memwrite_2),
    .RegWrite(id_ex_1_regwrite_2), .R1(EX_R1), .rd(id_ex_1_rd_2), .R(R), .MD(EX_R2), .IR(EX_IR), .PC(EX_PC),
    .PC_4(id_ex_1_pc_4_2), .LB_2(ex_mem_1_lb_2), .JALR_2(ex_mem_1_jalr_2), .MemToReg_2(ex_mem_1_memtoreg_2),
    .MemWrite_2(MemWrite), .RegWrite_2(ex_mem_1_regwrite_2), .R1_2(MEM_R1), .rd_2(ex_mem_1_rd_2),
    .R_2(ex_mem_1_r_2), .MD_2(MDin), .IR_2(MEM_IR), .PC_2(M_PC), .PC_4_2(ex_mem_1_pc_4_2), .RST(RST),
    .CLK(CLK), .JAL(JAL), .JAL_2(ex_mem_1_jal_2), .ecall(EX_ecall), .RegWrite_3(MEM_ecall), .en(not_3_out));
  or or_2 (or_2_out, JAL, JALR);
  Counter #(.width(16), .max('hffff), .ongoal("wrap"), .trigger("rising"), .behavior("old")) counter_3 (
    .count(or_2_out), .Q(\无条件分支数 ), .clk(CLK), .clr(RST));  // open: load, D, carry, preset
  Counter #(.width(16), .max('hffff), .ongoal("wrap"), .trigger("rising"), .behavior("old")) counter_4 (
    .count(Branch), .Q(\条件分支成功数 ), .clk(CLK), .clr(RST));  // open: load, D, carry, preset
  RAM #(.addrWidth(10), .dataWidth(32), .bus("separate"), .Select("high")) ram_1 (
    .addr(ex_mem_1_r_2[11:2]), .din(MDin), .data(ram_1_data), .str(MemWrite), .sel(1'b1), .clk(CLK),
    .ld(1'b1), .clr(RST));
  MEM__WB mem_wb_1 (
    .JALR(ex_mem_1_jalr_2), .JAL(ex_mem_1_jal_2), .MenToReg(ex_mem_1_memtoreg_2),
    .RegWrite(ex_mem_1_regwrite_2), .rd(ex_mem_1_rd_2), .R(ex_mem_1_r_2), .Dataout(ram_1_data), .IR(MEM_IR),
    .PC(M_PC), .PC_4(ex_mem_1_pc_4_2), .JALR_2(WB_JALR), .JAL_2(WB_JAL), .MemToReg(MemToReg),
    .RegWrite_2(RegWrite), .rd_2(WB_rd), .R_2(mem_wb_1_r_2), .Dataout_2(mem_wb_1_dataout_2), .IR_2(WB_IR),
    .PC_2(WB_PC), .PC_4_2(WB_PC_4), .RST(RST), .CLK(CLK), .LB(ex_mem_1_lb_2), .LB_2(LB), .Addr_2(Addr),
    .addr(ex_mem_1_r_2[1:0]), .R1(MEM_R1), .R1_2(WB_R1), .R2(MDin), .R2_2(WB_R2), .ecall(MEM_ecall),
    .ecall_2(WB_ecall), .en(not_3_out));
  or or_3 (or_3_out, WB_JAL, WB_JALR);
  Priority_Encoder #(.select(2), .disabled("Z")) priority_encoder_2 (
    .in0(1'b1), .in1(MemToReg), .in2(or_3_out), .out(priority_encoder_2_out));  // open: in3, gs, en_out, en_in
  Multiplexer #(.select(2), .width(32), .disabled("Z"), .enable("false")) multiplexer_6 (
    .in0(mem_wb_1_r_2), .in1(mem_wb_1_dataout_2), .in2(WB_PC_4), .out(word), .sel(priority_encoder_2_out));  // open: in3
  assign bit_extender_5_out = {{24{word[7]}}, word[7:0]};  // Bit_Extender bit_extender_5
  assign bit_extender_6_out = {{24{word[15]}}, word[15:8]};  // Bit_Extender bit_extender_6
  assign bit_extender_7_out = {{24{word[23]}}, word[23:16]};  // Bit_Extender bit_extender_7
  assign bit_extender_8_out = {{24{word[31]}}, word[31:24]};  // Bit_Extender bit_extender_8
  Multiplexer #(.select(1), .width(32), .disabled("Z"), .enable("false")) multiplexer_7 (
    .in0(word), .in1(\byte ), .out(RDin), .sel(LB));
  Multiplexer #(.select(2), .width(32), .disabled("Z"), .enable("false")) multiplexer_8 (
    .in0(bit_extender_5_out), .in1(bit_extender_6_out), .in2(bit_extender_7_out), .in3(bit_extender_8_out),
    .out(\byte ), .sel(Addr));

  // Other names for the same wires on the sheet: MEM_PC[31:0] = M_PC

  // Notes on the sheet:
  //   中断源
  //   时空图监测，可删除
  //   中断等待指示
  //   数码管输出
  //   指令存储器
  //   contents of rom_1 (hex, n*v repeats v):
  //   413 493 913 993 46413 14e493 296913 39e993 842023 942223 1242423 1342623 a00893 493 913 993 73
  //   JAL
  //   JALR
  //   LB
  //   BGE
  //   Beq
  //   Bne
  //   MemToReg
  //   MemWrite
  //   AluOP
  //   AluSrcB
  //   RegWrite
  //   S_Type
  //   控制位
  //   流水调试日志用
  //   暂停节拍，不能为0
  //   用这个时钟源需要去掉电路中的其他时钟源
  //   戳工具置1进入计数暂停模式，ctrl+k时钟自动运行到对应节拍暂停
  //   ctrl+k关闭时钟连续运行，将控制位置零，进入单步调试模式调试
  //   LB
  //   JALR
  //   JAL
  //   MemToReg
  //   MemWrite
  //   AluOP
  //   AluSrcB
  //   RegWrite
  //   可计数暂停的时钟源
  //   LB
  //   JALR
  //   JAL
  //   MemToReg
  //   RegWrite
  //   为方便自动评测，需要输出流水线各段保存的PC值，注意是PC不是PC+4，另外ID段寄存器写入信息，Mem段内存写入信息也要输出
  //   数据存储器
endmodule

module \气泡流水线  (
  output RegWrite,
  output MemWrite,
  output [31:0] IF_PC,
  output [31:0] ID_PC,
  output [31:0] EX_PC,
  output [31:0] M_PC,
  output [31:0] WB_PC,
  output [31:0] RDin,
  output [31:0] MDin,
  output [31:0] LedData
);

  wire and_1_out, and_2_out, and_3_out, and_5_out, and_6_out, and_7_out, and_8_out, and_9_out, Beq, BGE, Bne,
       Branch, BranchTaken, CLK, clock_1_out, clock_2_out, comparator_1_eq, comparator_2_eq, comparator_3_eq,
       comparator_3_lt, d_ff_1_q, EX_ecall, ex_mem_1_jal_2, ex_mem_1_jalr_2, ex_mem_1_lb_2,
       ex_mem_1_memtoreg_2, EX_RegWrite, flush, Go, halt, ID_ecall, id_ex_1_alusrcb_2, id_ex_1_lb_2,
       id_ex_1_memtoreg_2, id_ex_1_memwrite_2, IR1, IR2, IR3, JAL, JALR, LB, MEM_ecall, MEM_RegWrite,
       MemToReg, nand_1_out, not_2_out, not_3_out, not_4_out, or_2_out, or_3_out, RST, stall, tunnel,
       tunnel_t, tunnel_t_t, W1, W2, W3, WB_ecall, WB_JAL, WB_JALR, \单周期硬布线控制器_1_alu_src , \单周期硬布线控制器_1_beq ,
       \单周期硬布线控制器_1_bge , \单周期硬布线控制器_1_bne , \单周期硬布线控制器_1_jal , \单周期硬布线控制器_1_jalr , \单周期硬布线控制器_1_lb ,
       \单周期硬布线控制器_1_memtoreg , \单周期硬布线控制器_1_memwrite , \单周期硬布线控制器_1_regwrite , \单周期硬布线控制器_1_s_type ;
  wire [1:0] Addr, priority_encoder_1_out, priority_encoder_2_out;
  wire [3:0] id_ex_1_aluop_2, \单周期硬布线控制器_1_alu_op ;
  wire [4:0] EX_rd, MEM_rd, multiplexer_2_out, multiplexer_3_out, WB_rd;
  wire [12:0] CNT_num;
  wire [15:0] \LoadUse次数 , \总周期数 , \插入气泡数 , \无条件分支数 , \条件分支成功数 ;
  wire [31:0] B_Addr, bit_extender_1_out, bit_extender_2_out, bit_extender_3_out, bit_extender_4_out,
       bit_extender_5_out, bit_extender_6_out, bit_extender_7_out, bit_extender_8_out, \byte , EX_IR,
       ex_mem_1_pc_4_2, ex_mem_1_r_2, EX_R1, EX_R2, id_ex_1_imm_2, id_ex_1_imm_b_2, id_ex_1_imm_j_2,
       id_ex_1_pc_4_2, ID_IR, if_id_1_pc_4_2, IF_IR, IF_PC_4, J_Addr, MEM_IR, MEM_R1, mem_wb_1_dataout_2,
       mem_wb_1_r_2, multiplexer_1_out, multiplexer_4_out, multiplexer_5_out, R, ram_1_data,
       regifile_falling_edge_1_r1, regifile_falling_edge_1_r2, shifter_1_out, shifter_2_out, WB_IR, WB_PC_4,
       WB_R1, WB_R2, word;

  Button \u_总复位  (.out(RST));
  Button _1 (.out(IR1));
  Button _2 (.out(IR2));
  Button _3 (.out(IR3));
  // Probe on \总周期数 
  // Probe on \总周期数 
  Button \u_继续运行  (.out(Go));
  LED #(.active("true")) led_1 (.in(W1));
  LED #(.active("true")) led_2 (.in(W2));
  LED #(.active("true")) led_3 (.in(W3));
  Hex_Digit_Display hex_digit_display_1 (.value(LedData[31:28]));  // open: dp
  // Probe on IF_PC[19:0]
  // RiscV_Probe riscv_probe_1: pin names not known; wires that end beside it: IF_IR
  Comparator #(.width(32), .mode("twosComplement")) comparator_1 (
    .a(WB_R1), .b(32'ha), .eq(comparator_1_eq));  // open: gt, lt
  Priority_Encoder #(.select(2), .disabled("Z")) priority_encoder_1 (
    .in0(1'b1), .in1(Branch), .in2(JAL), .in3(JALR), .out(priority_encoder_1_out));  // open: gs, en_out, en_in
  Multiplexer #(.select(2), .width(32), .disabled("Z"), .enable("false")) multiplexer_1 (
    .in0(IF_PC_4), .in1(B_Addr), .in2(J_Addr), .in3(R), .out(multiplexer_1_out), .sel(priority_encoder_1_out));
  and and_1 (and_1_out, ~stall, not_2_out);  // AND_Gate
  Hex_Digit_Display hex_digit_display_2 (.value(LedData[23:20]));  // open: dp
  Hex_Digit_Display hex_digit_display_3 (.value(LedData[27:24]));  // open: dp
  // Probe on ID_PC[19:0]
  // RiscV_Probe riscv_probe_2: pin names not known; wires that end beside it: ID_IR
  \气泡  \u_气泡_1  (
    .in_1(EX_RegWrite), .in_2(EX_rd), .in_4(MEM_RegWrite), .in_5(MEM_rd), .in_6(ID_ecall), .out_8(stall),
    .out_9(flush), .in_7(BranchTaken), .in_3(ID_IR));
  Register #(.width(32), .trigger("rising"), .Select("low")) PC (
    .D(WB_R2), .en(and_2_out), .Q(LedData), .clk(CLK));  // open: clr
  and and_2 (and_2_out, WB_ecall, ~comparator_1_eq);  // AND_Gate
  and and_3 (and_3_out, WB_ecall, comparator_1_eq);
  not not_1 (BranchTaken, comparator_2_eq);
  Comparator #(.width(2), .mode("twosComplement")) comparator_2 (
    .a(2'b00), .b(priority_encoder_1_out), .eq(comparator_2_eq));  // open: gt, lt
  Register #(.width(32), .trigger("rising"), .Select("low")) PC_2 (
    .D(multiplexer_1_out), .en(and_1_out), .Q(IF_PC), .clk(CLK), .clr(RST));
  not not_2 (not_2_out, halt);
  Hex_Digit_Display hex_digit_display_4 (.value(LedData[19:16]));  // open: dp
  Hex_Digit_Display hex_digit_display_5 (.value(LedData[15:12]));  // open: dp
  and and_4 (halt, and_3_out, ~Go);  // AND_Gate
  Hex_Digit_Display hex_digit_display_6 (.value(LedData[7:4]));  // open: dp
  Hex_Digit_Display hex_digit_display_7 (.value(LedData[11:8]));  // open: dp
  Clock #(.highDuration(1), .lowDuration(1)) clock_1 (.out(clock_1_out));
  // Probe on EX_PC[19:0]
  // RiscV_Probe riscv_probe_3: pin names not known; wires that end beside it: clock_1_out, EX_IR, CLK
  not not_3 (not_3_out, halt);
  Adder #(.width(32)) adder_1 (.a(IF_PC), .b(32'h4), .out(IF_PC_4));  // open: cin, cout
  Hex_Digit_Display hex_digit_display_8 (.value(LedData[3:0]));  // open: dp
  and and_5 (and_5_out, Beq, tunnel_t);
  and and_6 (and_6_out, ~tunnel_t, Bne);  // AND_Gate
  and and_7 (and_7_out, tunnel_t_t, BGE);
  Counter #(.width(16), .max('hffff), .ongoal("stay"), .trigger("rising"), .behavior("old")) counter_1 (
    .count(not_3_out), .Q(\总周期数 ), .clk(CLK), .clr(RST));  // open: load, D, carry, preset
  ROM #(.addrWidth(10), .dataWidth(32), .Select("high")) rom_1 (.addr(IF_PC[11:2]), .data(IF_IR));
  not not_4 (not_4_out, halt);
  // Probe on \总周期数 
  // Probe on M_PC[19:0]
  // RiscV_Probe riscv_probe_4: pin names not known; wires that end beside it: MEM_IR
  or or_1 (Branch, and_5_out, and_6_out, and_7_out);
  IF__ID if_id_1 (
    .IR(IF_IR), .PC(IF_PC), .PC_4(IF_PC_4), .IR_2(ID_IR), .PC_2(ID_PC), .PC_4_2(if_id_1_pc_4_2), .RST(RST),
    .CLK(CLK), .en(and_8_out), .BranchTaken(BranchTaken));  // open: PredictJump, PredictJump_2
  and and_8 (and_8_out, ~stall, not_4_out);  // AND_Gate
  // Probe on \总周期数 
  // Probe on \无条件分支数 
  // Probe on \条件分支成功数 
  // Probe on \插入气泡数 
  // Probe on \LoadUse次数 
  // Probe on IF_PC[11:0]
  // Probe on WB_PC[19:0]
  // RiscV_Probe riscv_probe_5: pin names not known; wires that end beside it: WB_IR
  \单周期硬布线控制器  \u_单周期硬布线控制器_1  (
    .Funct({ID_IR[30], ID_IR[25], ID_IR[14:12]}), .OP(ID_IR[6:2]), .ALU_OP(\单周期硬布线控制器_1_alu_op ),
    .MemToReg(\单周期硬布线控制器_1_memtoreg ), .MemWrite(\单周期硬布线控制器_1_memwrite ), .ALU_SRC(\单周期硬布线控制器_1_alu_src ),
    .RegWrite(\单周期硬布线控制器_1_regwrite ), .ecall(ID_ecall), .S_type(\单周期硬布线控制器_1_s_type ),
    .Jalr(\单周期硬布线控制器_1_jalr ), .Beq(\单周期硬布线控制器_1_beq ), .JAL(\单周期硬布线控制器_1_jal ), .Bne(\单周期硬布线控制器_1_bne ),
    .in_3(ID_IR[21]), .LB(\单周期硬布线控制器_1_lb ), .BGE(\单周期硬布线控制器_1_bge ));  // open: uret, CSRRSI, CSRRCI
  Multiplexer #(.select(1), .width(5), .disabled("Z"), .enable("false")) multiplexer_2 (
    .in0(ID_IR[19:15]), .in1(5'b10001), .out(multiplexer_2_out), .sel(ID_ecall));
  Multiplexer #(.select(1), .width(5), .disabled("Z"), .enable("false")) multiplexer_3 (
    .in0(ID_IR[24:20]), .in1(5'b01010), .out(multiplexer_3_out), .sel(ID_ecall));
  assign bit_extender_1_out = {{20{ID_IR[31]}}, ID_IR[31:20]};  // Bit_Extender bit_extender_1
  assign bit_extender_2_out = {{20{ID_IR[31]}}, {ID_IR[31:25], ID_IR[11:7]}};  // Bit_Extender bit_extender_2
  // Probe on ID_PC[11:0]
  // Probe on EX_PC[11:0]
  Multiplexer #(.select(1), .width(32), .disabled("Z"), .enable("false")) multiplexer_4 (
    .in0(bit_extender_1_out), .in1(bit_extender_2_out), .out(multiplexer_4_out), .sel(\单周期硬布线控制器_1_s_type ));
  assign bit_extender_3_out = {{20{ID_IR[31]}}, {ID_IR[31], ID_IR[7], ID_IR[30:25], ID_IR[11:8]}};  // Bit_Extender bit_extender_3
  assign bit_extender_4_out = {{12{ID_IR[31]}}, {ID_IR[31], ID_IR[19:12], ID_IR[20], ID_IR[30:21]}};  // Bit_Extender bit_extender_4
  // Probe on M_PC[11:0]
  D_Flip_Flop #(.trigger("high"), .Pre_Clr_Positions("LEGACY"), .NegatePresetClear("false"), .enable("true"), .NewFFLayout("false")) d_ff_1 (.Q(d_ff_1_q));  // open: clk, D, Qn, preset, en, reset
  // Probe on 13'hc
  // Probe on WB_PC[11:0]
  Comparator #(.width(13), .mode("twosComplement")) comparator_3 (
    .a(CNT_num), .b(13'hc), .eq(comparator_3_eq), .lt(comparator_3_lt));  // open: gt
  Clock #(.highDuration(1), .lowDuration(1)) clock_2 (.out(clock_2_out));
  ID__EX id_ex_1 (
    .R1(regifile_falling_edge_1_r1), .R2(regifile_falling_edge_1_r2), .imm(multiplexer_4_out),
    .imm_b(bit_extender_3_out), .PC(ID_PC), .PC_4(if_id_1_pc_4_2), .IR(ID_IR), .R1_2(EX_R1), .R2_2(EX_R2),
    .imm_2(id_ex_1_imm_2), .imm_b_2(id_ex_1_imm_b_2), .PC_2(EX_PC), .PC_4_2(id_ex_1_pc_4_2), .IR_2(EX_IR),
    .RST_2(RST), .imm_j(bit_extender_4_out), .imm_j_2(id_ex_1_imm_j_2), .BGE_2(\单周期硬布线控制器_1_bge ),
    .LB(\单周期硬布线控制器_1_lb ), .JALR(\单周期硬布线控制器_1_jalr ), .JAL(\单周期硬布线控制器_1_jal ), .Beq(\单周期硬布线控制器_1_beq ),
    .Bne(\单周期硬布线控制器_1_bne ), .MemToReg(\单周期硬布线控制器_1_memtoreg ), .MemWrite(\单周期硬布线控制器_1_memwrite ),
    .AluSrcB(\单周期硬布线控制器_1_alu_src ), .RegWrite(\单周期硬布线控制器_1_regwrite ), .ecall(ID_ecall),
    .AluOP(\单周期硬布线控制器_1_alu_op ), .rd(ID_IR[11:7]), .BGE_4(BGE), .LB_2(id_ex_1_lb_2), .JALR_2(JALR),
    .JAL_2(JAL), .Beq_2(Beq), .Bne_2(Bne), .MemToReg_2(id_ex_1_memtoreg_2), .MemWrite_2(id_ex_1_memwrite_2),
    .AluSrcB_2(id_ex_1_alusrcb_2), .RegWrite_2(EX_RegWrite), .ecall_2(EX_ecall), .AluOP_2(id_ex_1_aluop_2),
    .rd_2(EX_rd), .CLK(CLK), .en(and_8_out), .flush(flush));  // open: rs1Forward, rs2Forward, rs1Forward_2, rs2Forward_2, BGE, BGE_3, RST
  Regifile_Falling_Edge regifile_falling_edge_1 (
    .Din(RDin), .Clk(CLK), .R1(regifile_falling_edge_1_r1), .R2(regifile_falling_edge_1_r2), .WE(RegWrite),
    .W_num(WB_rd), .R1_num(multiplexer_2_out), .R2_num(multiplexer_3_out));
  nand nand_1 (nand_1_out, d_ff_1_q, comparator_3_eq);
  Counter #(.width(13), .max('h1fff), .ongoal("stay"), .trigger("rising"), .behavior("old")) counter_2 (
    .count(comparator_3_lt), .Q(CNT_num), .clk(clock_2_out));  // open: load, D, carry, clr, preset
  assign CLK = nand_1_out ? clock_2_out : 1'bz;  // Controlled_Buffer controlled_buffer_1
  Multiplexer #(.select(1), .width(32), .disabled("Z"), .enable("false")) multiplexer_5 (
    .in0(EX_R2), .in1(id_ex_1_imm_2), .out(multiplexer_5_out), .sel(id_ex_1_alusrcb_2));
  Shifter #(.width(32), .shift("ll")) shifter_1 (.in(id_ex_1_imm_b_2), .\dist (5'b00001), .out(shifter_1_out));
  Shifter #(.width(32), .shift("ll")) shifter_2 (.in(id_ex_1_imm_j_2), .\dist (5'b00001), .out(shifter_2_out));
  Pull_Resistor #(.pull(1)) pull_resistor_1 (.node(CLK));
  ALU alu_1 (
    .X(EX_R1), .Y(multiplexer_5_out), .AluOP(id_ex_1_aluop_2), .Equal(tunnel_t), .Result(R),
    .out_4(tunnel_t_t), .out_6(tunnel));  // open: Result_2
  Adder #(.width(32)) adder_2 (.a(shifter_1_out), .b(EX_PC), .out(B_Addr));  // open: cin, cout
  Adder #(.width(32)) adder_3 (.a(shifter_2_out), .b(EX_PC), .out(J_Addr));  // open: cin, cout
  EX__MEM ex_mem_1 (
    .LB(id_ex_1_lb_2), .JALR(JALR), .MemToReg(id_ex_1_memtoreg_2), .MemWrite(id_ex_1_memwrite_2),
    .RegWrite(EX_RegWrite), .R1(EX_R1), .rd(EX_rd), .R(R), .MD(EX_R2), .IR(EX_IR), .PC(EX_PC),
    .PC_4(id_ex_1_pc_4_2), .LB_2(ex_mem_1_lb_2), .JALR_2(ex_mem_1_jalr_2), .MemToReg_2(ex_mem_1_memtoreg_2),
    .MemWrite_2(MemWrite), .RegWrite_2(MEM_RegWrite), .R1_2(MEM_R1), .rd_2(MEM_rd), .R_2(ex_mem_1_r_2),
    .MD_2(MDin), .IR_2(MEM_IR), .PC_2(M_PC), .PC_4_2(ex_mem_1_pc_4_2), .RST(RST), .CLK(CLK), .JAL(JAL),
    .JAL_2(ex_mem_1_jal_2), .ecall(EX_ecall), .RegWrite_3(MEM_ecall), .en(and_8_out));
  or or_2 (or_2_out, JAL, JALR);
  and and_9 (and_9_out, stall, ~halt);  // AND_Gate
  Counter #(.width(16), .max('hffff), .ongoal("wrap"), .trigger("rising"), .behavior("old")) counter_3 (
    .count(or_2_out), .Q(\无条件分支数 ), .clk(CLK), .clr(RST));  // open: load, D, carry, preset
  Counter #(.width(16), .max('hffff), .ongoal("wrap"), .trigger("rising"), .behavior("old")) counter_4 (
    .count(Branch), .Q(\条件分支成功数 ), .clk(CLK), .clr(RST));  // open: load, D, carry, preset
  Counter #(.width(16), .max('hffff), .ongoal("wrap"), .trigger("rising"), .behavior("old")) counter_5 (
    .count(and_9_out), .Q(\插入气泡数 ), .clk(CLK), .clr(RST));  // open: load, D, carry, preset
  RAM #(.addrWidth(10), .dataWidth(32), .bus("separate"), .Select("high")) ram_1 (
    .addr(ex_mem_1_r_2[11:2]), .din(MDin), .data(ram_1_data), .str(MemWrite), .sel(1'b1), .clk(CLK),
    .ld(1'b1), .clr(RST));
  MEM__WB mem_wb_1 (
    .JALR(ex_mem_1_jalr_2), .JAL(ex_mem_1_jal_2), .MenToReg(ex_mem_1_memtoreg_2), .RegWrite(MEM_RegWrite),
    .rd(MEM_rd), .R(ex_mem_1_r_2), .Dataout(ram_1_data), .IR(MEM_IR), .PC(M_PC), .PC_4(ex_mem_1_pc_4_2),
    .JALR_2(WB_JALR), .JAL_2(WB_JAL), .MemToReg(MemToReg), .RegWrite_2(RegWrite), .rd_2(WB_rd),
    .R_2(mem_wb_1_r_2), .Dataout_2(mem_wb_1_dataout_2), .IR_2(WB_IR), .PC_2(WB_PC), .PC_4_2(WB_PC_4),
    .RST(RST), .CLK(CLK), .LB(ex_mem_1_lb_2), .LB_2(LB), .Addr_2(Addr), .addr(ex_mem_1_r_2[1:0]),
    .R1(MEM_R1), .R1_2(WB_R1), .R2(MDin), .R2_2(WB_R2), .ecall(MEM_ecall), .ecall_2(WB_ecall), .en(and_8_out));
  or or_3 (or_3_out, WB_JAL, WB_JALR);
  Priority_Encoder #(.select(2), .disabled("Z")) priority_encoder_2 (
    .in0(1'b1), .in1(MemToReg), .in2(or_3_out), .out(priority_encoder_2_out));  // open: in3, gs, en_out, en_in
  Multiplexer #(.select(2), .width(32), .disabled("Z"), .enable("false")) multiplexer_6 (
    .in0(mem_wb_1_r_2), .in1(mem_wb_1_dataout_2), .in2(WB_PC_4), .out(word), .sel(priority_encoder_2_out));  // open: in3
  assign bit_extender_5_out = {{24{word[7]}}, word[7:0]};  // Bit_Extender bit_extender_5
  assign bit_extender_6_out = {{24{word[15]}}, word[15:8]};  // Bit_Extender bit_extender_6
  assign bit_extender_7_out = {{24{word[23]}}, word[23:16]};  // Bit_Extender bit_extender_7
  assign bit_extender_8_out = {{24{word[31]}}, word[31:24]};  // Bit_Extender bit_extender_8
  Multiplexer #(.select(1), .width(32), .disabled("Z"), .enable("false")) multiplexer_7 (
    .in0(word), .in1(\byte ), .out(RDin), .sel(LB));
  Multiplexer #(.select(2), .width(32), .disabled("Z"), .enable("false")) multiplexer_8 (
    .in0(bit_extender_5_out), .in1(bit_extender_6_out), .in2(bit_extender_7_out), .in3(bit_extender_8_out),
    .out(\byte ), .sel(Addr));

  // Other names for the same wires on the sheet: ID_rd[4:0] = ID_IR[11:7]; MEM_PC[31:0] = M_PC

  // Notes on the sheet:
  //   中断源
  //   时空图监测，可删除
  //   中断等待指示
  //   数码管输出
  //   指令存储器
  //   contents of rom_1 (hex, n*v repeats v):
  //   100493 100006f 100493 200913 300993 100006f 100493 200913 300993 100006f 100493 200913 300993
  //   100006f 100493 200913 300993 3d0000ef 100413 100493 1f49493 900533 2200893 73 24d493 48463 fedff06f
  //   900533 2200893 73 100493 249493 900533 2200893 73 48463 fedff06f 100493 1f49493 900533 2200893 73
  //   4034d493 900533 2200893 73 4044d493 900533 2200893 73 4044d493 900533 2200893 73 4044d493 900533
  //   2200893 73 4044d493 900533 2200893 73 4044d493 900533 2200893 73 4044d493 900533 2200893 73 4044d493
  //   900533 2200893 73 100413 1f41993 41f9d993 433 c00913 300b13 140413 f47413 800293 100313 499993
  //   89e9b3 1300533 2200893 73 406282b3 fe0294e3 140413 f00f93 1f47433 1c41413 800293 100313 49d993
  //   89e9b3 1300533 2200893 73 406282b3 fe0294e3 1c45413 406b0b33 b0463 f95ff06f 2b3 fff2c293 829293
  //   ff2e293 500533 2200893 73 fff00413 493 84a023 140413 448493 84a023 140413 448493 84a023 140413
  //   448493 84a023 140413 448493 84a023 140413 448493 84a023 140413 448493 84a023 140413 448493 84a023
  //   140413 448493 84a023 140413 448493 84a023 140413 448493 84a023 140413 448493 84a023 140413 448493
  //   84a023 140413 448493 84a023 140413 448493 84a023 140413 448493 84a023 140413 448493 140413 433
  //   3c00493 42983 4aa03 149a2b3 28663 134a023 1442023 ffc48493 fe9412e3 800533 2200893 73 440413 3c00493
  //   fc9416e3 a00893 73 100293 300313 800493 849493 7648493 900533 2200893 73 800e13 5494b3 6494b3 900533
  //   2200893 73 fffe0e13 fe0e14e3 a00893 73 100293 300313 800493 849493 7648493 1449493 900533 2200893 73
  //   800e13 54d4b3 64d4b3 900533 2200893 73 fffe0e13 fe0e14e3 a00893 73 313 1000e13 8400493 849493
  //   8348493 400913 891913 490913 849493 8248493 849493 8148493 891913 490913 891913 490913 932023
  //   12484b3 430313 fffe0e13 fe0e18e3 2000e13 313 30483 900533 2200893 73 130313 fffe0e13 fe0e14e3 a00893
  //   73 f00493 900533 2200893 73 fff48493 fe04d8e3 a00893 73 413 140413 800533 2200893 73 240413 800533
  //   2200893 73 340413 800533 2200893 73 440413 800533 2200893 73 540413 800533 2200893 73 640413 800533
  //   2200893 73 740413 800533 2200893 73 840413 800533 2200893 2200893 73 8067
  //   JAL
  //   JALR
  //   LB
  //   BGE
  //   Beq
  //   Bne
  //   AluOP
  //   AluSrcB
  //   RegWrite
  //   S_Type
  //   控制位
  //   MemToReg
  //   MemWrite
  //   流水调试日志用
  //   暂停节拍，不能为0
  //   戳工具置1进入计数暂停模式，ctrl+k时钟自动运行到对应节拍暂停
  //   ctrl+k关闭时钟连续运行，将控制位置零，进入单步调试模式调试
  //   LB
  //   JALR
  //   JAL
  //   MemToReg
  //   MemWrite
  //   AluOP
  //   AluSrcB
  //   可计数暂停的时钟源
  //   LB
  //   JALR
  //   JAL
  //   MemToReg
  //   为方便自动评测，需要输出流水线各段保存的PC值，注意是PC不是PC+4，另外ID段寄存器写入信息，Mem段内存写入信息也要输出
  //   数据存储器
endmodule

module \重定向流水线  (
  output RegWrite,
  output MemWrite,
  output [31:0] IF_PC,
  output [31:0] ID_PC,
  output [31:0] EX_PC,
  output [31:0] M_PC,
  output [31:0] WB_PC,
  output [31:0] RDin,
  output [31:0] MDin,
  output [31:0] LedData
);

  wire and_1_out, and_2_out, and_3_out, and_5_out, and_6_out, and_7_out, and_8_out, and_9_out, Beq, BGE, Bne,
       Branch, BranchTaken, CLK, clock_1_out, clock_2_out, comparator_1_eq, comparator_2_eq, comparator_3_eq,
       comparator_3_lt, d_ff_1_q, EX_ecall, ex_mem_1_jal_2, ex_mem_1_jalr_2, ex_mem_1_lb_2,
       ex_mem_1_memtoreg_2, EX_MemToReg, EX_RegWrite, flush, Go, halt, ID_ecall, id_ex_1_alusrcb_2,
       id_ex_1_lb_2, id_ex_1_memwrite_2, IR1, IR2, IR3, JAL, JALR, LB, MEM_ecall, MEM_RegWrite, MemToReg,
       nand_1_out, not_2_out, not_3_out, not_4_out, or_2_out, or_3_out, RST, stall, tunnel, tunnel_t,
       tunnel_t_t, W1, W2, W3, WB_ecall, WB_JAL, WB_JALR, \单周期硬布线控制器_1_alu_src , \单周期硬布线控制器_1_beq ,
       \单周期硬布线控制器_1_bge , \单周期硬布线控制器_1_bne , \单周期硬布线控制器_1_jal , \单周期硬布线控制器_1_jalr , \单周期硬布线控制器_1_lb ,
       \单周期硬布线控制器_1_memtoreg , \单周期硬布线控制器_1_memwrite , \单周期硬布线控制器_1_regwrite , \单周期硬布线控制器_1_s_type ;
  wire [1:0] Addr, id_ex_1_rs1forward_2, id_ex_1_rs2forward_2, priority_encoder_1_out,
       priority_encoder_2_out, rs1Fwd, rs2Fwd;
  wire [3:0] id_ex_1_aluop_2, \单周期硬布线控制器_1_alu_op ;
  wire [4:0] EX_rd, MEM_rd, multiplexer_2_out, multiplexer_3_out, WB_rd;
  wire [12:0] CNT_num;
  wire [15:0] \LoadUse次数 , \总周期数 , \插入气泡数 , \无条件分支数 , \条件分支成功数 ;
  wire [31:0] B_Addr, bit_extender_1_out, bit_extender_2_out, bit_extender_3_out, bit_extender_4_out,
       bit_extender_5_out, bit_extender_6_out, bit_extender_7_out, bit_extender_8_out, \byte , EX_IR,
       ex_mem_1_pc_4_2, EX_R1, EX_R2, id_ex_1_imm_2, id_ex_1_imm_b_2, id_ex_1_imm_j_2, id_ex_1_pc_4_2,
       id_ex_1_r1_2, id_ex_1_r2_2, ID_IR, if_id_1_pc_4_2, IF_IR, IF_PC_4, J_Addr, MEM_IR, MEM_R, MEM_R1,
       mem_wb_1_dataout_2, mem_wb_1_r_2, multiplexer_1_out, multiplexer_4_out, multiplexer_7_out, R,
       ram_1_data, regifile_falling_edge_1_r1, regifile_falling_edge_1_r2, shifter_1_out, shifter_2_out,
       WB_IR, WB_PC_4, WB_R1, WB_R2, word;

  Button \u_总复位  (.out(RST));
  Button _1 (.out(IR1));
  Button _2 (.out(IR2));
  Button _3 (.out(IR3));
  // Probe on \总周期数 
  // Probe on \总周期数 
  Button \u_继续运行  (.out(Go));
  LED #(.active("true")) led_1 (.in(W1));
  LED #(.active("true")) led_2 (.in(W2));
  LED #(.active("true")) led_3 (.in(W3));
  Hex_Digit_Display hex_digit_display_1 (.value(LedData[31:28]));  // open: dp
  // Probe on IF_PC[19:0]
  // RiscV_Probe riscv_probe_1: pin names not known; wires that end beside it: IF_IR
  Comparator #(.width(32), .mode("twosComplement")) comparator_1 (
    .a(WB_R1), .b(32'ha), .eq(comparator_1_eq));  // open: gt, lt
  Priority_Encoder #(.select(2), .disabled("Z")) priority_encoder_1 (
    .in0(1'b1), .in1(Branch), .in2(JAL), .in3(JALR), .out(priority_encoder_1_out));  // open: gs, en_out, en_in
  Multiplexer #(.select(2), .width(32), .disabled("Z"), .enable("false")) multiplexer_1 (
    .in0(IF_PC_4), .in1(B_Addr), .in2(J_Addr), .in3(R), .out(multiplexer_1_out), .sel(priority_encoder_1_out));
  and and_1 (and_1_out, ~stall, not_2_out);  // AND_Gate
  Hex_Digit_Display hex_digit_display_2 (.value(LedData[23:20]));  // open: dp
  Hex_Digit_Display hex_digit_display_3 (.value(LedData[27:24]));  // open: dp
  // Probe on ID_PC[19:0]
  // RiscV_Probe riscv_probe_2: pin names not known; wires that end beside it: ID_IR
  \重定向  \u_重定向_1  (
    .in_1(EX_rd), .in_3(MEM_rd), .in_4(EX_RegWrite), .in_5(MEM_RegWrite), .in_7(ID_ecall), .out_9(rs1Fwd),
    .out_10(rs2Fwd), .stall(stall), .BranchTaken(BranchTaken), .in_2(ID_IR), .in_6(EX_MemToReg), .flush(flush));
  Register #(.width(32), .trigger("rising"), .Select("low")) PC (
    .D(WB_R2), .en(and_2_out), .Q(LedData), .clk(CLK));  // open: clr
  and and_2 (and_2_out, WB_ecall, ~comparator_1_eq);  // AND_Gate
  and and_3 (and_3_out, WB_ecall, comparator_1_eq);
  Comparator #(.width(2), .mode("twosComplement")) comparator_2 (
    .a(2'b00), .b(priority_encoder_1_out), .eq(comparator_2_eq));  // open: gt, lt
  not not_1 (BranchTaken, comparator_2_eq);
  Register #(.width(32), .trigger("rising"), .Select("low")) PC_2 (
    .D(multiplexer_1_out), .en(and_1_out), .Q(IF_PC), .clk(CLK), .clr(RST));
  not not_2 (not_2_out, halt);
  Hex_Digit_Display hex_digit_display_4 (.value(LedData[15:12]));  // open: dp
  Hex_Digit_Display hex_digit_display_5 (.value(LedData[19:16]));  // open: dp
  and and_4 (halt, and_3_out, ~Go);  // AND_Gate
  Hex_Digit_Display hex_digit_display_6 (.value(LedData[11:8]));  // open: dp
  Hex_Digit_Display hex_digit_display_7 (.value(LedData[7:4]));  // open: dp
  Clock #(.highDuration(1), .lowDuration(1)) clock_1 (.out(clock_1_out));
  // Probe on EX_PC[19:0]
  // RiscV_Probe riscv_probe_3: pin names not known; wires that end beside it: clock_1_out, EX_IR, CLK
  not not_3 (not_3_out, halt);
  Adder #(.width(32)) adder_1 (.a(IF_PC), .b(32'h4), .out(IF_PC_4));  // open: cin, cout
  Hex_Digit_Display hex_digit_display_8 (.value(LedData[3:0]));  // open: dp
  and and_5 (and_5_out, Beq, tunnel_t);
  and and_6 (and_6_out, ~tunnel_t, Bne);  // AND_Gate
  and and_7 (and_7_out, tunnel_t_t, BGE);
  Counter #(.width(16), .max('hffff), .ongoal("stay"), .trigger("rising"), .behavior("old")) counter_1 (
    .count(not_3_out), .Q(\总周期数 ), .clk(CLK), .clr(RST));  // open: load, D, carry, preset
  ROM #(.addrWidth(10), .dataWidth(32), .Select("high")) rom_1 (.addr(IF_PC[11:2]), .data(IF_IR));
  // Probe on \总周期数 
  // Probe on M_PC[19:0]
  // RiscV_Probe riscv_probe_4: pin names not known; wires that end beside it: MEM_IR
  or or_1 (Branch, and_5_out, and_6_out, and_7_out);
  IF__ID if_id_1 (
    .IR(IF_IR), .PC(IF_PC), .PC_4(IF_PC_4), .IR_2(ID_IR), .PC_2(ID_PC), .PC_4_2(if_id_1_pc_4_2), .RST(RST),
    .CLK(CLK), .en(and_8_out), .BranchTaken(BranchTaken));  // open: PredictJump, PredictJump_2
  and and_8 (and_8_out, ~stall, not_4_out);  // AND_Gate
  not not_4 (not_4_out, halt);
  // Probe on \总周期数 
  // Probe on \无条件分支数 
  // Probe on \条件分支成功数 
  // Probe on \插入气泡数 
  // Probe on \LoadUse次数 
  // Probe on IF_PC[11:0]
  // Probe on WB_PC[19:0]
  // RiscV_Probe riscv_probe_5: pin names not known; wires that end beside it: WB_IR
  \单周期硬布线控制器  \u_单周期硬布线控制器_1  (
    .Funct({ID_IR[30], ID_IR[25], ID_IR[14:12]}), .OP(ID_IR[6:2]), .ALU_OP(\单周期硬布线控制器_1_alu_op ),
    .MemToReg(\单周期硬布线控制器_1_memtoreg ), .MemWrite(\单周期硬布线控制器_1_memwrite ), .ALU_SRC(\单周期硬布线控制器_1_alu_src ),
    .RegWrite(\单周期硬布线控制器_1_regwrite ), .ecall(ID_ecall), .S_type(\单周期硬布线控制器_1_s_type ),
    .Jalr(\单周期硬布线控制器_1_jalr ), .Beq(\单周期硬布线控制器_1_beq ), .JAL(\单周期硬布线控制器_1_jal ), .Bne(\单周期硬布线控制器_1_bne ),
    .in_3(ID_IR[21]), .LB(\单周期硬布线控制器_1_lb ), .BGE(\单周期硬布线控制器_1_bge ));  // open: uret, CSRRSI, CSRRCI
  Multiplexer #(.select(1), .width(5), .disabled("Z"), .enable("false")) multiplexer_2 (
    .in0(ID_IR[19:15]), .in1(5'b10001), .out(multiplexer_2_out), .sel(ID_ecall));
  Multiplexer #(.select(1), .width(5), .disabled("Z"), .enable("false")) multiplexer_3 (
    .in0(ID_IR[24:20]), .in1(5'b01010), .out(multiplexer_3_out), .sel(ID_ecall));
  assign bit_extender_1_out = {{20{ID_IR[31]}}, ID_IR[31:20]};  // Bit_Extender bit_extender_1
  assign bit_extender_2_out = {{20{ID_IR[31]}}, {ID_IR[31:25], ID_IR[11:7]}};  // Bit_Extender bit_extender_2
  // Probe on ID_PC[11:0]
  // Probe on EX_PC[11:0]
  Multiplexer #(.select(1), .width(32), .disabled("Z"), .enable("false")) multiplexer_4 (
    .in0(bit_extender_1_out), .in1(bit_extender_2_out), .out(multiplexer_4_out), .sel(\单周期硬布线控制器_1_s_type ));
  assign bit_extender_3_out = {{20{ID_IR[31]}}, {ID_IR[31], ID_IR[7], ID_IR[30:25], ID_IR[11:8]}};  // Bit_Extender bit_extender_3
  assign bit_extender_4_out = {{12{ID_IR[31]}}, {ID_IR[31], ID_IR[19:12], ID_IR[20], ID_IR[30:21]}};  // Bit_Extender bit_extender_4
  // Probe on M_PC[11:0]
  D_Flip_Flop #(.trigger("high"), .Pre_Clr_Positions("LEGACY"), .NegatePresetClear("false"), .enable("true"), .NewFFLayout("false")) d_ff_1 (.Q(d_ff_1_q));  // open: clk, D, Qn, preset, en, reset
  // Probe on 13'hc
  // Probe on WB_PC[11:0]
  Comparator #(.width(13), .mode("twosComplement")) comparator_3 (
    .a(CNT_num), .b(13'hc), .eq(comparator_3_eq), .lt(comparator_3_lt));  // open: gt
  Clock #(.highDuration(1), .lowDuration(1)) clock_2 (.out(clock_2_out));
  ID__EX id_ex_1 (
    .R1(regifile_falling_edge_1_r1), .R2(regifile_falling_edge_1_r2), .imm(multiplexer_4_out),
    .imm_b(bit_extender_3_out), .PC(ID_PC), .PC_4(if_id_1_pc_4_2), .IR(ID_IR), .rs1Forward(rs1Fwd),
    .rs2Forward(rs2Fwd), .R1_2(id_ex_1_r1_2), .R2_2(id_ex_1_r2_2), .imm_2(id_ex_1_imm_2),
    .imm_b_2(id_ex_1_imm_b_2), .PC_2(EX_PC), .PC_4_2(id_ex_1_pc_4_2), .IR_2(EX_IR),
    .rs1Forward_2(id_ex_1_rs1forward_2), .rs2Forward_2(id_ex_1_rs2forward_2), .RST_2(RST),
    .imm_j(bit_extender_4_out), .imm_j_2(id_ex_1_imm_j_2), .BGE_2(\单周期硬布线控制器_1_bge ), .LB(\单周期硬布线控制器_1_lb ),
    .JALR(\单周期硬布线控制器_1_jalr ), .JAL(\单周期硬布线控制器_1_jal ), .Beq(\单周期硬布线控制器_1_beq ), .Bne(\单周期硬布线控制器_1_bne ),
    .MemToReg(\单周期硬布线控制器_1_memtoreg ), .MemWrite(\单周期硬布线控制器_1_memwrite ), .AluSrcB(\单周期硬布线控制器_1_alu_src ),
    .RegWrite(\单周期硬布线控制器_1_regwrite ), .ecall(ID_ecall), .AluOP(\单周期硬布线控制器_1_alu_op ), .rd(ID_IR[11:7]),
    .BGE_4(BGE), .LB_2(id_ex_1_lb_2), .JALR_2(JALR), .JAL_2(JAL), .Beq_2(Beq), .Bne_2(Bne),
    .MemToReg_2(EX_MemToReg), .MemWrite_2(id_ex_1_memwrite_2), .AluSrcB_2(id_ex_1_alusrcb_2),
    .RegWrite_2(EX_RegWrite), .ecall_2(EX_ecall), .AluOP_2(id_ex_1_aluop_2), .rd_2(EX_rd), .CLK(CLK),
    .en(not_4_out), .flush(flush));  // open: BGE, BGE_3, RST
  Regifile_Falling_Edge regifile_falling_edge_1 (
    .Din(RDin), .Clk(CLK), .R1(regifile_falling_edge_1_r1), .R2(regifile_falling_edge_1_r2), .WE(RegWrite),
    .W_num(WB_rd), .R1_num(multiplexer_2_out), .R2_num(multiplexer_3_out));
  nand nand_1 (nand_1_out, d_ff_1_q, comparator_3_eq);
  Counter #(.width(13), .max('h1fff), .ongoal("stay"), .trigger("rising"), .behavior("old")) counter_2 (
    .count(comparator_3_lt), .Q(CNT_num), .clk(clock_2_out));  // open: load, D, carry, clr, preset
  assign CLK = nand_1_out ? clock_2_out : 1'bz;  // Controlled_Buffer controlled_buffer_1
  Multiplexer #(.select(2), .width(32), .disabled("Z"), .enable("false")) multiplexer_5 (
    .in0(id_ex_1_r1_2), .in1(MEM_R), .in2(RDin), .out(EX_R1), .sel(id_ex_1_rs1forward_2));  // open: in3
  Multiplexer #(.select(2), .width(32), .disabled("Z"), .enable("false")) multiplexer_6 (
    .in0(id_ex_1_r2_2), .in1(MEM_R), .in2(RDin), .out(EX_R2), .sel(id_ex_1_rs2forward_2));  // open: in3
  Shifter #(.width(32), .shift("ll")) shifter_1 (.in(id_ex_1_imm_b_2), .\dist (5'b00001), .out(shifter_1_out));
  Shifter #(.width(32), .shift("ll")) shifter_2 (.in(id_ex_1_imm_j_2), .\dist (5'b00001), .out(shifter_2_out));
  Pull_Resistor #(.pull(1)) pull_resistor_1 (.node(CLK));
  Adder #(.width(32)) adder_2 (.a(shifter_1_out), .b(EX_PC), .out(B_Addr));  // open: cin, cout
  Adder #(.width(32)) adder_3 (.a(shifter_2_out), .b(EX_PC), .out(J_Addr));  // open: cin, cout
  Multiplexer #(.select(1), .width(32), .disabled("Z"), .enable("false")) multiplexer_7 (
    .in0(EX_R2), .in1(id_ex_1_imm_2), .out(multiplexer_7_out), .sel(id_ex_1_alusrcb_2));
  or or_2 (or_2_out, JAL, JALR);
  and and_9 (and_9_out, stall, ~halt);  // AND_Gate
  ALU alu_1 (
    .X(EX_R1), .Y(multiplexer_7_out), .AluOP(id_ex_1_aluop_2), .Equal(tunnel_t), .Result(R),
    .out_4(tunnel_t_t), .out_6(tunnel));  // open: Result_2
  Counter #(.width(16), .max('hffff), .ongoal("wrap"), .trigger("rising"), .behavior("old")) counter_3 (
    .count(or_2_out), .Q(\无条件分支数 ), .clk(CLK), .clr(RST));  // open: load, D, carry, preset
  Counter #(.width(16), .max('hffff), .ongoal("wrap"), .trigger("rising"), .behavior("old")) counter_4 (
    .count(Branch), .Q(\条件分支成功数 ), .clk(CLK), .clr(RST));  // open: load, D, carry, preset
  Counter #(.width(16), .max('hffff), .ongoal("wrap"), .trigger("rising"), .behavior("old")) counter_5 (
    .count(and_9_out), .Q(\LoadUse次数 ), .clk(CLK), .clr(RST));  // open: load, D, carry, preset
  EX__MEM ex_mem_1 (
    .LB(id_ex_1_lb_2), .JALR(JALR), .MemToReg(EX_MemToReg), .MemWrite(id_ex_1_memwrite_2),
    .RegWrite(EX_RegWrite), .R1(EX_R1), .rd(EX_rd), .R(R), .MD(EX_R2), .IR(EX_IR), .PC(EX_PC),
    .PC_4(id_ex_1_pc_4_2), .LB_2(ex_mem_1_lb_2), .JALR_2(ex_mem_1_jalr_2), .MemToReg_2(ex_mem_1_memtoreg_2),
    .MemWrite_2(MemWrite), .RegWrite_2(MEM_RegWrite), .R1_2(MEM_R1), .rd_2(MEM_rd), .R_2(MEM_R), .MD_2(MDin),
    .IR_2(MEM_IR), .PC_2(M_PC), .PC_4_2(ex_mem_1_pc_4_2), .RST(RST), .CLK(CLK), .JAL(JAL),
    .JAL_2(ex_mem_1_jal_2), .ecall(EX_ecall), .RegWrite_3(MEM_ecall), .en(not_4_out));
  RAM #(.addrWidth(10), .dataWidth(32), .bus("separate"), .Select("high")) ram_1 (
    .addr(MEM_R[11:2]), .din(MDin), .data(ram_1_data), .str(MemWrite), .sel(1'b1), .clk(CLK), .ld(1'b1),
    .clr(RST));
  MEM__WB mem_wb_1 (
    .JALR(ex_mem_1_jalr_2), .JAL(ex_mem_1_jal_2), .MenToReg(ex_mem_1_memtoreg_2), .RegWrite(MEM_RegWrite),
    .rd(MEM_rd), .R(MEM_R), .Dataout(ram_1_data), .IR(MEM_IR), .PC(M_PC), .PC_4(ex_mem_1_pc_4_2),
    .JALR_2(WB_JALR), .JAL_2(WB_JAL), .MemToReg(MemToReg), .RegWrite_2(RegWrite), .rd_2(WB_rd),
    .R_2(mem_wb_1_r_2), .Dataout_2(mem_wb_1_dataout_2), .IR_2(WB_IR), .PC_2(WB_PC), .PC_4_2(WB_PC_4),
    .RST(RST), .CLK(CLK), .LB(ex_mem_1_lb_2), .LB_2(LB), .Addr_2(Addr), .addr(MEM_R[1:0]), .R1(MEM_R1),
    .R1_2(WB_R1), .R2(MDin), .R2_2(WB_R2), .ecall(MEM_ecall), .ecall_2(WB_ecall), .en(not_4_out));
  or or_3 (or_3_out, WB_JAL, WB_JALR);
  Priority_Encoder #(.select(2), .disabled("Z")) priority_encoder_2 (
    .in0(1'b1), .in1(MemToReg), .in2(or_3_out), .out(priority_encoder_2_out));  // open: in3, gs, en_out, en_in
  Multiplexer #(.select(2), .width(32), .disabled("Z"), .enable("false")) multiplexer_8 (
    .in0(mem_wb_1_r_2), .in1(mem_wb_1_dataout_2), .in2(WB_PC_4), .out(word), .sel(priority_encoder_2_out));  // open: in3
  assign bit_extender_5_out = {{24{word[7]}}, word[7:0]};  // Bit_Extender bit_extender_5
  assign bit_extender_6_out = {{24{word[15]}}, word[15:8]};  // Bit_Extender bit_extender_6
  assign bit_extender_7_out = {{24{word[23]}}, word[23:16]};  // Bit_Extender bit_extender_7
  assign bit_extender_8_out = {{24{word[31]}}, word[31:24]};  // Bit_Extender bit_extender_8
  Multiplexer #(.select(1), .width(32), .disabled("Z"), .enable("false")) multiplexer_9 (
    .in0(word), .in1(\byte ), .out(RDin), .sel(LB));
  Multiplexer #(.select(2), .width(32), .disabled("Z"), .enable("false")) multiplexer_10 (
    .in0(bit_extender_5_out), .in1(bit_extender_6_out), .in2(bit_extender_7_out), .in3(bit_extender_8_out),
    .out(\byte ), .sel(Addr));

  // Other names for the same wires on the sheet: ID_rd[4:0] = ID_IR[11:7]; MEM_PC[31:0] = M_PC

  // Notes on the sheet:
  //   中断源
  //   时空图监测，可删除
  //   中断等待指示
  //   数码管输出
  //   指令存储器
  //   contents of rom_1 (hex, n*v repeats v):
  //   100493 100006f 100493 200913 300993 100006f 100493 200913 300993 100006f 100493 200913 300993
  //   100006f 100493 200913 300993 3d0000ef 100413 100493 1f49493 900533 2200893 73 24d493 48463 fedff06f
  //   900533 2200893 73 100493 249493 900533 2200893 73 48463 fedff06f 100493 1f49493 900533 2200893 73
  //   4034d493 900533 2200893 73 4044d493 900533 2200893 73 4044d493 900533 2200893 73 4044d493 900533
  //   2200893 73 4044d493 900533 2200893 73 4044d493 900533 2200893 73 4044d493 900533 2200893 73 4044d493
  //   900533 2200893 73 100413 1f41993 41f9d993 433 c00913 300b13 140413 f47413 800293 100313 499993
  //   89e9b3 1300533 2200893 73 406282b3 fe0294e3 140413 f00f93 1f47433 1c41413 800293 100313 49d993
  //   89e9b3 1300533 2200893 73 406282b3 fe0294e3 1c45413 406b0b33 b0463 f95ff06f 2b3 fff2c293 829293
  //   ff2e293 500533 2200893 73 fff00413 493 84a023 140413 448493 84a023 140413 448493 84a023 140413
  //   448493 84a023 140413 448493 84a023 140413 448493 84a023 140413 448493 84a023 140413 448493 84a023
  //   140413 448493 84a023 140413 448493 84a023 140413 448493 84a023 140413 448493 84a023 140413 448493
  //   84a023 140413 448493 84a023 140413 448493 84a023 140413 448493 84a023 140413 448493 140413 433
  //   3c00493 42983 4aa03 149a2b3 28663 134a023 1442023 ffc48493 fe9412e3 800533 2200893 73 440413 3c00493
  //   fc9416e3 a00893 73 100293 300313 800493 849493 7648493 900533 2200893 73 800e13 5494b3 6494b3 900533
  //   2200893 73 fffe0e13 fe0e14e3 a00893 73 100293 300313 800493 849493 7648493 1449493 900533 2200893 73
  //   800e13 54d4b3 64d4b3 900533 2200893 73 fffe0e13 fe0e14e3 a00893 73 313 1000e13 8400493 849493
  //   8348493 400913 891913 490913 849493 8248493 849493 8148493 891913 490913 891913 490913 932023
  //   12484b3 430313 fffe0e13 fe0e18e3 2000e13 313 30483 900533 2200893 73 130313 fffe0e13 fe0e14e3 a00893
  //   73 f00493 900533 2200893 73 fff48493 fe04d8e3 a00893 73 413 140413 800533 2200893 73 240413 800533
  //   2200893 73 340413 800533 2200893 73 440413 800533 2200893 73 540413 800533 2200893 73 640413 800533
  //   2200893 73 740413 800533 2200893 73 840413 800533 2200893 2200893 73 8067
  //   JAL
  //   JALR
  //   LB
  //   BGE
  //   Beq
  //   Bne
  //   AluOP
  //   AluSrcB
  //   RegWrite
  //   S_Type
  //   控制位
  //   MemToReg
  //   MemWrite
  //   流水调试日志用
  //   暂停节拍，不能为0
  //   戳工具置1进入计数暂停模式，ctrl+k时钟自动运行到对应节拍暂停
  //   ctrl+k关闭时钟连续运行，将控制位置零，进入单步调试模式调试
  //   LB
  //   JALR
  //   JAL
  //   MemWrite
  //   AluOP
  //   AluSrcB
  //   可计数暂停的时钟源
  //   为方便自动评测，需要输出流水线各段保存的PC值，注意是PC不是PC+4，另外ID段寄存器写入信息，Mem段内存写入信息也要输出
  //   LB
  //   JALR
  //   JAL
  //   MemToReg
  //   数据存储器
endmodule

module \中断按键参考电路  (
  input  \同步清零信号 ,
  output \与中断屏蔽位与 
);

  wire \_1号中断_out , and_1_out, clock_1_out, d_ff_1_q, or_1_out, or_2_out;

  Button \_1号中断  (.out(\_1号中断_out ));
  or or_1 (or_1_out, \与中断屏蔽位与 , d_ff_1_q);
  LED #(.active("true")) \_1号中断等待指示灯  (.in(or_1_out));
  D_Flip_Flop #(.trigger("rising"), .Pre_Clr_Positions("LEGACY"), .NegatePresetClear("false"), .enable("true"), .NewFFLayout("false")) d_ff_1 (
    .clk(\_1号中断_out ), .D(1'b1), .Q(d_ff_1_q), .reset(\与中断屏蔽位与 ));  // open: Qn, preset, en
  or or_2 (or_2_out, d_ff_1_q, \与中断屏蔽位与 );
  Clock #(.highDuration(1), .lowDuration(1)) clock_1 (.out(clock_1_out));
  and and_1 (and_1_out, or_2_out, ~\同步清零信号 );  // AND_Gate
  D_Flip_Flop #(.trigger("rising"), .Pre_Clr_Positions("LEGACY"), .NegatePresetClear("false"), .enable("true"), .NewFFLayout("false")) IR1 (
    .clk(clock_1_out), .D(and_1_out), .Q(\与中断屏蔽位与 ));  // open: Qn, preset, en, reset

  // Notes on the sheet:
  //   中断信号采样参考电路
  //   Reset 
endmodule
module \单周期_单级中断  (
  input  IR1,
  input  IR2,
  input  IR3,
  output RegWrite,
  output MemWrite,
  output [31:0] PC,
  output [31:0] IR,
  output [31:0] RDin,
  output [31:0] MDin,
  output [31:0] LedData
);

  wire and_1_out, and_2_out, and_3_out, and_4_out, and_5_out, and_7_out, and_8_out, and_9_out, Beq, BGE, Bne,
       Branch, CLK, Clr1, Clr2, Clr3, comparator_1_eq, d_ff_1_q, d_ff_2_q, d_ff_3_q, d_ff_4_q, d_ff_5_q,
       d_ff_6_q, decoder_1_out1, decoder_1_out2, decoder_1_out3, ecall, Go, halt, IE, INT, IR1_t, IR2_t,
       IR3_t, IRA, IRB, IRC, JAL, JALR, LB, MemToReg, not_1_out, not_2_out, not_3_out, or_5_out, or_6_out,
       or_7_out, or_11_out, register_2_q, RST, tunnel, tunnel_t, tunnel_t_t, URET, W1, W2, W3, \中断信号 ,
       \单周期硬布线控制器_1_alu_src , \单周期硬布线控制器_1_s_type ;
  wire [1:0] Addr, now, priority_encoder_1_out, priority_encoder_2_out, priority_encoder_4_out, \中断号 ;
  wire [3:0] \单周期硬布线控制器_1_alu_op ;
  wire [4:0] multiplexer_3_out, multiplexer_4_out;
  wire [15:0] \总周期数 ;
  wire [31:0] B_Addr, bit_extender_1_out, bit_extender_2_out, bit_extender_3_out, bit_extender_4_out,
       bit_extender_5_out, bit_extender_6_out, bit_extender_7_out, bit_extender_8_out, \byte , INT_PC,
       J_Addr, multiplexer_2_out, multiplexer_5_out, multiplexer_7_out, PC_4, R1, ram_1_data, RET_PC,
       shifter_1_out, shifter_2_out, word, \现场 ;
  wire [31:2] R;

  Clock #(.highDuration(1), .lowDuration(1)) clock_1 (.out(CLK));
  Button _1 (.out(IRA));
  Button _2 (.out(IRB));
  Button _3 (.out(IRC));
  Button \u_继续运行  (.out(Go));
  LED #(.active("true")) led_1 (.in(W1));
  LED #(.active("true")) led_2 (.in(W2));
  LED #(.active("true")) led_3 (.in(W3));
  Hex_Digit_Display hex_digit_display_1 (.value(LedData[31:28]));  // open: dp
  Priority_Encoder #(.select(2), .disabled("Z")) priority_encoder_1 (
    .in0(1'b1), .in1(Branch), .in2(JAL), .in3(JALR), .out(priority_encoder_1_out));  // open: gs, en_out, en_in
  Comparator #(.width(32), .mode("twosComplement")) comparator_1 (
    .a(R1), .b(32'ha), .eq(comparator_1_eq));  // open: gt, lt
  Hex_Digit_Display hex_digit_display_2 (.value(LedData[23:20]));  // open: dp
  Hex_Digit_Display hex_digit_display_3 (.value(LedData[27:24]));  // open: dp
  and and_1 (and_1_out, Beq, tunnel_t);
  and and_2 (and_2_out, ~tunnel_t, Bne);  // AND_Gate
  or or_1 (Branch, and_1_out, and_2_out, and_3_out);
  and and_3 (and_3_out, tunnel_t_t, BGE);
  Multiplexer #(.select(2), .width(32), .disabled("Z"), .enable("false")) multiplexer_1 (
    .in0(PC_4), .in1(B_Addr), .in2(J_Addr), .in3({R, Addr}), .out(\现场 ), .sel(priority_encoder_1_out));
  Priority_Encoder #(.select(2), .disabled("Z")) priority_encoder_2 (
    .in0(1'b1), .in1(URET), .in2(INT), .out(priority_encoder_2_out));  // open: in3, gs, en_out, en_in
  and and_4 (and_4_out, ecall, ~comparator_1_eq);  // AND_Gate
  and and_5 (and_5_out, ecall, comparator_1_eq);
  Hex_Digit_Display hex_digit_display_4 (.value(LedData[19:16]));  // open: dp
  Hex_Digit_Display hex_digit_display_5 (.value(LedData[15:12]));  // open: dp
  Multiplexer #(.select(2), .width(32), .disabled("Z"), .enable("false")) multiplexer_2 (
    .in0(\现场 ), .in1(RET_PC), .in2(INT_PC), .out(multiplexer_2_out), .sel(priority_encoder_2_out));  // open: in3
  not not_1 (not_1_out, halt);
  Register #(.width(32), .trigger("rising"), .Select("low")) u_PC (
    .D(MDin), .en(and_4_out), .Q(LedData), .clk(CLK));  // open: clr
  and and_6 (halt, and_5_out, ~Go);  // AND_Gate
  Hex_Digit_Display hex_digit_display_6 (.value(LedData[7:4]));  // open: dp
  Hex_Digit_Display hex_digit_display_7 (.value(LedData[11:8]));  // open: dp
  // Probe on \总周期数 
  or or_2 (W1, d_ff_4_q, d_ff_1_q);
  or or_3 (W2, d_ff_5_q, d_ff_2_q);
  or or_4 (W3, d_ff_6_q, d_ff_3_q);
  Register #(.width(32), .trigger("rising"), .Select("low")) PC_2 (
    .D(multiplexer_2_out), .en(not_1_out), .Q(PC), .clk(CLK), .clr(RST));
  Hex_Digit_Display hex_digit_display_8 (.value(LedData[3:0]));  // open: dp
  D_Flip_Flop #(.trigger("rising"), .Pre_Clr_Positions("LEGACY"), .NegatePresetClear("false"), .enable("false"), .NewFFLayout("false")) d_ff_1 (
    .clk(IR1_t), .D(1'b1), .Q(d_ff_1_q), .reset(d_ff_4_q));  // open: Qn, preset
  D_Flip_Flop #(.trigger("rising"), .Pre_Clr_Positions("LEGACY"), .NegatePresetClear("false"), .enable("false"), .NewFFLayout("false")) d_ff_2 (
    .clk(IR2_t), .D(1'b1), .Q(d_ff_2_q), .reset(d_ff_5_q));  // open: Qn, preset
  D_Flip_Flop #(.trigger("rising"), .Pre_Clr_Positions("LEGACY"), .NegatePresetClear("false"), .enable("false"), .NewFFLayout("false")) d_ff_3 (
    .clk(IR3_t), .D(1'b1), .Q(d_ff_3_q), .reset(d_ff_6_q));  // open: Qn, preset
  Counter #(.width(16), .max('hffff), .ongoal("stay"), .trigger("rising"), .behavior("old")) counter_1 (
    .count(not_2_out), .Q(\总周期数 ), .clk(CLK), .clr(RST));  // open: load, D, carry, preset
  not not_2 (not_2_out, halt);
  or or_5 (or_5_out, d_ff_1_q, d_ff_4_q);
  or or_6 (or_6_out, d_ff_2_q, d_ff_5_q);
  or or_7 (or_7_out, d_ff_3_q, d_ff_6_q);
  // RiscV_Probe riscv_probe_1: pin names not known; wires that end beside it: IR
  ROM #(.addrWidth(10), .dataWidth(32), .Select("high")) rom_1 (.addr(PC[11:2]), .data(IR));
  Adder #(.width(32)) adder_1 (.a(PC), .b(32'h4), .out(PC_4));  // open: cin, cout
  or or_8 (IR1_t, IR1, IRA);
  and and_7 (and_7_out, or_5_out, ~Clr1);  // AND_Gate
  and and_8 (and_8_out, or_6_out, ~Clr2);  // AND_Gate
  and and_9 (and_9_out, or_7_out, ~Clr3);  // AND_Gate
  or or_9 (IR2_t, IR2, IRB);
  D_Flip_Flop #(.trigger("rising"), .Pre_Clr_Positions("LEGACY"), .NegatePresetClear("false"), .enable("false"), .NewFFLayout("false")) d_ff_4 (
    .clk(CLK), .D(and_7_out), .Q(d_ff_4_q), .reset(RST));  // open: Qn, preset
  D_Flip_Flop #(.trigger("rising"), .Pre_Clr_Positions("LEGACY"), .NegatePresetClear("false"), .enable("false"), .NewFFLayout("false")) d_ff_5 (
    .clk(CLK), .D(and_8_out), .Q(d_ff_5_q), .reset(RST));  // open: Qn, preset
  D_Flip_Flop #(.trigger("rising"), .Pre_Clr_Positions("LEGACY"), .NegatePresetClear("false"), .enable("false"), .NewFFLayout("false")) d_ff_6 (
    .clk(CLK), .D(and_9_out), .Q(d_ff_6_q), .reset(RST));  // open: Qn, preset
  \单周期硬布线控制器  \u_单周期硬布线控制器_1  (
    .Funct({IR[30], IR[25], IR[14:12]}), .OP(IR[6:2]), .ALU_OP(\单周期硬布线控制器_1_alu_op ), .MemToReg(MemToReg),
    .MemWrite(MemWrite), .ALU_SRC(\单周期硬布线控制器_1_alu_src ), .RegWrite(RegWrite), .ecall(ecall),
    .S_type(\单周期硬布线控制器_1_s_type ), .Jalr(JALR), .Beq(Beq), .JAL(JAL), .Bne(Bne), .in_3(IR[21]), .uret(URET),
    .LB(LB), .BGE(BGE));  // open: CSRRSI, CSRRCI
  Multiplexer #(.select(1), .width(5), .disabled("Z"), .enable("false")) multiplexer_3 (
    .in0(IR[19:15]), .in1(5'b10001), .out(multiplexer_3_out), .sel(ecall));
  Multiplexer #(.select(1), .width(5), .disabled("Z"), .enable("false")) multiplexer_4 (
    .in0(IR[24:20]), .in1(5'b01010), .out(multiplexer_4_out), .sel(ecall));
  assign bit_extender_1_out = {{20{IR[31]}}, IR[31:20]};  // Bit_Extender bit_extender_1
  assign bit_extender_2_out = {{20{IR[31]}}, {IR[31:25], IR[11:7]}};  // Bit_Extender bit_extender_2
  Priority_Encoder #(.select(2), .disabled("Z")) priority_encoder_3 (
    .in1(d_ff_4_q), .in2(d_ff_5_q), .in3(d_ff_6_q), .out(\中断号 ), .gs(\中断信号 ));  // open: in0, en_out, en_in
  Multiplexer #(.select(1), .width(32), .disabled("Z"), .enable("false")) multiplexer_5 (
    .in0(bit_extender_1_out), .in1(bit_extender_2_out), .out(multiplexer_5_out), .sel(\单周期硬布线控制器_1_s_type ));
  assign bit_extender_3_out = {{20{IR[31]}}, {IR[31], IR[7], IR[30:25], IR[11:8]}};  // Bit_Extender bit_extender_3
  assign bit_extender_4_out = {{12{IR[31]}}, {IR[31], IR[19:12], IR[20], IR[30:21]}};  // Bit_Extender bit_extender_4
  or or_10 (IR3_t, IR3, IRC);
  Register #(.width(2), .trigger("falling"), .Select("low")) register_1 (
    .D(\中断号 ), .Q(now), .clk(INT), .clr(RST));  // open: en
  Multiplexer #(.select(2), .width(32), .disabled("Z"), .enable("false")) multiplexer_6 (
    .in1(32'h30ac), .in2(32'h3150), .in3(32'h31f4), .out(INT_PC), .sel(\中断号 ));  // open: in0
  Shifter #(.width(32), .shift("ll")) shifter_1 (.in(bit_extender_3_out), .\dist (5'b00001), .out(shifter_1_out));
  Shifter #(.width(32), .shift("ll")) shifter_2 (.in(bit_extender_4_out), .\dist (5'b00001), .out(shifter_2_out));
  Button \u_总复位  (.out(RST));
  Decoder #(.select(2), .tristate("false"), .disabled("Z"), .enable("false")) decoder_1 (
    .out1(decoder_1_out1), .out2(decoder_1_out2), .out3(decoder_1_out3), .sel(now));  // open: out0
  Regifile regifile_1 (
    .Din(RDin), .Clk(CLK), .R1(R1), .R2(MDin), .WE(RegWrite), .W_num(IR[11:7]), .R1_num(multiplexer_3_out),
    .R2_num(multiplexer_4_out));
  Adder #(.width(32)) adder_2 (.a(shifter_1_out), .b(PC), .out(B_Addr));  // open: cin, cout
  Adder #(.width(32)) adder_3 (.a(shifter_2_out), .b(PC), .out(J_Addr));  // open: cin, cout
  and and_10 (Clr1, decoder_1_out1, URET);
  and and_11 (Clr2, decoder_1_out2, URET);
  and and_12 (Clr3, decoder_1_out3, URET);
  Multiplexer #(.select(1), .width(32), .disabled("Z"), .enable("false")) multiplexer_7 (
    .in0(MDin), .in1(multiplexer_5_out), .out(multiplexer_7_out), .sel(\单周期硬布线控制器_1_alu_src ));
  ALU alu_1 (
    .X(R1), .Y(multiplexer_7_out), .AluOP(\单周期硬布线控制器_1_alu_op ), .Equal(tunnel_t), .Result({R, Addr}),
    .out_4(tunnel_t_t), .out_6(tunnel));  // open: Result_2
  Register #(.width(32), .trigger("falling"), .Select("low")) mEPC (
    .D(\现场 ), .Q(RET_PC), .clk(INT), .clr(RST));  // open: en
  D_Flip_Flop #(.trigger("rising"), .Pre_Clr_Positions("LEGACY"), .NegatePresetClear("false"), .enable("false"), .NewFFLayout("false")) d_ff_7 (
    .clk(not_3_out), .D(1'b0), .Qn(IE), .preset(register_2_q), .reset(RST));  // open: Q
  not not_3 (not_3_out, URET);
  Register #(.width(1), .trigger("rising"), .Select("low")) register_2 (
    .D(INT), .Q(register_2_q), .clk(CLK), .clr(RST));  // open: en
  and and_13 (INT, IE, \中断信号 );
  or or_11 (or_11_out, JAL, JALR);
  RAM #(.addrWidth(10), .dataWidth(32), .bus("separate"), .Select("high")) ram_1 (
    .addr(R[11:2]), .din(MDin), .data(ram_1_data), .str(MemWrite), .sel(1'b1), .clk(CLK), .ld(1'b1), .clr(RST));
  Priority_Encoder #(.select(2), .disabled("Z")) priority_encoder_4 (
    .in0(1'b1), .in1(MemToReg), .in2(or_11_out), .out(priority_encoder_4_out));  // open: in3, gs, en_out, en_in
  Multiplexer #(.select(2), .width(32), .disabled("Z"), .enable("false")) multiplexer_8 (
    .in0({R, Addr}), .in1(ram_1_data), .in2(PC_4), .out(word), .sel(priority_encoder_4_out));  // open: in3
  assign bit_extender_5_out = {{24{word[7]}}, word[7:0]};  // Bit_Extender bit_extender_5
  assign bit_extender_6_out = {{24{word[15]}}, word[15:8]};  // Bit_Extender bit_extender_6
  assign bit_extender_7_out = {{24{word[23]}}, word[23:16]};  // Bit_Extender bit_extender_7
  assign bit_extender_8_out = {{24{word[31]}}, word[31:24]};  // Bit_Extender bit_extender_8
  Multiplexer #(.select(1), .width(32), .disabled("Z"), .enable("false")) multiplexer_9 (
    .in0(word), .in1(\byte ), .out(RDin), .sel(LB));
  Multiplexer #(.select(2), .width(32), .disabled("Z"), .enable("false")) multiplexer_10 (
    .in0(bit_extender_5_out), .in1(bit_extender_6_out), .in2(bit_extender_7_out), .in3(bit_extender_8_out),
    .out(\byte ), .sel(Addr));

  // Other names for the same wires on the sheet: R[1:0] = Addr

  // Notes on the sheet:
  //   中断源
  //   中断等待指示
  //   总复位信号应将除ROM以外所有存储组件全部清零
  //   数码管输出
  //   数码管输出应该用寄存器锁存，否则显示数据只能一闪而过
  //   指令探针
  //   指令存储器
  //   contents of rom_1 (hex, n*v repeats v):
  //   7d000113 100413 1f41993 41f9d993 433 c00913 800b13 140413 f47413 800293 100313 499993 89e9b3 1300533
  //   2200893 73 406282b3 fe0294e3 140413 f00f93 1f47433 1c41413 800293 100313 49d993 89e9b3 1300533
  //   2200893 73 406282b3 fe0294e3 1c45413 406b0b33 b0463 f95ff06f 2b3 fff2c293 1029293 fff2e293 500533
  //   2200893 73 f5dff06f 1112023 410113 a12023 410113 812023 410113 1312023 410113 1412023 410113 1512023
  //   410113 1612023 410113 100b13 300a13 100a93 1600433 441413 14469b3 1300533 2200893 73 fe0416e3
  //   415a0a33 fe0a10e3 ffc10113 12b03 ffc10113 12a83 ffc10113 12a03 ffc10113 12983 ffc10113 12403
  //   ffc10113 12503 ffc10113 12883 200073 1112023 410113 a12023 410113 812023 410113 1312023 410113
  //   1412023 410113 1512023 410113 1612023 410113 200b13 300a13 100a93 1600433 441413 14469b3 1300533
  //   2200893 73 fe0416e3 415a0a33 fe0a10e3 ffc10113 12b03 ffc10113 12a83 ffc10113 12a03 ffc10113 12983
  //   ffc10113 12403 ffc10113 12503 ffc10113 12883 200073 1112023 410113 a12023 410113 812023 410113
  //   1312023 410113 1412023 410113 1512023 410113 1612023 410113 300b13 300a13 100a93 1600433 441413
  //   14469b3 1300533 2200893 73 fe0416e3 415a0a33 fe0a10e3 ffc10113 12b03 ffc10113 12a83 ffc10113 12a03
  //   ffc10113 12983 ffc10113 12403 ffc10113 12503 ffc10113 12883 200073
  //   指令字
  //   JAL
  //   JALR
  //   URET
  //   Beq
  //   Bne
  //   MemToReg
  //   MemWrite
  //   AluOP
  //   AluSrcB
  //   RegWrite
  //   S_Type
  //   入口
  //   返回清零
  //   为方便自动评测，需要输出PC，IR，寄存器堆写如数据RDin
  //   RAM写使能MemWrite、RAM写入数据MDin等信号
  //   保存现场
  //   中断使能
  //   中断请求
  //   数据存储器
endmodule

module \单周期_多级中断  (
  input  IR1,
  input  IR2,
  input  IR3,
  output RegWrite,
  output MemWrite,
  output [31:0] PC,
  output [31:0] IR,
  output [31:0] RDin,
  output [31:0] MDin,
  output [31:0] LedData
);

  wire _1, _2, _3, and_1_out, and_2_out, and_3_out, and_4_out, and_5_out, and_6_out, and_7_out, and_8_out,
       and_13_out, and_14_out, and_15_out, and_16_out, and_17_out, and_18_out, Beq, BGE, Bne, Branch, CLK,
       Clr1, Clr2, Clr3, comparator_1_eq, comparator_3_eq, CSRRCI, CSRRSI, d_ff_1_q, d_ff_2_q, d_ff_3_q,
       d_ff_4_q, d_ff_5_q, d_ff_6_q, d_ff_7_qn, decoder_1_out1, decoder_1_out2, ecall, Go, halt, IE, IE0,
       IE1, IE2, IE3, INT, IR1_t, IR2_t, IR3_t, IRA, IRB, IRC, JAL, JALR, LB, MemToReg, multiplexer_3_out,
       multiplexer_16_out, \new , not_1_out, not_2_out, not_3_out, or_4_out, or_5_out, or_6_out, or_11_out,
       or_12_out, or_13_out, or_14_out, or_15_out, register_5_q, register_6_q, register_7_q, RST, tunnel,
       tunnel_t, tunnel_t_t, URET, W1, W2, W3, \中断信号 , \单周期硬布线控制器_1_alu_src , \单周期硬布线控制器_1_s_type ;
  wire [1:0] Addr, last, multiplexer_5_out, multiplexer_8_out, now, priority_encoder_1_out,
       priority_encoder_2_out, priority_encoder_4_out, register_1_q, register_2_q, register_3_q,
       subtractor_1_out, \中断号 , \级数 ;
  wire [3:0] \单周期硬布线控制器_1_alu_op ;
  wire [4:0] multiplexer_6_out, multiplexer_7_out;
  wire [15:0] \总周期数 ;
  wire [31:0] B_Addr, bit_extender_1_out, bit_extender_2_out, bit_extender_3_out, bit_extender_4_out,
       bit_extender_5_out, bit_extender_6_out, bit_extender_7_out, bit_extender_8_out, \byte , INT_PC,
       J_Addr, mEPC1_q, mEPC2_q, mEPC_q, multiplexer_2_out, multiplexer_10_out, multiplexer_12_out, PC_4, R1,
       ram_1_data, RET_PC, shifter_1_out, shifter_2_out, word, \现场 ;
  wire [31:2] R;

  Clock #(.highDuration(1), .lowDuration(1)) clock_1 (.out(CLK));
  Button u__1 (.out(IRA));
  Button u__2 (.out(IRB));
  Button u__3 (.out(IRC));
  Button \u_继续运行  (.out(Go));
  LED #(.active("true")) led_1 (.in(W1));
  LED #(.active("true")) led_2 (.in(W2));
  LED #(.active("true")) led_3 (.in(W3));
  Hex_Digit_Display hex_digit_display_1 (.value(LedData[31:28]));  // open: dp
  or or_1 (W1, d_ff_4_q, d_ff_1_q);
  or or_2 (W2, d_ff_5_q, d_ff_2_q);
  or or_3 (W3, d_ff_6_q, d_ff_3_q);
  Comparator #(.width(32), .mode("twosComplement")) comparator_1 (
    .a(R1), .b(32'ha), .eq(comparator_1_eq));  // open: gt, lt
  Hex_Digit_Display hex_digit_display_2 (.value(LedData[23:20]));  // open: dp
  Hex_Digit_Display hex_digit_display_3 (.value(LedData[27:24]));  // open: dp
  D_Flip_Flop #(.trigger("rising"), .Pre_Clr_Positions("LEGACY"), .NegatePresetClear("false"), .enable("false"), .NewFFLayout("false")) d_ff_1 (
    .clk(IR1_t), .D(1'b1), .Q(d_ff_1_q), .reset(d_ff_4_q));  // open: Qn, preset
  D_Flip_Flop #(.trigger("rising"), .Pre_Clr_Positions("LEGACY"), .NegatePresetClear("false"), .enable("false"), .NewFFLayout("false")) d_ff_2 (
    .clk(IR2_t), .D(1'b1), .Q(d_ff_2_q), .reset(d_ff_5_q));  // open: Qn, preset
  D_Flip_Flop #(.trigger("rising"), .Pre_Clr_Positions("LEGACY"), .NegatePresetClear("false"), .enable("false"), .NewFFLayout("false")) d_ff_3 (
    .clk(IR3_t), .D(1'b1), .Q(d_ff_3_q), .reset(d_ff_6_q));  // open: Qn, preset
  and and_1 (and_1_out, Beq, tunnel_t);
  and and_2 (and_2_out, ~tunnel_t, Bne);  // AND_Gate
  and and_3 (and_3_out, tunnel_t_t, BGE);
  Priority_Encoder #(.select(2), .disabled("Z")) priority_encoder_1 (
    .in0(1'b1), .in1(Branch), .in2(JAL), .in3(JALR), .out(priority_encoder_1_out));  // open: gs, en_out, en_in
  and and_4 (and_4_out, ecall, comparator_1_eq);
  Hex_Digit_Display hex_digit_display_4 (.value(LedData[15:12]));  // open: dp
  Hex_Digit_Display hex_digit_display_5 (.value(LedData[19:16]));  // open: dp
  or or_4 (or_4_out, d_ff_1_q, d_ff_4_q);
  or or_5 (or_5_out, d_ff_2_q, d_ff_5_q);
  or or_6 (or_6_out, d_ff_3_q, d_ff_6_q);
  or or_7 (Branch, and_1_out, and_2_out, and_3_out);
  Multiplexer #(.select(2), .width(32), .disabled("Z"), .enable("false")) multiplexer_1 (
    .in0(PC_4), .in1(B_Addr), .in2(J_Addr), .in3({R, Addr}), .out(\现场 ), .sel(priority_encoder_1_out));
  Priority_Encoder #(.select(2), .disabled("Z")) priority_encoder_2 (
    .in0(1'b1), .in1(URET), .in2(INT), .out(priority_encoder_2_out));  // open: in3, gs, en_out, en_in
  Register #(.width(32), .trigger("rising"), .Select("low")) u_PC (
    .D(MDin), .en(and_5_out), .Q(LedData), .clk(CLK));  // open: clr
  and and_5 (and_5_out, ecall, ~comparator_1_eq);  // AND_Gate
  Hex_Digit_Display hex_digit_display_6 (.value(LedData[7:4]));  // open: dp
  Hex_Digit_Display hex_digit_display_7 (.value(LedData[11:8]));  // open: dp
  // Probe on \总周期数 
  and and_6 (and_6_out, or_4_out, ~Clr1);  // AND_Gate
  and and_7 (and_7_out, or_5_out, ~Clr2);  // AND_Gate
  and and_8 (and_8_out, or_6_out, ~Clr3);  // AND_Gate
  Multiplexer #(.select(2), .width(32), .disabled("Z"), .enable("false")) multiplexer_2 (
    .in0(\现场 ), .in1(RET_PC), .in2(INT_PC), .out(multiplexer_2_out), .sel(priority_encoder_2_out));  // open: in3
  Register #(.width(32), .trigger("rising"), .Select("low")) PC_2 (
    .D(multiplexer_2_out), .en(not_1_out), .Q(PC), .clk(CLK), .clr(RST));
  not not_1 (not_1_out, halt);
  and and_9 (halt, and_4_out, ~Go);  // AND_Gate
  Hex_Digit_Display hex_digit_display_8 (.value(LedData[3:0]));  // open: dp
  D_Flip_Flop #(.trigger("rising"), .Pre_Clr_Positions("LEGACY"), .NegatePresetClear("false"), .enable("false"), .NewFFLayout("false")) d_ff_4 (
    .clk(CLK), .D(and_6_out), .Q(d_ff_4_q), .reset(RST));  // open: Qn, preset
  D_Flip_Flop #(.trigger("rising"), .Pre_Clr_Positions("LEGACY"), .NegatePresetClear("false"), .enable("false"), .NewFFLayout("false")) d_ff_5 (
    .clk(CLK), .D(and_7_out), .Q(d_ff_5_q), .reset(RST));  // open: Qn, preset
  D_Flip_Flop #(.trigger("rising"), .Pre_Clr_Positions("LEGACY"), .NegatePresetClear("false"), .enable("false"), .NewFFLayout("false")) d_ff_6 (
    .clk(CLK), .D(and_8_out), .Q(d_ff_6_q), .reset(RST));  // open: Qn, preset
  not not_2 (not_2_out, halt);
  Priority_Encoder #(.select(2), .disabled("Z")) priority_encoder_3 (
    .in1(d_ff_4_q), .in2(d_ff_5_q), .in3(d_ff_6_q), .out(\中断号 ), .gs(\中断信号 ));  // open: in0, en_out, en_in
  Counter #(.width(2), .max('h3), .ongoal("wrap"), .trigger("falling"), .behavior("old")) counter_1 (
    .load(URET), .Q(\级数 ), .clk(multiplexer_3_out), .clr(RST));  // open: D, count, carry, preset
  Multiplexer #(.select(1), .width(1), .disabled("Z"), .enable("false")) multiplexer_3 (
    .in0(\new ), .in1(d_ff_7_qn), .out(multiplexer_3_out), .sel(URET));
  D_Flip_Flop #(.trigger("falling"), .Pre_Clr_Positions("LEGACY"), .NegatePresetClear("false"), .enable("false"), .NewFFLayout("false")) d_ff_7 (
    .clk(CLK), .D(URET), .Qn(d_ff_7_qn));  // open: Q, preset, reset
  // RiscV_Probe riscv_probe_1: pin names not known; wires that end beside it: IR
  Adder #(.width(32)) adder_1 (.a(PC), .b(32'h4), .out(PC_4));  // open: cin, cout
  Counter #(.width(16), .max('hffff), .ongoal("stay"), .trigger("rising"), .behavior("old")) counter_2 (
    .count(not_2_out), .Q(\总周期数 ), .clk(CLK), .clr(RST));  // open: load, D, carry, preset
  or or_8 (IR1_t, IR1, IRA);
  Multiplexer #(.select(2), .width(32), .disabled("Z"), .enable("false")) multiplexer_4 (
    .in1(32'h30ac), .in2(32'h3158), .in3(32'h3204), .out(INT_PC), .sel(\中断号 ));  // open: in0
  Decoder #(.select(2), .tristate("false"), .disabled("Z"), .enable("false")) decoder_1 (
    .out1(decoder_1_out1), .out2(decoder_1_out2), .sel(\级数 ));  // open: out0, out3
  ROM #(.addrWidth(10), .dataWidth(32), .Select("high")) rom_1 (.addr(PC[11:2]), .data(IR));
  or or_9 (IR2_t, IR2, IRB);
  Comparator #(.width(2), .mode("unsigned")) comparator_2 (.a(\中断号 ), .b(now), .gt(\new ));  // open: eq, lt
  Register #(.width(2), .trigger("falling"), .Select("low")) register_1 (
    .D(now), .en(decoder_1_out1), .Q(register_1_q), .clk(CLK), .clr(RST));
  Register #(.width(2), .trigger("falling"), .Select("low")) register_2 (
    .D(now), .en(decoder_1_out2), .Q(register_2_q), .clk(CLK), .clr(RST));
  Multiplexer #(.select(1), .width(2), .disabled("Z"), .enable("false")) multiplexer_5 (
    .in0(now), .in1(\中断号 ), .out(multiplexer_5_out), .sel(\new ));
  Subtractor #(.width(2)) subtractor_1 (.a(\级数 ), .b(2'b01), .out(subtractor_1_out));  // open: bin, bout
  \单周期硬布线控制器  \u_单周期硬布线控制器_1  (
    .Funct({IR[30], IR[25], IR[14:12]}), .OP(IR[6:2]), .ALU_OP(\单周期硬布线控制器_1_alu_op ), .MemToReg(MemToReg),
    .MemWrite(MemWrite), .ALU_SRC(\单周期硬布线控制器_1_alu_src ), .RegWrite(RegWrite), .ecall(ecall),
    .S_type(\单周期硬布线控制器_1_s_type ), .Jalr(JALR), .Beq(Beq), .JAL(JAL), .Bne(Bne), .in_3(IR[21]), .uret(URET),
    .LB(LB), .BGE(BGE), .CSRRSI(CSRRSI), .CSRRCI(CSRRCI));
  Multiplexer #(.select(1), .width(5), .disabled("Z"), .enable("false")) multiplexer_6 (
    .in0(IR[19:15]), .in1(5'b10001), .out(multiplexer_6_out), .sel(ecall));
  Multiplexer #(.select(1), .width(5), .disabled("Z"), .enable("false")) multiplexer_7 (
    .in0(IR[24:20]), .in1(5'b01010), .out(multiplexer_7_out), .sel(ecall));
  assign bit_extender_1_out = {{20{IR[31]}}, IR[31:20]};  // Bit_Extender bit_extender_1
  assign bit_extender_2_out = {{20{IR[31]}}, {IR[31:25], IR[11:7]}};  // Bit_Extender bit_extender_2
  or or_10 (IR3_t, IR3, IRC);
  Multiplexer #(.select(1), .width(2), .disabled("Z"), .enable("false")) multiplexer_8 (
    .in0(multiplexer_5_out), .in1(last), .out(multiplexer_8_out), .sel(URET));
  or or_11 (or_11_out, URET, INT);
  Multiplexer #(.select(2), .width(2), .disabled("Z"), .enable("false")) multiplexer_9 (
    .in0(2'b00), .in1(register_1_q), .in2(register_2_q), .out(last), .sel(subtractor_1_out));  // open: in3
  Multiplexer #(.select(1), .width(32), .disabled("Z"), .enable("false")) multiplexer_10 (
    .in0(bit_extender_1_out), .in1(bit_extender_2_out), .out(multiplexer_10_out), .sel(\单周期硬布线控制器_1_s_type ));
  assign bit_extender_3_out = {{20{IR[31]}}, {IR[31], IR[7], IR[30:25], IR[11:8]}};  // Bit_Extender bit_extender_3
  assign bit_extender_4_out = {{12{IR[31]}}, {IR[31], IR[19:12], IR[20], IR[30:21]}};  // Bit_Extender bit_extender_4
  Button \u_总复位  (.out(RST));
  Register #(.width(2), .trigger("falling"), .Select("low")) register_3 (
    .D(multiplexer_8_out), .en(or_11_out), .Q(register_3_q), .clk(CLK), .clr(RST));
  Register #(.width(2), .trigger("rising"), .Select("low")) register_4 (
    .D(register_3_q), .Q(now), .clk(CLK), .clr(RST));  // open: en
  Regifile regifile_1 (
    .Din(RDin), .Clk(CLK), .R1(R1), .R2(MDin), .WE(RegWrite), .W_num(IR[11:7]), .R1_num(multiplexer_6_out),
    .R2_num(multiplexer_7_out));
  Shifter #(.width(32), .shift("ll")) shifter_1 (.in(bit_extender_3_out), .\dist (5'b00001), .out(shifter_1_out));
  Shifter #(.width(32), .shift("ll")) shifter_2 (.in(bit_extender_4_out), .\dist (5'b00001), .out(shifter_2_out));
  Decoder #(.select(2), .tristate("false"), .disabled("Z"), .enable("false")) decoder_2 (
    .out1(_1), .out2(_2), .out3(_3), .sel(now));  // open: out0
  Register #(.width(32), .trigger("falling"), .Select("low")) mEPC (
    .D(\现场 ), .en(_1), .Q(mEPC_q), .clk(INT), .clr(RST));
  Register #(.width(32), .trigger("falling"), .Select("low")) mEPC1 (
    .D(\现场 ), .en(_2), .Q(mEPC1_q), .clk(INT), .clr(RST));
  Register #(.width(32), .trigger("falling"), .Select("low")) mEPC2 (
    .D(\现场 ), .en(_3), .Q(mEPC2_q), .clk(INT), .clr(RST));
  Adder #(.width(32)) adder_2 (.a(shifter_1_out), .b(PC), .out(B_Addr));  // open: cin, cout
  Adder #(.width(32)) adder_3 (.a(shifter_2_out), .b(PC), .out(J_Addr));  // open: cin, cout
  Multiplexer #(.select(2), .width(32), .disabled("Z"), .enable("false")) multiplexer_11 (
    .in1(mEPC_q), .in2(mEPC1_q), .in3(mEPC2_q), .out(RET_PC), .sel(now));  // open: in0
  Multiplexer #(.select(1), .width(32), .disabled("Z"), .enable("false")) multiplexer_12 (
    .in0(MDin), .in1(multiplexer_10_out), .out(multiplexer_12_out), .sel(\单周期硬布线控制器_1_alu_src ));
  and and_10 (Clr1, _1, URET);
  and and_11 (Clr2, _2, URET);
  and and_12 (Clr3, _3, URET);
  ALU alu_1 (
    .X(R1), .Y(multiplexer_12_out), .AluOP(\单周期硬布线控制器_1_alu_op ), .Equal(tunnel_t), .Result({R, Addr}),
    .out_4(tunnel_t_t), .out_6(tunnel));  // open: Result_2
  RAM #(.addrWidth(10), .dataWidth(32), .bus("separate"), .Select("high")) ram_1 (
    .addr(R[11:2]), .din(MDin), .data(ram_1_data), .str(MemWrite), .sel(1'b1), .clk(CLK), .ld(1'b1), .clr(RST));
  Priority_Encoder #(.select(2), .disabled("Z")) priority_encoder_4 (
    .in0(1'b1), .in1(MemToReg), .in2(or_12_out), .out(priority_encoder_4_out));  // open: in3, gs, en_out, en_in
  or or_12 (or_12_out, JAL, JALR);
  Register #(.width(1), .trigger("rising"), .Select("low")) register_5 (
    .D(CSRRSI), .Q(register_5_q), .clk(CLK));  // open: en, clr
  Register #(.width(1), .trigger("rising"), .Select("low")) register_6 (
    .D(CSRRCI), .Q(register_6_q), .clk(CLK));  // open: en, clr
  Multiplexer #(.select(2), .width(32), .disabled("Z"), .enable("false")) multiplexer_13 (
    .in0({R, Addr}), .in1(ram_1_data), .in2(PC_4), .out(word), .sel(priority_encoder_4_out));  // open: in3
  assign bit_extender_5_out = {{24{word[7]}}, word[7:0]};  // Bit_Extender bit_extender_5
  assign bit_extender_6_out = {{24{word[15]}}, word[15:8]};  // Bit_Extender bit_extender_6
  assign bit_extender_7_out = {{24{word[23]}}, word[23:16]};  // Bit_Extender bit_extender_7
  assign bit_extender_8_out = {{24{word[31]}}, word[31:24]};  // Bit_Extender bit_extender_8
  and and_13 (and_13_out, register_5_q, _1);
  and and_14 (and_14_out, _1, register_6_q);
  and and_15 (and_15_out, register_5_q, _2);
  and and_16 (and_16_out, _2, register_6_q);
  and and_17 (and_17_out, register_5_q, _3);
  and and_18 (and_18_out, _3, register_6_q);
  Multiplexer #(.select(1), .width(32), .disabled("Z"), .enable("false")) multiplexer_14 (
    .in0(word), .in1(\byte ), .out(RDin), .sel(LB));
  Multiplexer #(.select(2), .width(32), .disabled("Z"), .enable("false")) multiplexer_15 (
    .in0(bit_extender_5_out), .in1(bit_extender_6_out), .in2(bit_extender_7_out), .in3(bit_extender_8_out),
    .out(\byte ), .sel(Addr));
  not not_3 (not_3_out, URET);
  Register #(.width(1), .trigger("rising"), .Select("low")) register_7 (
    .D(INT), .Q(register_7_q), .clk(CLK), .clr(RST));  // open: en
  or or_13 (or_13_out, RST, and_14_out);
  or or_14 (or_14_out, RST, and_16_out);
  or or_15 (or_15_out, RST, and_18_out);
  D_Flip_Flop #(.trigger("rising"), .Pre_Clr_Positions("LEGACY"), .NegatePresetClear("false"), .enable("false"), .NewFFLayout("false")) d_ff_8 (
    .clk(not_3_out), .D(1'b0), .Qn(IE0), .preset(register_7_q), .reset(RST));  // open: Q
  D_Flip_Flop #(.trigger("rising"), .Pre_Clr_Positions("LEGACY"), .NegatePresetClear("false"), .enable("false"), .NewFFLayout("false")) d_ff_9 (
    .Q(IE1), .preset(and_13_out), .reset(or_13_out));  // open: clk, D, Qn
  D_Flip_Flop #(.trigger("rising"), .Pre_Clr_Positions("LEGACY"), .NegatePresetClear("false"), .enable("false"), .NewFFLayout("false")) d_ff_10 (
    .Q(IE2), .preset(and_15_out), .reset(or_14_out));  // open: clk, D, Qn
  D_Flip_Flop #(.trigger("rising"), .Pre_Clr_Positions("LEGACY"), .NegatePresetClear("false"), .enable("false"), .NewFFLayout("false")) d_ff_11 (
    .Q(IE3), .preset(and_17_out), .reset(or_15_out));  // open: clk, D, Qn
  Multiplexer #(.select(2), .width(1), .disabled("Z"), .enable("false")) multiplexer_16 (
    .in0(IE0), .in1(IE1), .in2(IE2), .in3(IE3), .out(multiplexer_16_out), .sel(now));
  Comparator #(.width(2), .mode("unsigned")) comparator_3 (.a(\中断号 ), .b(now), .eq(comparator_3_eq));  // open: gt, lt
  and and_19 (INT, IE, \中断信号 );
  and and_20 (IE, multiplexer_16_out, ~comparator_3_eq);  // AND_Gate

  // Other names for the same wires on the sheet: R[1:0] = Addr

  // Notes on the sheet:
  //   中断源
  //   中断等待指示
  //   总复位信号应将除ROM以外所有存储组件全部清零
  //   数码管输出
  //   数码管输出应该用寄存器锁存，否则显示数据只能一闪而过
  //   入口
  //   指令探针
  //   指令存储器
  //   指令字
  //   contents of rom_1 (hex, n*v repeats v):
  //   7d000113 100413 1f41993 41f9d993 433 c00913 800b13 140413 f47413 800293 100313 499993 89e9b3 1300533
  //   2200893 73 406282b3 fe0294e3 140413 f00f93 1f47433 1c41413 800293 100313 49d993 89e9b3 1300533
  //   2200893 73 406282b3 fe0294e3 1c45413 406b0b33 b0463 f95ff06f 2b3 fff2c293 1029293 fff2e293 500533
  //   2200893 73 f5dff06f 1112023 410113 a12023 410113 812023 410113 1312023 410113 1412023 410113 1512023
  //   410113 1612023 410113 40e073 100b13 300a13 100a93 1600433 441413 14469b3 1300533 2200893 73 fe0416e3
  //   415a0a33 fe0a10e3 40f073 ffc10113 12b03 ffc10113 12a83 ffc10113 12a03 ffc10113 12983 ffc10113 12403
  //   ffc10113 12503 ffc10113 12883 200073 1112023 410113 a12023 410113 812023 410113 1312023 410113
  //   1412023 410113 1512023 410113 1612023 410113 40e073 200b13 300a13 100a93 1600433 441413 14469b3
  //   1300533 2200893 73 fe0416e3 415a0a33 fe0a10e3 40f073 ffc10113 12b03 ffc10113 12a83 ffc10113 12a03
  //   ffc10113 12983 ffc10113 12403 ffc10113 12503 ffc10113 12883 200073 1112023 410113 a12023 410113
  //   812023 410113 1312023 410113 1412023 410113 1512023 410113 1612023 410113 40e073 300b13 300a13
  //   100a93 1600433 441413 14469b3 1300533 2200893 73 fe0416e3 415a0a33 fe0a10e3 40f073 ffc10113 12b03
  //   ffc10113 12a83 ffc10113 12a03 ffc10113 12983 ffc10113 12403 ffc10113 12503 ffc10113 12883 200073
  //   保存上一级中断号
  //   JAL
  //   JALR
  //   URET
  //   Beq
  //   Bne
  //   MemToReg
  //   MemWrite
  //   AluOP
  //   AluSrcB
  //   RegWrite
  //   S_Type
  //   保存现场
  //   为方便自动评测，需要输出PC，IR，寄存器堆写如数据RDin
  //   RAM写使能MemWrite、RAM写入数据MDin等信号
  //   中断请求
  //   数据存储器
endmodule

module \封装正确性测试  (
);

  wire IR1, IR2, IR3, MemW, RegW;
  wire [31:0] EX_PC, ID_PC, IF_PC, IR, LED, MDin, MDinr, MEM_PC, PC, RDin, RDinr, WB_PC;

  \单周期RISC_V  \u_单周期risc_v_1  (
    .IR1(IR1), .IR2(IR2), .IR3(IR3), .RegWrite(RegW), .MemWrite(MemW), .PC(PC), .IR(IR), .RDin(RDin),
    .MDin(MDin), .LedData(LED));
  \气泡流水线  \u_气泡流水线_1  (
    .RegWrite(RegW), .MemWrite(MemW), .IF_PC(IF_PC), .ID_PC(ID_PC), .EX_PC(EX_PC), .M_PC(MEM_PC),
    .WB_PC(WB_PC), .RDin(RDinr), .MDin(MDinr), .LedData(LED));
  \单周期_单级中断  \u_单周期_单级中断_1  (
    .IR1(IR1), .IR2(IR2), .IR3(IR3), .RegWrite(RegW), .MemWrite(MemW), .PC(PC), .IR(IR), .RDin(RDin),
    .MDin(MDin), .LedData(LED));
  \理想流水线  \u_理想流水线_1  (
    .RegWrite(RegW), .MemWrite(MemW), .IF_PC(IF_PC), .ID_PC(ID_PC), .EX_PC(EX_PC), .M_PC(MEM_PC),
    .WB_PC(WB_PC), .RDin(RDinr), .MDin(MDinr), .LedData(LED));
  \重定向流水线  \u_重定向流水线_1  (
    .RegWrite(RegW), .MemWrite(MemW), .IF_PC(IF_PC), .ID_PC(ID_PC), .EX_PC(EX_PC), .M_PC(MEM_PC),
    .WB_PC(WB_PC), .RDin(RDinr), .MDin(MDinr), .LedData(LED));
  \单周期_多级中断  \u_单周期_多级中断_1  (
    .IR1(IR1), .IR2(IR2), .IR3(IR3), .RegWrite(RegW), .MemWrite(MemW), .PC(PC), .IR(IR), .RDin(RDin),
    .MDin(MDin), .LedData(LED));

  // Notes on the sheet:
  //   单周期封装测试
  //   气泡流水封装测试
  //   单周期+单级中断封装测试
  //   请检查上面封装有无位宽不匹配，引脚标签是否和连接的标签相对应，否则无法在educoder平台上正确测试
  //   理想流水封装测试
  //   重定向流水封装测试
  //   单周期+多级中断封装测试
endmodule

module IF__ID (
  input  PredictJump,
  input  [31:0] IR,
  input  [31:0] PC,
  input  [31:0] PC_4,
  input  RST,
  input  en,
  input  CLK,
  input  BranchTaken,
  output PredictJump_2,
  output [31:0] IR_2,
  output [31:0] PC_2,
  output [31:0] PC_4_2
);

  wire multiplexer_1_out, or_1_out;
  wire [31:0] multiplexer_2_out, multiplexer_3_out, multiplexer_4_out;

  Multiplexer #(.select(1), .width(1), .disabled("Z"), .enable("false")) multiplexer_1 (
    .in0(PredictJump), .in1(1'b0), .out(multiplexer_1_out), .sel(or_1_out));
  Multiplexer #(.select(1), .width(32), .disabled("Z"), .enable("false")) multiplexer_2 (
    .in0(IR), .in1({32{1'b0}}), .out(multiplexer_2_out), .sel(or_1_out));
  Multiplexer #(.select(1), .width(32), .disabled("Z"), .enable("false")) multiplexer_3 (
    .in0(PC), .in1({32{1'b0}}), .out(multiplexer_3_out), .sel(or_1_out));
  Multiplexer #(.select(1), .width(32), .disabled("Z"), .enable("false")) multiplexer_4 (
    .in0(PC_4), .in1({32{1'b0}}), .out(multiplexer_4_out), .sel(or_1_out));
  or or_1 (or_1_out, RST, BranchTaken);
  Register #(.width(1), .trigger("rising"), .Select("low")) register_1 (
    .D(multiplexer_1_out), .en(en), .Q(PredictJump_2), .clk(CLK));  // open: clr
  Register #(.width(32), .trigger("rising"), .Select("low")) register_2 (
    .D(multiplexer_2_out), .en(en), .Q(IR_2), .clk(CLK));  // open: clr
  Register #(.width(32), .trigger("rising"), .Select("low")) register_3 (
    .D(multiplexer_3_out), .en(en), .Q(PC_2), .clk(CLK));  // open: clr
  Register #(.width(32), .trigger("rising"), .Select("low")) register_4 (
    .D(multiplexer_4_out), .en(en), .Q(PC_4_2), .clk(CLK));  // open: clr
endmodule

module ID__EX (
  input  BGE,
  input  BGE_2,
  input  LB,
  input  JALR,
  input  JAL,
  input  Beq,
  input  Bne,
  input  MemToReg,
  input  MemWrite,
  input  AluSrcB,
  input  RegWrite,
  input  ecall,
  input  [3:0] AluOP,
  input  [4:0] rd,
  input  [31:0] R1,
  input  [31:0] R2,
  input  [31:0] imm,
  input  [31:0] imm_b,
  input  [31:0] imm_j,
  input  [31:0] IR,
  input  [31:0] PC,
  input  [31:0] PC_4,
  input  [1:0] rs1Forward,
  input  [1:0] rs2Forward,
  input  en,
  input  CLK,
  input  RST,
  input  RST_2,
  input  flush,
  output BGE_3,
  output BGE_4,
  output LB_2,
  output JALR_2,
  output JAL_2,
  output Beq_2,
  output Bne_2,
  output MemToReg_2,
  output MemWrite_2,
  output AluSrcB_2,
  output RegWrite_2,
  output ecall_2,
  output [3:0] AluOP_2,
  output [4:0] rd_2,
  output [31:0] R1_2,
  output [31:0] R2_2,
  output [31:0] imm_2,
  output [31:0] imm_b_2,
  output [31:0] imm_j_2,
  output [31:0] IR_2,
  output [31:0] PC_2,
  output [31:0] PC_4_2,
  output [1:0] rs1Forward_2,
  output [1:0] rs2Forward_2
);

  wire multiplexer_1_out, multiplexer_2_out, multiplexer_3_out, multiplexer_4_out, multiplexer_5_out,
       multiplexer_6_out, multiplexer_7_out, multiplexer_8_out, multiplexer_9_out, multiplexer_10_out,
       multiplexer_11_out, multiplexer_12_out, or_1_out;
  wire [1:0] multiplexer_23_out, multiplexer_24_out;
  wire [3:0] multiplexer_13_out;
  wire [4:0] multiplexer_14_out;
  wire [31:0] multiplexer_15_out, multiplexer_16_out, multiplexer_17_out, multiplexer_18_out,
       multiplexer_19_out, multiplexer_20_out, multiplexer_21_out, multiplexer_22_out;

  Multiplexer #(.select(1), .width(1), .disabled("Z"), .enable("false")) multiplexer_1 (
    .in0(BGE), .in1(1'b0), .out(multiplexer_1_out), .sel(or_1_out));
  Multiplexer #(.select(1), .width(1), .disabled("Z"), .enable("false")) multiplexer_2 (
    .in0(BGE_2), .in1(1'b0), .out(multiplexer_2_out), .sel(or_1_out));
  Multiplexer #(.select(1), .width(1), .disabled("Z"), .enable("false")) multiplexer_3 (
    .in0(LB), .in1(1'b0), .out(multiplexer_3_out), .sel(or_1_out));
  Multiplexer #(.select(1), .width(1), .disabled("Z"), .enable("false")) multiplexer_4 (
    .in0(JALR), .in1(1'b0), .out(multiplexer_4_out), .sel(or_1_out));
  Multiplexer #(.select(1), .width(1), .disabled("Z"), .enable("false")) multiplexer_5 (
    .in0(JAL), .in1(1'b0), .out(multiplexer_5_out), .sel(or_1_out));
  Multiplexer #(.select(1), .width(1), .disabled("Z"), .enable("false")) multiplexer_6 (
    .in0(Beq), .in1(1'b0), .out(multiplexer_6_out), .sel(or_1_out));
  Multiplexer #(.select(1), .width(1), .disabled("Z"), .enable("false")) multiplexer_7 (
    .in0(Bne), .in1(1'b0), .out(multiplexer_7_out), .sel(or_1_out));
  Multiplexer #(.select(1), .width(1), .disabled("Z"), .enable("false")) multiplexer_8 (
    .in0(MemToReg), .in1(1'b0), .out(multiplexer_8_out), .sel(or_1_out));
  Multiplexer #(.select(1), .width(1), .disabled("Z"), .enable("false")) multiplexer_9 (
    .in0(MemWrite), .in1(1'b0), .out(multiplexer_9_out), .sel(or_1_out));
  Multiplexer #(.select(1), .width(1), .disabled("Z"), .enable("false")) multiplexer_10 (
    .in0(AluSrcB), .in1(1'b0), .out(multiplexer_10_out), .sel(or_1_out));
  Multiplexer #(.select(1), .width(1), .disabled("Z"), .enable("false")) multiplexer_11 (
    .in0(RegWrite), .in1(1'b0), .out(multiplexer_11_out), .sel(or_1_out));
  Multiplexer #(.select(1), .width(1), .disabled("Z"), .enable("false")) multiplexer_12 (
    .in0(ecall), .in1(1'b0), .out(multiplexer_12_out), .sel(or_1_out));
  Multiplexer #(.select(1), .width(4), .disabled("Z"), .enable("false")) multiplexer_13 (
    .in0(AluOP), .in1(4'b0000), .out(multiplexer_13_out), .sel(or_1_out));
  Multiplexer #(.select(1), .width(5), .disabled("Z"), .enable("false")) multiplexer_14 (
    .in0(rd), .in1({5{1'b0}}), .out(multiplexer_14_out), .sel(or_1_out));
  Multiplexer #(.select(1), .width(32), .disabled("Z"), .enable("false")) multiplexer_15 (
    .in0(R1), .in1({32{1'b0}}), .out(multiplexer_15_out), .sel(or_1_out));
  Multiplexer #(.select(1), .width(32), .disabled("Z"), .enable("false")) multiplexer_16 (
    .in0(R2), .in1({32{1'b0}}), .out(multiplexer_16_out), .sel(or_1_out));
  Multiplexer #(.select(1), .width(32), .disabled("Z"), .enable("false")) multiplexer_17 (
    .in0(imm), .in1({32{1'b0}}), .out(multiplexer_17_out), .sel(or_1_out));
  Multiplexer #(.select(1), .width(32), .disabled("Z"), .enable("false")) multiplexer_18 (
    .in0(imm_b), .in1({32{1'b0}}), .out(multiplexer_18_out), .sel(or_1_out));
  Multiplexer #(.select(1), .width(32), .disabled("Z"), .enable("false")) multiplexer_19 (
    .in0(imm_j), .in1({32{1'b0}}), .out(multiplexer_19_out), .sel(or_1_out));
  Multiplexer #(.select(1), .width(32), .disabled("Z"), .enable("false")) multiplexer_20 (
    .in0(IR), .in1({32{1'b0}}), .out(multiplexer_20_out), .sel(or_1_out));
  Multiplexer #(.select(1), .width(32), .disabled("Z"), .enable("false")) multiplexer_21 (
    .in0(PC), .in1({32{1'b0}}), .out(multiplexer_21_out), .sel(or_1_out));
  Multiplexer #(.select(1), .width(32), .disabled("Z"), .enable("false")) multiplexer_22 (
    .in0(PC_4), .in1({32{1'b0}}), .out(multiplexer_22_out), .sel(or_1_out));
  Multiplexer #(.select(1), .width(2), .disabled("Z"), .enable("false")) multiplexer_23 (
    .in0(rs1Forward), .in1(2'b00), .out(multiplexer_23_out), .sel(or_1_out));
  Multiplexer #(.select(1), .width(2), .disabled("Z"), .enable("false")) multiplexer_24 (
    .in0(rs2Forward), .in1(2'b00), .out(multiplexer_24_out), .sel(or_1_out));
  or or_1 (or_1_out, RST_2, flush);
  Register #(.width(1), .trigger("rising"), .Select("low")) register_1 (
    .D(multiplexer_1_out), .en(en), .Q(BGE_3), .clk(CLK), .clr(RST));
  Register #(.width(1), .trigger("rising"), .Select("low")) register_2 (
    .D(multiplexer_2_out), .en(en), .Q(BGE_4), .clk(CLK), .clr(RST));
  Register #(.width(1), .trigger("rising"), .Select("low")) register_3 (
    .D(multiplexer_3_out), .en(en), .Q(LB_2), .clk(CLK), .clr(RST));
  Register #(.width(1), .trigger("rising"), .Select("low")) register_4 (
    .D(multiplexer_4_out), .en(en), .Q(JALR_2), .clk(CLK), .clr(RST));
  Register #(.width(1), .trigger("rising"), .Select("low")) register_5 (
    .D(multiplexer_5_out), .en(en), .Q(JAL_2), .clk(CLK), .clr(RST));
  Register #(.width(1), .trigger("rising"), .Select("low")) register_6 (
    .D(multiplexer_6_out), .en(en), .Q(Beq_2), .clk(CLK), .clr(RST));
  Register #(.width(1), .trigger("rising"), .Select("low")) register_7 (
    .D(multiplexer_7_out), .en(en), .Q(Bne_2), .clk(CLK), .clr(RST));
  Register #(.width(1), .trigger("rising"), .Select("low")) register_8 (
    .D(multiplexer_8_out), .en(en), .Q(MemToReg_2), .clk(CLK), .clr(RST));
  Register #(.width(1), .trigger("rising"), .Select("low")) register_9 (
    .D(multiplexer_9_out), .en(en), .Q(MemWrite_2), .clk(CLK), .clr(RST));
  Register #(.width(1), .trigger("rising"), .Select("low")) register_10 (
    .D(multiplexer_10_out), .en(en), .Q(AluSrcB_2), .clk(CLK), .clr(RST));
  Register #(.width(1), .trigger("rising"), .Select("low")) register_11 (
    .D(multiplexer_11_out), .en(en), .Q(RegWrite_2), .clk(CLK), .clr(RST));
  Register #(.width(1), .trigger("rising"), .Select("low")) register_12 (
    .D(multiplexer_12_out), .en(en), .Q(ecall_2), .clk(CLK), .clr(RST));
  Register #(.width(4), .trigger("rising"), .Select("low")) register_13 (
    .D(multiplexer_13_out), .en(en), .Q(AluOP_2), .clk(CLK), .clr(RST));
  Register #(.width(5), .trigger("rising"), .Select("low")) register_14 (
    .D(multiplexer_14_out), .en(en), .Q(rd_2), .clk(CLK), .clr(RST));
  Register #(.width(32), .trigger("rising"), .Select("low")) register_15 (
    .D(multiplexer_15_out), .en(en), .Q(R1_2), .clk(CLK), .clr(RST));
  Register #(.width(32), .trigger("rising"), .Select("low")) register_16 (
    .D(multiplexer_16_out), .en(en), .Q(R2_2), .clk(CLK), .clr(RST));
  Register #(.width(32), .trigger("rising"), .Select("low")) register_17 (
    .D(multiplexer_17_out), .en(en), .Q(imm_2), .clk(CLK), .clr(RST));
  Register #(.width(32), .trigger("rising"), .Select("low")) register_18 (
    .D(multiplexer_18_out), .en(en), .Q(imm_b_2), .clk(CLK), .clr(RST));
  Register #(.width(32), .trigger("rising"), .Select("low")) register_19 (
    .D(multiplexer_19_out), .en(en), .Q(imm_j_2), .clk(CLK), .clr(RST));
  Register #(.width(32), .trigger("rising"), .Select("low")) register_20 (
    .D(multiplexer_20_out), .en(en), .Q(IR_2), .clk(CLK), .clr(RST));
  Register #(.width(32), .trigger("rising"), .Select("low")) register_21 (
    .D(multiplexer_21_out), .en(en), .Q(PC_2), .clk(CLK), .clr(RST));
  Register #(.width(32), .trigger("rising"), .Select("low")) register_22 (
    .D(multiplexer_22_out), .en(en), .Q(PC_4_2), .clk(CLK), .clr(RST));
  Register #(.width(2), .trigger("rising"), .Select("low")) register_23 (
    .D(multiplexer_23_out), .en(en), .Q(rs1Forward_2), .clk(CLK), .clr(RST));
  Register #(.width(2), .trigger("rising"), .Select("low")) register_24 (
    .D(multiplexer_24_out), .en(en), .Q(rs2Forward_2), .clk(CLK), .clr(RST));
endmodule

module EX__MEM (
  input  LB,
  input  JALR,
  input  JAL,
  input  MemToReg,
  input  MemWrite,
  input  RegWrite,
  input  ecall,
  input  [4:0] rd,
  input  [31:0] R1,
  input  [31:0] R,
  input  [31:0] MD,
  input  [31:0] IR,
  input  [31:0] PC,
  input  [31:0] PC_4,
  input  RST,
  input  en,
  input  CLK,
  output LB_2,
  output JALR_2,
  output JAL_2,
  output MemToReg_2,
  output MemWrite_2,
  output RegWrite_2,
  output RegWrite_3,
  output [4:0] rd_2,
  output [31:0] R1_2,
  output [31:0] R_2,
  output [31:0] MD_2,
  output [31:0] IR_2,
  output [31:0] PC_2,
  output [31:0] PC_4_2
);

  wire multiplexer_1_out, multiplexer_2_out, multiplexer_3_out, multiplexer_4_out, multiplexer_5_out,
       multiplexer_6_out, multiplexer_7_out;
  wire [4:0] multiplexer_8_out;
  wire [31:0] multiplexer_9_out, multiplexer_10_out, multiplexer_11_out, multiplexer_12_out,
       multiplexer_13_out, multiplexer_14_out;

  Multiplexer #(.select(1), .width(1), .disabled("Z"), .enable("false")) multiplexer_1 (
    .in0(LB), .in1(1'b0), .out(multiplexer_1_out), .sel(RST));
  Multiplexer #(.select(1), .width(1), .disabled("Z"), .enable("false")) multiplexer_2 (
    .in0(JALR), .in1(1'b0), .out(multiplexer_2_out), .sel(RST));
  Multiplexer #(.select(1), .width(1), .disabled("Z"), .enable("false")) multiplexer_3 (
    .in0(JAL), .in1(1'b0), .out(multiplexer_3_out), .sel(RST));
  Multiplexer #(.select(1), .width(1), .disabled("Z"), .enable("false")) multiplexer_4 (
    .in0(MemToReg), .in1(1'b0), .out(multiplexer_4_out), .sel(RST));
  Multiplexer #(.select(1), .width(1), .disabled("Z"), .enable("false")) multiplexer_5 (
    .in0(MemWrite), .in1(1'b0), .out(multiplexer_5_out), .sel(RST));
  Multiplexer #(.select(1), .width(1), .disabled("Z"), .enable("false")) multiplexer_6 (
    .in0(RegWrite), .in1(1'b0), .out(multiplexer_6_out), .sel(RST));
  Multiplexer #(.select(1), .width(1), .disabled("Z"), .enable("false")) multiplexer_7 (
    .in0(ecall), .in1(1'b0), .out(multiplexer_7_out), .sel(RST));
  Multiplexer #(.select(1), .width(5), .disabled("Z"), .enable("false")) multiplexer_8 (
    .in0(rd), .in1({5{1'b0}}), .out(multiplexer_8_out), .sel(RST));
  Multiplexer #(.select(1), .width(32), .disabled("Z"), .enable("false")) multiplexer_9 (
    .in0(R1), .in1({32{1'b0}}), .out(multiplexer_9_out), .sel(RST));
  Multiplexer #(.select(1), .width(32), .disabled("Z"), .enable("false")) multiplexer_10 (
    .in0(R), .in1({32{1'b0}}), .out(multiplexer_10_out), .sel(RST));
  Multiplexer #(.select(1), .width(32), .disabled("Z"), .enable("false")) multiplexer_11 (
    .in0(MD), .in1({32{1'b0}}), .out(multiplexer_11_out), .sel(RST));
  Multiplexer #(.select(1), .width(32), .disabled("Z"), .enable("false")) multiplexer_12 (
    .in0(IR), .in1({32{1'b0}}), .out(multiplexer_12_out), .sel(RST));
  Multiplexer #(.select(1), .width(32), .disabled("Z"), .enable("false")) multiplexer_13 (
    .in0(PC), .in1({32{1'b0}}), .out(multiplexer_13_out), .sel(RST));
  Multiplexer #(.select(1), .width(32), .disabled("Z"), .enable("false")) multiplexer_14 (
    .in0(PC_4), .in1({32{1'b0}}), .out(multiplexer_14_out), .sel(RST));
  Register #(.width(1), .trigger("rising"), .Select("low")) register_1 (
    .D(multiplexer_1_out), .en(en), .Q(LB_2), .clk(CLK));  // open: clr
  Register #(.width(1), .trigger("rising"), .Select("low")) register_2 (
    .D(multiplexer_2_out), .en(en), .Q(JALR_2), .clk(CLK));  // open: clr
  Register #(.width(1), .trigger("rising"), .Select("low")) register_3 (
    .D(multiplexer_3_out), .en(en), .Q(JAL_2), .clk(CLK));  // open: clr
  Register #(.width(1), .trigger("rising"), .Select("low")) register_4 (
    .D(multiplexer_4_out), .en(en), .Q(MemToReg_2), .clk(CLK));  // open: clr
  Register #(.width(1), .trigger("rising"), .Select("low")) register_5 (
    .D(multiplexer_5_out), .en(en), .Q(MemWrite_2), .clk(CLK));  // open: clr
  Register #(.width(1), .trigger("rising"), .Select("low")) register_6 (
    .D(multiplexer_6_out), .en(en), .Q(RegWrite_2), .clk(CLK));  // open: clr
  Register #(.width(1), .trigger("rising"), .Select("low")) register_7 (
    .D(multiplexer_7_out), .en(en), .Q(RegWrite_3), .clk(CLK));  // open: clr
  Register #(.width(5), .trigger("rising"), .Select("low")) register_8 (
    .D(multiplexer_8_out), .en(en), .Q(rd_2), .clk(CLK));  // open: clr
  Register #(.width(32), .trigger("rising"), .Select("low")) register_9 (
    .D(multiplexer_9_out), .en(en), .Q(R1_2), .clk(CLK));  // open: clr
  Register #(.width(32), .trigger("rising"), .Select("low")) register_10 (
    .D(multiplexer_10_out), .en(en), .Q(R_2), .clk(CLK));  // open: clr
  Register #(.width(32), .trigger("rising"), .Select("low")) register_11 (
    .D(multiplexer_11_out), .en(en), .Q(MD_2), .clk(CLK));  // open: clr
  Register #(.width(32), .trigger("rising"), .Select("low")) register_12 (
    .D(multiplexer_12_out), .en(en), .Q(IR_2), .clk(CLK));  // open: clr
  Register #(.width(32), .trigger("rising"), .Select("low")) register_13 (
    .D(multiplexer_13_out), .en(en), .Q(PC_2), .clk(CLK));  // open: clr
  Register #(.width(32), .trigger("rising"), .Select("low")) register_14 (
    .D(multiplexer_14_out), .en(en), .Q(PC_4_2), .clk(CLK));  // open: clr
endmodule

module MEM__WB (
  input  LB,
  input  JALR,
  input  JAL,
  input  MenToReg,
  input  RegWrite,
  input  ecall,
  input  [4:0] rd,
  input  [1:0] addr,
  input  [31:0] R1,
  input  [31:0] R2,
  input  [31:0] R,
  input  [31:0] Dataout,
  input  [31:0] IR,
  input  [31:0] PC,
  input  [31:0] PC_4,
  input  RST,
  input  en,
  input  CLK,
  output LB_2,
  output JALR_2,
  output JAL_2,
  output MemToReg,
  output RegWrite_2,
  output ecall_2,
  output [4:0] rd_2,
  output [1:0] Addr_2,
  output [31:0] R1_2,
  output [31:0] R2_2,
  output [31:0] R_2,
  output [31:0] Dataout_2,
  output [31:0] IR_2,
  output [31:0] PC_2,
  output [31:0] PC_4_2
);

  wire multiplexer_1_out, multiplexer_2_out, multiplexer_3_out, multiplexer_4_out, multiplexer_5_out,
       multiplexer_6_out;
  wire [1:0] multiplexer_8_out;
  wire [4:0] multiplexer_7_out;
  wire [31:0] multiplexer_9_out, multiplexer_10_out, multiplexer_11_out, multiplexer_12_out,
       multiplexer_13_out, multiplexer_14_out, multiplexer_15_out;

  Multiplexer #(.select(1), .width(1), .disabled("Z"), .enable("false")) multiplexer_1 (
    .in0(LB), .in1(1'b0), .out(multiplexer_1_out), .sel(RST));
  Multiplexer #(.select(1), .width(1), .disabled("Z"), .enable("false")) multiplexer_2 (
    .in0(JALR), .in1(1'b0), .out(multiplexer_2_out), .sel(RST));
  Multiplexer #(.select(1), .width(1), .disabled("Z"), .enable("false")) multiplexer_3 (
    .in0(JAL), .in1(1'b0), .out(multiplexer_3_out), .sel(RST));
  Multiplexer #(.select(1), .width(1), .disabled("Z"), .enable("false")) multiplexer_4 (
    .in0(MenToReg), .in1(1'b0), .out(multiplexer_4_out), .sel(RST));
  Multiplexer #(.select(1), .width(1), .disabled("Z"), .enable("false")) multiplexer_5 (
    .in0(RegWrite), .in1(1'b0), .out(multiplexer_5_out), .sel(RST));
  Multiplexer #(.select(1), .width(1), .disabled("Z"), .enable("false")) multiplexer_6 (
    .in0(ecall), .in1(1'b0), .out(multiplexer_6_out), .sel(RST));
  Multiplexer #(.select(1), .width(5), .disabled("Z"), .enable("false")) multiplexer_7 (
    .in0(rd), .in1({5{1'b0}}), .out(multiplexer_7_out), .sel(RST));
  Multiplexer #(.select(1), .width(2), .disabled("Z"), .enable("false")) multiplexer_8 (
    .in0(addr), .in1(2'b00), .out(multiplexer_8_out), .sel(RST));
  Multiplexer #(.select(1), .width(32), .disabled("Z"), .enable("false")) multiplexer_9 (
    .in0(R1), .in1({32{1'b0}}), .out(multiplexer_9_out), .sel(RST));
  Multiplexer #(.select(1), .width(32), .disabled("Z"), .enable("false")) multiplexer_10 (
    .in0(R2), .in1({32{1'b0}}), .out(multiplexer_10_out), .sel(RST));
  Multiplexer #(.select(1), .width(32), .disabled("Z"), .enable("false")) multiplexer_11 (
    .in0(R), .in1({32{1'b0}}), .out(multiplexer_11_out), .sel(RST));
  Multiplexer #(.select(1), .width(32), .disabled("Z"), .enable("false")) multiplexer_12 (
    .in0(Dataout), .in1({32{1'b0}}), .out(multiplexer_12_out), .sel(RST));
  Multiplexer #(.select(1), .width(32), .disabled("Z"), .enable("false")) multiplexer_13 (
    .in0(IR), .in1({32{1'b0}}), .out(multiplexer_13_out), .sel(RST));
  Multiplexer #(.select(1), .width(32), .disabled("Z"), .enable("false")) multiplexer_14 (
    .in0(PC), .in1({32{1'b0}}), .out(multiplexer_14_out), .sel(RST));
  Multiplexer #(.select(1), .width(32), .disabled("Z"), .enable("false")) multiplexer_15 (
    .in0(PC_4), .in1({32{1'b0}}), .out(multiplexer_15_out), .sel(RST));
  Register #(.width(1), .trigger("rising"), .Select("low")) register_1 (
    .D(multiplexer_1_out), .en(en), .Q(LB_2), .clk(CLK));  // open: clr
  Register #(.width(1), .trigger("rising"), .Select("low")) register_2 (
    .D(multiplexer_2_out), .en(en), .Q(JALR_2), .clk(CLK));  // open: clr
  Register #(.width(1), .trigger("rising"), .Select("low")) register_3 (
    .D(multiplexer_3_out), .en(en), .Q(JAL_2), .clk(CLK));  // open: clr
  Register #(.width(1), .trigger("rising"), .Select("low")) register_4 (
    .D(multiplexer_4_out), .en(en), .Q(MemToReg), .clk(CLK));  // open: clr
  Register #(.width(1), .trigger("rising"), .Select("low")) register_5 (
    .D(multiplexer_5_out), .en(en), .Q(RegWrite_2), .clk(CLK));  // open: clr
  Register #(.width(1), .trigger("rising"), .Select("low")) register_6 (
    .D(multiplexer_6_out), .en(en), .Q(ecall_2), .clk(CLK));  // open: clr
  Register #(.width(5), .trigger("rising"), .Select("low")) register_7 (
    .D(multiplexer_7_out), .en(en), .Q(rd_2), .clk(CLK));  // open: clr
  Register #(.width(2), .trigger("rising"), .Select("low")) register_8 (
    .D(multiplexer_8_out), .en(en), .Q(Addr_2), .clk(CLK));  // open: clr
  Register #(.width(32), .trigger("rising"), .Select("low")) register_9 (
    .D(multiplexer_9_out), .en(en), .Q(R1_2), .clk(CLK));  // open: clr
  Register #(.width(32), .trigger("rising"), .Select("low")) register_10 (
    .D(multiplexer_10_out), .en(en), .Q(R2_2), .clk(CLK));  // open: clr
  Register #(.width(32), .trigger("rising"), .Select("low")) register_11 (
    .D(multiplexer_11_out), .en(en), .Q(R_2), .clk(CLK));  // open: clr
  Register #(.width(32), .trigger("rising"), .Select("low")) register_12 (
    .D(multiplexer_12_out), .en(en), .Q(Dataout_2), .clk(CLK));  // open: clr
  Register #(.width(32), .trigger("rising"), .Select("low")) register_13 (
    .D(multiplexer_13_out), .en(en), .Q(IR_2), .clk(CLK));  // open: clr
  Register #(.width(32), .trigger("rising"), .Select("low")) register_14 (
    .D(multiplexer_14_out), .en(en), .Q(PC_2), .clk(CLK));  // open: clr
  Register #(.width(32), .trigger("rising"), .Select("low")) register_15 (
    .D(multiplexer_15_out), .en(en), .Q(PC_4_2), .clk(CLK));  // open: clr
endmodule

module \气泡  (
  input  in_1,
  input  [4:0] in_2,
  input  [31:0] in_3,
  input  in_4,
  input  [4:0] in_5,
  input  in_6,
  input  in_7,
  output out_8,
  output out_9
);

  wire and_1_out, and_2_out, and_3_out, and_4_out, and_5_out, and_6_out, and_7_out, and_8_out,
       comparator_1_eq, comparator_2_eq, comparator_3_eq, comparator_4_eq, comparator_5_eq, comparator_6_eq,
       comparator_7_eq, comparator_8_eq, comparator_9_eq, comparator_10_eq, or_1_out, or_2_out, or_3_out,
       or_4_out, rs1_used, rs2_used;

  Comparator #(.width(5), .mode("twosComplement")) comparator_1 (
    .a({5{1'b0}}), .b(in_3[19:15]), .eq(comparator_1_eq));  // open: gt, lt
  Comparator #(.width(5), .mode("twosComplement")) comparator_2 (
    .a(in_3[19:15]), .b(in_2), .eq(comparator_2_eq));  // open: gt, lt
  Comparator #(.width(5), .mode("twosComplement")) comparator_3 (
    .a(in_3[19:15]), .b(in_5), .eq(comparator_3_eq));  // open: gt, lt
  Comparator #(.width(5), .mode("twosComplement")) comparator_4 (
    .a({5{1'b0}}), .b(in_3[24:20]), .eq(comparator_4_eq));  // open: gt, lt
  Comparator #(.width(5), .mode("twosComplement")) comparator_5 (
    .a(in_3[24:20]), .b(in_2), .eq(comparator_5_eq));  // open: gt, lt
  Comparator #(.width(5), .mode("twosComplement")) comparator_6 (
    .a(in_3[24:20]), .b(in_5), .eq(comparator_6_eq));  // open: gt, lt
  and and_1 (and_1_out, comparator_2_eq, in_1);
  and and_2 (and_2_out, comparator_3_eq, in_4);
  and and_3 (and_3_out, comparator_5_eq, in_1);
  and and_4 (and_4_out, comparator_6_eq, in_4);
  Comparator #(.width(5), .mode("twosComplement")) comparator_7 (
    .a(5'b10001), .b(in_2), .eq(comparator_7_eq));  // open: gt, lt
  Comparator #(.width(5), .mode("twosComplement")) comparator_8 (
    .a(in_2), .b(5'b01010), .eq(comparator_8_eq));  // open: gt, lt
  Comparator #(.width(5), .mode("twosComplement")) comparator_9 (
    .a(5'b10001), .b(in_5), .eq(comparator_9_eq));  // open: gt, lt
  Comparator #(.width(5), .mode("twosComplement")) comparator_10 (
    .a(in_5), .b(5'b01010), .eq(comparator_10_eq));  // open: gt, lt
  or or_1 (or_1_out, and_1_out, and_2_out);
  or or_2 (or_2_out, and_3_out, and_4_out);
  or or_3 (or_3_out, comparator_7_eq, comparator_8_eq);
  or or_4 (or_4_out, comparator_9_eq, comparator_10_eq);
  and and_5 (and_5_out, rs1_used, ~comparator_1_eq, or_1_out);  // AND_Gate
  and and_6 (and_6_out, rs2_used, ~comparator_4_eq, or_2_out);  // AND_Gate
  and and_7 (and_7_out, in_1, or_3_out, in_6);
  and and_8 (and_8_out, in_6, or_4_out, in_4);
  or or_5 (out_8, and_5_out, and_6_out, and_7_out, and_8_out);
  rs_used rs_used_1 (
    .OP2(in_3[2]), .OP3(in_3[3]), .OP4(in_3[4]), .OP5(in_3[5]), .OP6(in_3[6]), .F12(in_3[12]),
    .F13(in_3[13]), .F14(in_3[14]), .F25(in_3[25]), .F30(in_3[30]), .rs1_used(rs1_used), .rs2_used(rs2_used));
  or or_6 (out_9, out_8, in_7);

  // Other names for the same wires on the sheet: BranchTaken = in_7; ecall = in_6; EX_rd[4:0] = in_2;
  //   EX_RegWrite = in_1; flush = out_9; ID_IR[31:0] = in_3; rs1[4:0] = in_3[19:15]; rs2[4:0] = in_3[24:20];
  //   MEM_rd[4:0] = in_5; MEM_RegWrite = in_4; datahazzard = out_8; stall = out_8
endmodule

module \重定向  (
  input  [4:0] in_1,
  input  [31:0] in_2,
  input  [4:0] in_3,
  input  in_4,
  input  in_5,
  input  in_6,
  input  in_7,
  input  BranchTaken,
  output [1:0] out_9,
  output [1:0] out_10,
  output stall,
  output flush
);

  wire and_1_out, and_2_out, and_7_out, and_8_out, and_9_out, and_10_out, and_11_out, and_12_out,
       comparator_1_eq, comparator_2_eq, comparator_3_eq, comparator_4_eq, comparator_5_eq, comparator_6_eq,
       comparator_7_eq, comparator_8_eq, comparator_9_eq, comparator_10_eq, EX_ecall1, EX_ecall2, EX_rs1,
       EX_rs2, MEM_ecall1, MEM_ecall2, MEM_rs1, MEM_rs2, or_3_out, or_4_out, or_5_out, or_6_out, rs1_used,
       rs2_used;

  Comparator #(.width(5), .mode("twosComplement")) comparator_1 (
    .a(in_1), .b(in_2[19:15]), .eq(comparator_1_eq));  // open: gt, lt
  Comparator #(.width(5), .mode("twosComplement")) comparator_2 (
    .a({5{1'b0}}), .b(in_2[19:15]), .eq(comparator_2_eq));  // open: gt, lt
  Comparator #(.width(5), .mode("twosComplement")) comparator_3 (
    .a(in_2[19:15]), .b(in_3), .eq(comparator_3_eq));  // open: gt, lt
  Comparator #(.width(5), .mode("twosComplement")) comparator_4 (
    .a(in_1), .b(in_2[24:20]), .eq(comparator_4_eq));  // open: gt, lt
  Comparator #(.width(5), .mode("twosComplement")) comparator_5 (
    .a({5{1'b0}}), .b(in_2[24:20]), .eq(comparator_5_eq));  // open: gt, lt
  Comparator #(.width(5), .mode("twosComplement")) comparator_6 (
    .a(in_2[24:20]), .b(in_3), .eq(comparator_6_eq));  // open: gt, lt
  rs_used rs_used_1 (
    .OP2(in_2[2]), .OP3(in_2[3]), .OP4(in_2[4]), .OP5(in_2[5]), .OP6(in_2[6]), .F12(in_2[12]),
    .F13(in_2[13]), .F14(in_2[14]), .F25(in_2[25]), .F30(in_2[30]), .rs1_used(rs1_used), .rs2_used(rs2_used));
  and and_1 (and_1_out, EX_rs1, in_6);
  and and_2 (and_2_out, in_6, EX_rs2);
  and and_3 (EX_rs1, comparator_1_eq, rs1_used, ~comparator_2_eq);  // AND_Gate
  and and_4 (MEM_rs1, ~comparator_2_eq, rs1_used, comparator_3_eq);  // AND_Gate
  and and_5 (EX_rs2, comparator_4_eq, rs2_used, ~comparator_5_eq);  // AND_Gate
  and and_6 (MEM_rs2, ~comparator_5_eq, rs2_used, comparator_6_eq);  // AND_Gate
  or or_1 (stall, and_1_out, and_2_out);
  and and_7 (and_7_out, EX_rs1, in_4);
  and and_8 (and_8_out, MEM_rs1, in_5);
  and and_9 (and_9_out, EX_rs2, in_4);
  and and_10 (and_10_out, MEM_rs2, in_5);
  or or_2 (flush, stall, BranchTaken);
  Comparator #(.width(5), .mode("twosComplement")) comparator_7 (
    .a(in_1), .b(5'b10001), .eq(comparator_7_eq));  // open: gt, lt
  Comparator #(.width(5), .mode("twosComplement")) comparator_8 (
    .a(in_3), .b(5'b10001), .eq(comparator_8_eq));  // open: gt, lt
  Comparator #(.width(5), .mode("twosComplement")) comparator_9 (
    .a(in_1), .b(5'b01010), .eq(comparator_9_eq));  // open: gt, lt
  Comparator #(.width(5), .mode("twosComplement")) comparator_10 (
    .a(in_3), .b(5'b01010), .eq(comparator_10_eq));  // open: gt, lt
  or or_3 (or_3_out, and_7_out, EX_ecall1);
  and and_11 (and_11_out, ~or_3_out, or_4_out);  // AND_Gate
  or or_4 (or_4_out, MEM_ecall1, and_8_out);
  or or_5 (or_5_out, and_9_out, EX_ecall2);
  and and_12 (and_12_out, ~or_5_out, or_6_out);  // AND_Gate
  or or_6 (or_6_out, MEM_ecall2, and_10_out);
  and and_13 (EX_ecall1, in_4, in_7, comparator_7_eq);
  and and_14 (MEM_ecall1, in_7, in_5, comparator_8_eq);
  and and_15 (EX_ecall2, in_4, in_7, comparator_9_eq);
  and and_16 (MEM_ecall2, in_5, in_7, comparator_10_eq);
  Priority_Encoder #(.select(2), .disabled("Z")) priority_encoder_1 (
    .in0(1'b1), .in1(or_3_out), .in2(and_11_out), .out(out_9));  // open: in3, gs, en_out, en_in
  Priority_Encoder #(.select(2), .disabled("Z")) priority_encoder_2 (
    .in0(1'b1), .in1(or_5_out), .in2(and_12_out), .out(out_10));  // open: in3, gs, en_out, en_in

  // Other names for the same wires on the sheet: ecall = in_7; EX_MemToReg = in_6; EX_rd[4:0] = in_1;
  //   EX_RegWrite = in_4; ID_IR[31:0] = in_2; rs1[4:0] = in_2[19:15]; rs2[4:0] = in_2[24:20]; LoadUse = stall;
  //   MEM_rd[4:0] = in_3; MEM_RegWrite = in_5; rs1Forward[1:0] = out_9; rs2Forward[1:0] = out_10
endmodule

module rs_used (
  input  OP2,
  input  OP3,
  input  OP4,
  input  OP5,
  input  OP6,
  input  F12,
  input  F13,
  input  F14,
  input  F25,
  input  F30,
  output rs1_used,
  output rs2_used
);

  wire and_1_out, and_2_out, and_3_out, and_4_out, and_5_out, and_6_out, and_7_out, and_8_out, and_9_out,
       and_10_out, and_11_out, and_12_out, and_13_out, and_14_out, and_15_out, and_16_out, and_17_out,
       and_18_out, and_19_out, and_20_out, and_21_out, and_22_out, and_23_out, and_24_out, and_25_out,
       and_26_out, and_27_out, and_28_out, and_29_out, and_30_out, and_31_out, and_32_out, and_33_out,
       and_34_out, and_35_out, not_1_out, not_2_out, not_3_out, not_4_out, not_5_out, not_6_out, not_7_out,
       not_8_out, not_9_out, not_10_out, not_11_out, not_12_out, not_13_out, not_14_out, not_15_out,
       not_16_out, not_17_out, not_18_out, not_19_out, not_20_out, not_21_out, not_22_out, not_23_out,
       not_24_out, not_25_out, not_26_out, not_27_out, not_28_out, not_29_out, not_30_out, not_31_out,
       not_32_out, not_33_out, not_34_out, not_35_out, not_36_out, not_37_out, not_38_out, not_39_out,
       not_40_out, not_41_out, not_42_out, not_43_out, not_44_out, not_45_out, not_46_out, not_47_out,
       not_48_out, not_49_out, not_50_out, not_51_out, not_52_out, not_53_out, not_54_out, not_55_out,
       not_56_out, not_57_out, not_58_out, not_59_out, not_60_out, not_61_out, not_62_out, not_63_out,
       not_64_out, not_65_out, not_66_out, not_67_out, not_68_out, not_69_out, not_70_out, not_71_out,
       not_72_out, not_73_out, not_74_out, not_75_out, not_76_out, not_77_out, not_78_out, not_79_out,
       not_80_out, not_81_out, not_82_out, not_83_out, not_84_out, not_85_out, not_86_out, not_87_out,
       not_88_out, not_89_out, not_90_out, not_91_out, not_92_out, not_93_out, not_94_out, not_95_out,
       not_96_out, not_97_out, not_98_out, not_99_out, not_100_out, not_101_out, not_102_out, not_103_out,
       not_104_out, not_105_out, not_106_out, not_107_out, not_108_out, not_109_out, not_110_out,
       not_111_out, not_112_out, not_113_out, not_114_out, not_115_out, not_116_out, not_117_out,
       not_118_out, not_119_out, not_120_out, not_121_out, not_122_out, not_123_out, not_124_out,
       not_125_out, not_126_out, not_127_out, not_128_out, not_129_out, not_130_out, not_131_out,
       not_132_out, not_133_out, not_134_out, not_135_out, not_136_out, not_137_out, not_138_out,
       not_139_out, not_140_out, not_141_out, not_142_out, not_143_out, not_144_out, not_145_out,
       not_146_out, not_147_out, not_148_out, not_149_out, not_150_out, not_151_out, not_152_out,
       not_153_out, not_154_out, not_155_out, not_156_out, not_157_out, not_158_out, not_159_out,
       not_160_out, not_161_out, not_162_out, not_163_out, not_164_out, not_165_out, not_166_out,
       not_167_out, not_168_out, not_169_out, not_170_out, not_171_out, not_172_out, not_173_out,
       not_174_out, not_175_out, not_176_out, not_177_out, not_178_out, not_179_out, not_180_out,
       not_181_out, not_182_out, not_183_out, not_184_out, not_185_out, not_186_out, not_187_out,
       not_188_out, not_189_out, not_190_out, not_191_out, not_192_out, not_193_out, not_194_out,
       not_195_out, not_196_out, not_197_out, not_198_out, not_199_out, not_200_out, not_201_out,
       not_202_out, not_203_out, not_204_out, not_205_out, not_206_out, not_207_out, not_208_out,
       not_209_out, not_210_out, not_211_out, not_212_out, not_213_out, not_214_out, not_215_out;

  not not_1 (not_1_out, F30);
  not not_2 (not_2_out, F25);
  not not_3 (not_3_out, F14);
  not not_4 (not_4_out, F13);
  not not_5 (not_5_out, F12);
  not not_6 (not_6_out, OP6);
  not not_7 (not_7_out, OP3);
  not not_8 (not_8_out, OP2);
  not not_9 (not_9_out, F25);
  not not_10 (not_10_out, F14);
  not not_11 (not_11_out, F13);
  not not_12 (not_12_out, F12);
  not not_13 (not_13_out, OP6);
  not not_14 (not_14_out, OP3);
  not not_15 (not_15_out, OP2);
  not not_16 (not_16_out, F30);
  not not_17 (not_17_out, F25);
  not not_18 (not_18_out, OP6);
  not not_19 (not_19_out, OP3);
  not not_20 (not_20_out, OP2);
  not not_21 (not_21_out, F30);
  not not_22 (not_22_out, F25);
  not not_23 (not_23_out, F12);
  not not_24 (not_24_out, OP6);
  not not_25 (not_25_out, OP3);
  not not_26 (not_26_out, OP2);
  not not_27 (not_27_out, F30);
  not not_28 (not_28_out, F25);
  not not_29 (not_29_out, F14);
  not not_30 (not_30_out, F12);
  not not_31 (not_31_out, OP6);
  not not_32 (not_32_out, OP3);
  not not_33 (not_33_out, OP2);
  not not_34 (not_34_out, F30);
  not not_35 (not_35_out, F25);
  not not_36 (not_36_out, F14);
  not not_37 (not_37_out, OP6);
  not not_38 (not_38_out, OP3);
  not not_39 (not_39_out, OP2);
  not not_40 (not_40_out, F14);
  not not_41 (not_41_out, F13);
  not not_42 (not_42_out, F12);
  not not_43 (not_43_out, OP6);
  not not_44 (not_44_out, OP5);
  not not_45 (not_45_out, OP3);
  not not_46 (not_46_out, OP2);
  not not_47 (not_47_out, OP6);
  not not_48 (not_48_out, OP5);
  not not_49 (not_49_out, OP3);
  not not_50 (not_50_out, OP2);
  not not_51 (not_51_out, F12);
  not not_52 (not_52_out, OP6);
  not not_53 (not_53_out, OP5);
  not not_54 (not_54_out, OP3);
  not not_55 (not_55_out, OP2);
  not not_56 (not_56_out, F13);
  not not_57 (not_57_out, F12);
  not not_58 (not_58_out, OP6);
  not not_59 (not_59_out, OP5);
  not not_60 (not_60_out, OP3);
  not not_61 (not_61_out, OP2);
  not not_62 (not_62_out, F14);
  not not_63 (not_63_out, F12);
  not not_64 (not_64_out, OP6);
  not not_65 (not_65_out, OP5);
  not not_66 (not_66_out, OP3);
  not not_67 (not_67_out, OP2);
  not not_68 (not_68_out, F30);
  not not_69 (not_69_out, F25);
  not not_70 (not_70_out, F14);
  not not_71 (not_71_out, F13);
  not not_72 (not_72_out, OP6);
  not not_73 (not_73_out, OP5);
  not not_74 (not_74_out, OP3);
  not not_75 (not_75_out, OP2);
  not not_76 (not_76_out, F30);
  not not_77 (not_77_out, F25);
  not not_78 (not_78_out, F13);
  not not_79 (not_79_out, OP6);
  not not_80 (not_80_out, OP5);
  not not_81 (not_81_out, OP3);
  not not_82 (not_82_out, OP2);
  not not_83 (not_83_out, F25);
  not not_84 (not_84_out, F13);
  not not_85 (not_85_out, OP6);
  not not_86 (not_86_out, OP5);
  not not_87 (not_87_out, OP3);
  not not_88 (not_88_out, OP2);
  not not_89 (not_89_out, F14);
  not not_90 (not_90_out, F12);
  not not_91 (not_91_out, OP6);
  not not_92 (not_92_out, OP5);
  not not_93 (not_93_out, OP4);
  not not_94 (not_94_out, OP3);
  not not_95 (not_95_out, OP2);
  not not_96 (not_96_out, F14);
  not not_97 (not_97_out, F12);
  not not_98 (not_98_out, OP6);
  not not_99 (not_99_out, OP4);
  not not_100 (not_100_out, OP3);
  not not_101 (not_101_out, OP2);
  not not_102 (not_102_out, F14);
  not not_103 (not_103_out, F13);
  not not_104 (not_104_out, F12);
  not not_105 (not_105_out, OP4);
  not not_106 (not_106_out, OP3);
  not not_107 (not_107_out, OP2);
  not not_108 (not_108_out, F14);
  not not_109 (not_109_out, F13);
  not not_110 (not_110_out, OP4);
  not not_111 (not_111_out, OP3);
  not not_112 (not_112_out, OP2);
  not not_113 (not_113_out, F14);
  not not_114 (not_114_out, F13);
  not not_115 (not_115_out, F12);
  not not_116 (not_116_out, OP4);
  not not_117 (not_117_out, OP3);
  not not_118 (not_118_out, F30);
  not not_119 (not_119_out, F25);
  not not_120 (not_120_out, F14);
  not not_121 (not_121_out, F13);
  not not_122 (not_122_out, OP6);
  not not_123 (not_123_out, OP3);
  not not_124 (not_124_out, OP2);
  not not_125 (not_125_out, F30);
  not not_126 (not_126_out, F25);
  not not_127 (not_127_out, F13);
  not not_128 (not_128_out, OP6);
  not not_129 (not_129_out, OP3);
  not not_130 (not_130_out, OP2);
  not not_131 (not_131_out, F14);
  not not_132 (not_132_out, F13);
  not not_133 (not_133_out, F12);
  not not_134 (not_134_out, OP6);
  not not_135 (not_135_out, OP5);
  not not_136 (not_136_out, OP4);
  not not_137 (not_137_out, OP3);
  not not_138 (not_138_out, OP2);
  not not_139 (not_139_out, F13);
  not not_140 (not_140_out, OP4);
  not not_141 (not_141_out, OP3);
  not not_142 (not_142_out, OP2);
  not not_143 (not_143_out, F30);
  not not_144 (not_144_out, F25);
  not not_145 (not_145_out, F14);
  not not_146 (not_146_out, F13);
  not not_147 (not_147_out, F12);
  not not_148 (not_148_out, OP6);
  not not_149 (not_149_out, OP3);
  not not_150 (not_150_out, OP2);
  not not_151 (not_151_out, F25);
  not not_152 (not_152_out, F14);
  not not_153 (not_153_out, F13);
  not not_154 (not_154_out, F12);
  not not_155 (not_155_out, OP6);
  not not_156 (not_156_out, OP3);
  not not_157 (not_157_out, OP2);
  not not_158 (not_158_out, F30);
  not not_159 (not_159_out, F25);
  not not_160 (not_160_out, OP6);
  not not_161 (not_161_out, OP3);
  not not_162 (not_162_out, OP2);
  not not_163 (not_163_out, F30);
  not not_164 (not_164_out, F25);
  not not_165 (not_165_out, F12);
  not not_166 (not_166_out, OP6);
  not not_167 (not_167_out, OP3);
  not not_168 (not_168_out, OP2);
  not not_169 (not_169_out, F30);
  not not_170 (not_170_out, F25);
  not not_171 (not_171_out, F14);
  not not_172 (not_172_out, F12);
  not not_173 (not_173_out, OP6);
  not not_174 (not_174_out, OP3);
  not not_175 (not_175_out, OP2);
  not not_176 (not_176_out, F30);
  not not_177 (not_177_out, F25);
  not not_178 (not_178_out, F14);
  not not_179 (not_179_out, OP6);
  not not_180 (not_180_out, OP3);
  not not_181 (not_181_out, OP2);
  not not_182 (not_182_out, F14);
  not not_183 (not_183_out, F12);
  not not_184 (not_184_out, OP6);
  not not_185 (not_185_out, OP4);
  not not_186 (not_186_out, OP3);
  not not_187 (not_187_out, OP2);
  not not_188 (not_188_out, F14);
  not not_189 (not_189_out, F13);
  not not_190 (not_190_out, F12);
  not not_191 (not_191_out, OP4);
  not not_192 (not_192_out, OP3);
  not not_193 (not_193_out, OP2);
  not not_194 (not_194_out, F14);
  not not_195 (not_195_out, F13);
  not not_196 (not_196_out, OP4);
  not not_197 (not_197_out, OP3);
  not not_198 (not_198_out, OP2);
  not not_199 (not_199_out, F30);
  not not_200 (not_200_out, F25);
  not not_201 (not_201_out, F14);
  not not_202 (not_202_out, F13);
  not not_203 (not_203_out, OP6);
  not not_204 (not_204_out, OP3);
  not not_205 (not_205_out, OP2);
  not not_206 (not_206_out, F30);
  not not_207 (not_207_out, F25);
  not not_208 (not_208_out, F13);
  not not_209 (not_209_out, OP6);
  not not_210 (not_210_out, OP3);
  not not_211 (not_211_out, OP2);
  not not_212 (not_212_out, F13);
  not not_213 (not_213_out, OP4);
  not not_214 (not_214_out, OP3);
  not not_215 (not_215_out, OP2);
  and and_1 (and_1_out, not_1_out, not_2_out, not_3_out, not_4_out, not_5_out, not_6_out, OP5, OP4, not_7_out, not_8_out);
  and and_2 (and_2_out, F30, not_9_out, not_10_out, not_11_out, not_12_out, not_13_out, OP5, OP4, not_14_out, not_15_out);
  and and_3 (and_3_out, not_16_out, not_17_out, F14, F13, F12, not_18_out, OP5, OP4, not_19_out, not_20_out);
  and and_4 (and_4_out, not_21_out, not_22_out, F14, F13, not_23_out, not_24_out, OP5, OP4, not_25_out, not_26_out);
  and and_5 (and_5_out, not_27_out, not_28_out, not_29_out, F13, not_30_out, not_31_out, OP5, OP4, not_32_out, not_33_out);
  and and_6 (and_6_out, not_34_out, not_35_out, not_36_out, F13, F12, not_37_out, OP5, OP4, not_38_out, not_39_out);
  and and_7 (and_7_out, not_40_out, not_41_out, not_42_out, not_43_out, not_44_out, OP4, not_45_out, not_46_out);
  and and_8 (and_8_out, F14, F13, F12, not_47_out, not_48_out, OP4, not_49_out, not_50_out);
  and and_9 (and_9_out, F14, F13, not_51_out, not_52_out, not_53_out, OP4, not_54_out, not_55_out);
  and and_10 (and_10_out, F14, not_56_out, not_57_out, not_58_out, not_59_out, OP4, not_60_out, not_61_out);
  and and_11 (and_11_out, not_62_out, F13, not_63_out, not_64_out, not_65_out, OP4, not_66_out, not_67_out);
  and and_12 (and_12_out, not_68_out, not_69_out, not_70_out, not_71_out, F12, not_72_out, not_73_out, OP4, not_74_out, not_75_out);
  and and_13 (and_13_out, not_76_out, not_77_out, F14, not_78_out, F12, not_79_out, not_80_out, OP4, not_81_out, not_82_out);
  and and_14 (and_14_out, F30, not_83_out, F14, not_84_out, F12, not_85_out, not_86_out, OP4, not_87_out, not_88_out);
  and and_15 (and_15_out, not_89_out, F13, not_90_out, not_91_out, not_92_out, not_93_out, not_94_out, not_95_out);
  and and_16 (and_16_out, not_96_out, F13, not_97_out, not_98_out, OP5, not_99_out, not_100_out, not_101_out);
  and and_17 (and_17_out, not_102_out, not_103_out, not_104_out, OP6, OP5, not_105_out, not_106_out, not_107_out);
  and and_18 (and_18_out, not_108_out, not_109_out, F12, OP6, OP5, not_110_out, not_111_out, not_112_out);
  and and_19 (and_19_out, not_113_out, not_114_out, not_115_out, OP6, OP5, not_116_out, not_117_out, OP2);
  and and_20 (and_20_out, not_118_out, not_119_out, not_120_out, not_121_out, F12, not_122_out, OP5, OP4, not_123_out, not_124_out);
  and and_21 (and_21_out, not_125_out, not_126_out, F14, not_127_out, F12, not_128_out, OP5, OP4, not_129_out, not_130_out);
  and and_22 (and_22_out, not_131_out, not_132_out, not_133_out, not_134_out, not_135_out, not_136_out, not_137_out, not_138_out);
  and and_23 (and_23_out, F14, not_139_out, F12, OP6, OP5, not_140_out, not_141_out, not_142_out);
  and and_24 (and_24_out, not_143_out, not_144_out, not_145_out, not_146_out, not_147_out, not_148_out, OP5, OP4, not_149_out, not_150_out);
  and and_25 (and_25_out, F30, not_151_out, not_152_out, not_153_out, not_154_out, not_155_out, OP5, OP4, not_156_out, not_157_out);
  and and_26 (and_26_out, not_158_out, not_159_out, F14, F13, F12, not_160_out, OP5, OP4, not_161_out, not_162_out);
  and and_27 (and_27_out, not_163_out, not_164_out, F14, F13, not_165_out, not_166_out, OP5, OP4, not_167_out, not_168_out);
  and and_28 (and_28_out, not_169_out, not_170_out, not_171_out, F13, not_172_out, not_173_out, OP5, OP4, not_174_out, not_175_out);
  and and_29 (and_29_out, not_176_out, not_177_out, not_178_out, F13, F12, not_179_out, OP5, OP4, not_180_out, not_181_out);
  and and_30 (and_30_out, not_182_out, F13, not_183_out, not_184_out, OP5, not_185_out, not_186_out, not_187_out);
  and and_31 (and_31_out, not_188_out, not_189_out, not_190_out, OP6, OP5, not_191_out, not_192_out, not_193_out);
  and and_32 (and_32_out, not_194_out, not_195_out, F12, OP6, OP5, not_196_out, not_197_out, not_198_out);
  and and_33 (and_33_out, not_199_out, not_200_out, not_201_out, not_202_out, F12, not_203_out, OP5, OP4, not_204_out, not_205_out);
  and and_34 (and_34_out, not_206_out, not_207_out, F14, not_208_out, F12, not_209_out, OP5, OP4, not_210_out, not_211_out);
  and and_35 (and_35_out, F14, not_212_out, F12, OP6, OP5, not_213_out, not_214_out, not_215_out);
  or or_1 (rs2_used, and_24_out, and_25_out, and_26_out, and_27_out, and_28_out, and_29_out, and_30_out, and_31_out, and_32_out, and_33_out, and_34_out, and_35_out);
  or or_2 (rs1_used, and_1_out, and_2_out, and_3_out, and_4_out, and_5_out, and_6_out, and_7_out, and_8_out, and_9_out, and_10_out, and_11_out, and_12_out, and_13_out, and_14_out, and_15_out, and_16_out, and_17_out, and_18_out, and_19_out, and_20_out, and_21_out, and_22_out, and_23_out);
endmodule

module \单级自测  (
  input  IR1,
  input  IR2,
  input  IR3,
  output RegWrite,
  output MemWrite,
  output [31:0] PC,
  output [31:0] IR,
  output [31:0] RDin,
  output [31:0] MDin,
  output [31:0] LedData
);

  wire _1_out, _2_out, _3_out, and_1_out, and_2_out, and_3_out, and_4_out, and_5_out, and_7_out, and_8_out,
       and_9_out, Beq, BGE, Bne, Branch, CLK, Clr1, Clr2, Clr3, comparator_1_eq, comparator_2_eq,
       comparator_3_eq, comparator_4_eq, comparator_5_eq, d_ff_1_q, d_ff_2_q, d_ff_3_q, d_ff_4_q, d_ff_5_q,
       d_ff_6_q, decoder_1_out1, decoder_1_out2, decoder_1_out3, ecall, Go, halt, IE, INT, IR1_t, IR2_t,
       IR3_t, IRA, IRB, IRC, JAL, JALR, LB, MemToReg, not_1_out, not_2_out, not_3_out, or_1_out, or_6_out,
       or_7_out, or_8_out, or_12_out, register_1_q, RST, tunnel, tunnel_t, tunnel_t_t, URET, W1, W2, W3,
       \中断信号 , \单周期硬布线控制器_1_alu_src , \单周期硬布线控制器_1_s_type ;
  wire [1:0] Addr, now_q, priority_encoder_1_out, priority_encoder_2_out, priority_encoder_4_out, \中断号 ;
  wire [3:0] \单周期硬布线控制器_1_alu_op ;
  wire [4:0] multiplexer_3_out, multiplexer_4_out;
  wire [15:0] \总周期数 ;
  wire [31:0] b, bit_extender_1_out, bit_extender_2_out, bit_extender_3_out, bit_extender_4_out,
       bit_extender_5_out, bit_extender_6_out, bit_extender_7_out, bit_extender_8_out, \byte , INT_PC, j,
       multiplexer_2_out, multiplexer_5_out, multiplexer_7_out, PC_4, R1, ram_1_data, RET_PC, shifter_1_out,
       shifter_2_out, word, \现场 ;
  wire [31:2] R;

  Clock #(.highDuration(1), .lowDuration(1)) clock_1 (.out(CLK));
  Button _1 (.out(_1_out));
  Button _2 (.out(_2_out));
  Button _3 (.out(_3_out));
  Button \u_继续运行  (.out(Go));
  LED #(.active("true")) led_1 (.in(W1));
  LED #(.active("true")) led_2 (.in(W2));
  LED #(.active("true")) led_3 (.in(W3));
  Hex_Digit_Display hex_digit_display_1 (.value(LedData[31:28]));  // open: dp
  Comparator #(.width(16), .mode("twosComplement")) comparator_1 (
    .a(16'h23b), .b(\总周期数 ), .eq(comparator_1_eq));  // open: gt, lt
  Comparator #(.width(16), .mode("twosComplement")) comparator_2 (
    .a(\总周期数 ), .b(16'h1), .eq(comparator_2_eq));  // open: gt, lt
  Comparator #(.width(16), .mode("twosComplement")) comparator_3 (
    .a(\总周期数 ), .b(16'h4), .eq(comparator_3_eq));  // open: gt, lt
  Comparator #(.width(16), .mode("twosComplement")) comparator_4 (
    .a(\总周期数 ), .b(16'h7), .eq(comparator_4_eq));  // open: gt, lt
  Comparator #(.width(32), .mode("twosComplement")) comparator_5 (
    .a(R1), .b(32'ha), .eq(comparator_5_eq));  // open: gt, lt
  Hex_Digit_Display hex_digit_display_2 (.value(LedData[27:24]));  // open: dp
  Hex_Digit_Display hex_digit_display_3 (.value(LedData[23:20]));  // open: dp
  or or_1 (or_1_out, comparator_1_eq, comparator_2_eq);
  assign IRA = or_1_out ? ~CLK : 1'bz;  // Controlled_Inverter controlled_inverter_1
  assign IRB = comparator_3_eq ? ~CLK : 1'bz;  // Controlled_Inverter controlled_inverter_2
  assign IRC = comparator_4_eq ? ~CLK : 1'bz;  // Controlled_Inverter controlled_inverter_3
  and and_1 (and_1_out, Beq, tunnel_t);
  or or_2 (Branch, and_1_out, and_2_out, and_3_out);
  and and_2 (and_2_out, ~tunnel_t, Bne);  // AND_Gate
  and and_3 (and_3_out, tunnel_t_t, BGE);
  Priority_Encoder #(.select(2), .disabled("Z")) priority_encoder_1 (
    .in0(1'b1), .in1(Branch), .in2(JAL), .in3(JALR), .out(priority_encoder_1_out));  // open: gs, en_out, en_in
  Multiplexer #(.select(2), .width(32), .disabled("Z"), .enable("false")) multiplexer_1 (
    .in0(PC_4), .in1(b), .in2(j), .in3({R, Addr}), .out(\现场 ), .sel(priority_encoder_1_out));
  Priority_Encoder #(.select(2), .disabled("Z")) priority_encoder_2 (
    .in0(1'b1), .in1(URET), .in2(INT), .out(priority_encoder_2_out));  // open: in3, gs, en_out, en_in
  and and_4 (and_4_out, ecall, ~comparator_5_eq);  // AND_Gate
  and and_5 (and_5_out, ecall, comparator_5_eq);
  Hex_Digit_Display hex_digit_display_4 (.value(LedData[15:12]));  // open: dp
  Hex_Digit_Display hex_digit_display_5 (.value(LedData[19:16]));  // open: dp
  Pull_Resistor #(.pull(0)) pull_resistor_1 (.node(IRA));
  Pull_Resistor #(.pull(0)) pull_resistor_2 (.node(IRB));
  Pull_Resistor #(.pull(0)) pull_resistor_3 (.node(IRC));
  Multiplexer #(.select(2), .width(32), .disabled("Z"), .enable("false")) multiplexer_2 (
    .in0(\现场 ), .in1(RET_PC), .in2(INT_PC), .out(multiplexer_2_out), .sel(priority_encoder_2_out));  // open: in3
  not not_1 (not_1_out, halt);
  Register #(.width(32), .trigger("rising"), .Select("low")) u_PC (
    .D(MDin), .en(and_4_out), .Q(LedData), .clk(CLK));  // open: clr
  and and_6 (halt, and_5_out, ~Go);  // AND_Gate
  Hex_Digit_Display hex_digit_display_6 (.value(LedData[7:4]));  // open: dp
  Hex_Digit_Display hex_digit_display_7 (.value(LedData[11:8]));  // open: dp
  // Probe on \总周期数 
  or or_3 (W1, d_ff_4_q, d_ff_1_q);
  or or_4 (W2, d_ff_5_q, d_ff_2_q);
  or or_5 (W3, d_ff_6_q, d_ff_3_q);
  Register #(.width(32), .trigger("rising"), .Select("low")) PC_2 (
    .D(multiplexer_2_out), .en(not_1_out), .Q(PC), .clk(CLK), .clr(RST));
  Hex_Digit_Display hex_digit_display_8 (.value(LedData[3:0]));  // open: dp
  D_Flip_Flop #(.trigger("rising"), .Pre_Clr_Positions("LEGACY"), .NegatePresetClear("false"), .enable("false"), .NewFFLayout("false")) d_ff_1 (
    .clk(IR1_t), .D(1'b1), .Q(d_ff_1_q), .reset(d_ff_4_q));  // open: Qn, preset
  D_Flip_Flop #(.trigger("rising"), .Pre_Clr_Positions("LEGACY"), .NegatePresetClear("false"), .enable("false"), .NewFFLayout("false")) d_ff_2 (
    .clk(IR2_t), .D(1'b1), .Q(d_ff_2_q), .reset(d_ff_5_q));  // open: Qn, preset
  D_Flip_Flop #(.trigger("rising"), .Pre_Clr_Positions("LEGACY"), .NegatePresetClear("false"), .enable("false"), .NewFFLayout("false")) d_ff_3 (
    .clk(IR3_t), .D(1'b1), .Q(d_ff_3_q), .reset(d_ff_6_q));  // open: Qn, preset
  Counter #(.width(16), .max('hffff), .ongoal("stay"), .trigger("rising"), .behavior("old")) counter_1 (
    .count(not_2_out), .Q(\总周期数 ), .clk(CLK), .clr(RST));  // open: load, D, carry, preset
  not not_2 (not_2_out, halt);
  // Probe on PC
  or or_6 (or_6_out, d_ff_1_q, d_ff_4_q);
  or or_7 (or_7_out, d_ff_2_q, d_ff_5_q);
  or or_8 (or_8_out, d_ff_3_q, d_ff_6_q);
  // RiscV_Probe riscv_probe_1: pin names not known; wires that end beside it: IR
  ROM #(.addrWidth(10), .dataWidth(32), .Select("high")) rom_1 (.addr(PC[11:2]), .data(IR));
  Adder #(.width(32)) adder_1 (.a(PC), .b(32'h4), .out(PC_4));  // open: cin, cout
  or or_9 (IR1_t, IR1, IRA);
  and and_7 (and_7_out, or_6_out, ~Clr1);  // AND_Gate
  and and_8 (and_8_out, or_7_out, ~Clr2);  // AND_Gate
  and and_9 (and_9_out, or_8_out, ~Clr3);  // AND_Gate
  or or_10 (IR2_t, IR2, IRB);
  D_Flip_Flop #(.trigger("rising"), .Pre_Clr_Positions("LEGACY"), .NegatePresetClear("false"), .enable("false"), .NewFFLayout("false")) d_ff_4 (
    .clk(CLK), .D(and_7_out), .Q(d_ff_4_q), .reset(RST));  // open: Qn, preset
  D_Flip_Flop #(.trigger("rising"), .Pre_Clr_Positions("LEGACY"), .NegatePresetClear("false"), .enable("false"), .NewFFLayout("false")) d_ff_5 (
    .clk(CLK), .D(and_8_out), .Q(d_ff_5_q), .reset(RST));  // open: Qn, preset
  D_Flip_Flop #(.trigger("rising"), .Pre_Clr_Positions("LEGACY"), .NegatePresetClear("false"), .enable("false"), .NewFFLayout("false")) d_ff_6 (
    .clk(CLK), .D(and_9_out), .Q(d_ff_6_q), .reset(RST));  // open: Qn, preset
  \单周期硬布线控制器  \u_单周期硬布线控制器_1  (
    .Funct({IR[30], IR[25], IR[14:12]}), .OP(IR[6:2]), .ALU_OP(\单周期硬布线控制器_1_alu_op ), .MemToReg(MemToReg),
    .MemWrite(MemWrite), .ALU_SRC(\单周期硬布线控制器_1_alu_src ), .RegWrite(RegWrite), .ecall(ecall),
    .S_type(\单周期硬布线控制器_1_s_type ), .Jalr(JALR), .Beq(Beq), .JAL(JAL), .Bne(Bne), .in_3(IR[21]), .uret(URET),
    .LB(LB), .BGE(BGE));  // open: CSRRSI, CSRRCI
  Multiplexer #(.select(1), .width(5), .disabled("Z"), .enable("false")) multiplexer_3 (
    .in0(IR[19:15]), .in1(5'b10001), .out(multiplexer_3_out), .sel(ecall));
  Multiplexer #(.select(1), .width(5), .disabled("Z"), .enable("false")) multiplexer_4 (
    .in0(IR[24:20]), .in1(5'b01010), .out(multiplexer_4_out), .sel(ecall));
  assign bit_extender_1_out = {{20{IR[31]}}, IR[31:20]};  // Bit_Extender bit_extender_1
  assign bit_extender_2_out = {{20{IR[31]}}, {IR[31:25], IR[11:7]}};  // Bit_Extender bit_extender_2
  Priority_Encoder #(.select(2), .disabled("Z")) priority_encoder_3 (
    .in1(d_ff_4_q), .in2(d_ff_5_q), .in3(d_ff_6_q), .out(\中断号 ), .gs(\中断信号 ));  // open: in0, en_out, en_in
  Multiplexer #(.select(1), .width(32), .disabled("Z"), .enable("false")) multiplexer_5 (
    .in0(bit_extender_1_out), .in1(bit_extender_2_out), .out(multiplexer_5_out), .sel(\单周期硬布线控制器_1_s_type ));
  assign bit_extender_3_out = {{20{IR[31]}}, {IR[31], IR[7], IR[30:25], IR[11:8]}};  // Bit_Extender bit_extender_3
  assign bit_extender_4_out = {{12{IR[31]}}, {IR[31], IR[19:12], IR[20], IR[30:21]}};  // Bit_Extender bit_extender_4
  or or_11 (IR3_t, IR3, IRC);
  Multiplexer #(.select(2), .width(32), .disabled("Z"), .enable("false")) multiplexer_6 (
    .in1(32'h30ac), .in2(32'h3150), .in3(32'h31f4), .out(INT_PC), .sel(\中断号 ));  // open: in0
  Shifter #(.width(32), .shift("ll")) shifter_1 (.in(bit_extender_3_out), .\dist (5'b00001), .out(shifter_1_out));
  Shifter #(.width(32), .shift("ll")) shifter_2 (.in(bit_extender_4_out), .\dist (5'b00001), .out(shifter_2_out));
  Button \u_总复位  (.out(RST));
  Decoder #(.select(2), .tristate("false"), .disabled("Z"), .enable("false")) decoder_1 (
    .out1(decoder_1_out1), .out2(decoder_1_out2), .out3(decoder_1_out3), .sel(now_q));  // open: out0
  Register #(.width(2), .trigger("rising"), .Select("low")) now (.D(\中断号 ), .en(INT), .Q(now_q), .clk(CLK), .clr(RST));
  Regifile regifile_1 (
    .Din(RDin), .Clk(CLK), .R1(R1), .R2(MDin), .WE(RegWrite), .W_num(IR[11:7]), .R1_num(multiplexer_3_out),
    .R2_num(multiplexer_4_out));
  Adder #(.width(32)) adder_2 (.a(shifter_1_out), .b(PC), .out(b));  // open: cin, cout
  Adder #(.width(32)) adder_3 (.a(shifter_2_out), .b(PC), .out(j));  // open: cin, cout
  Multiplexer #(.select(1), .width(32), .disabled("Z"), .enable("false")) multiplexer_7 (
    .in0(MDin), .in1(multiplexer_5_out), .out(multiplexer_7_out), .sel(\单周期硬布线控制器_1_alu_src ));
  and and_10 (Clr1, decoder_1_out1, URET);
  and and_11 (Clr2, decoder_1_out2, URET);
  and and_12 (Clr3, decoder_1_out3, URET);
  ALU alu_1 (
    .X(R1), .Y(multiplexer_7_out), .AluOP(\单周期硬布线控制器_1_alu_op ), .Equal(tunnel_t), .Result({R, Addr}),
    .out_4(tunnel_t_t), .out_6(tunnel));  // open: Result_2
  Register #(.width(32), .trigger("falling"), .Select("low")) mEPC (
    .D(\现场 ), .Q(RET_PC), .clk(INT), .clr(RST));  // open: en
  not not_3 (not_3_out, URET);
  Register #(.width(1), .trigger("rising"), .Select("low")) register_1 (
    .D(INT), .Q(register_1_q), .clk(CLK), .clr(RST));  // open: en
  D_Flip_Flop #(.trigger("rising"), .Pre_Clr_Positions("LEGACY"), .NegatePresetClear("false"), .enable("false"), .NewFFLayout("false")) d_ff_7 (
    .clk(not_3_out), .D(1'b0), .Qn(IE), .preset(register_1_q), .reset(RST));  // open: Q
  and and_13 (INT, IE, \中断信号 );
  or or_12 (or_12_out, JAL, JALR);
  RAM #(.addrWidth(10), .dataWidth(32), .bus("separate"), .Select("high")) ram_1 (
    .addr(R[11:2]), .din(MDin), .data(ram_1_data), .str(MemWrite), .sel(1'b1), .clk(CLK), .ld(1'b1), .clr(RST));
  Priority_Encoder #(.select(2), .disabled("Z")) priority_encoder_4 (
    .in0(1'b1), .in1(MemToReg), .in2(or_12_out), .out(priority_encoder_4_out));  // open: in3, gs, en_out, en_in
  Multiplexer #(.select(2), .width(32), .disabled("Z"), .enable("false")) multiplexer_8 (
    .in0({R, Addr}), .in1(ram_1_data), .in2(PC_4), .out(word), .sel(priority_encoder_4_out));  // open: in3
  assign bit_extender_5_out = {{24{word[7]}}, word[7:0]};  // Bit_Extender bit_extender_5
  assign bit_extender_6_out = {{24{word[15]}}, word[15:8]};  // Bit_Extender bit_extender_6
  assign bit_extender_7_out = {{24{word[23]}}, word[23:16]};  // Bit_Extender bit_extender_7
  assign bit_extender_8_out = {{24{word[31]}}, word[31:24]};  // Bit_Extender bit_extender_8
  Multiplexer #(.select(1), .width(32), .disabled("Z"), .enable("false")) multiplexer_9 (
    .in0(word), .in1(\byte ), .out(RDin), .sel(LB));
  Multiplexer #(.select(2), .width(32), .disabled("Z"), .enable("false")) multiplexer_10 (
    .in0(bit_extender_5_out), .in1(bit_extender_6_out), .in2(bit_extender_7_out), .in3(bit_extender_8_out),
    .out(\byte ), .sel(Addr));

  // Other names for the same wires on the sheet: R[1:0] = Addr

  // Notes on the sheet:
  //   中断源
  //   中断等待指示
  //   总复位信号应将除ROM以外所有存储组件全部清零
  //   单级中断测试信号模拟器
  //   数码管输出
  //   数码管输出应该用寄存器锁存，否则显示数据只能一闪而过
  //   指令探针
  //   指令存储器
  //   contents of rom_1 (hex, n*v repeats v):
  //   7d000113 100413 1f41993 41f9d993 433 c00913 800b13 140413 f47413 800293 100313 499993 89e9b3 1300533
  //   2200893 73 406282b3 fe0294e3 140413 f00f93 1f47433 1c41413 800293 100313 49d993 89e9b3 1300533
  //   2200893 73 406282b3 fe0294e3 1c45413 406b0b33 b0463 f95ff06f 2b3 fff2c293 1029293 fff2e293 500533
  //   2200893 73 f5dff06f 1112023 410113 a12023 410113 812023 410113 1312023 410113 1412023 410113 1512023
  //   410113 1612023 410113 100b13 300a13 100a93 1600433 441413 14469b3 1300533 2200893 73 fe0416e3
  //   415a0a33 fe0a10e3 ffc10113 12b03 ffc10113 12a83 ffc10113 12a03 ffc10113 12983 ffc10113 12403
  //   ffc10113 12503 ffc10113 12883 200073 1112023 410113 a12023 410113 812023 410113 1312023 410113
  //   1412023 410113 1512023 410113 1612023 410113 200b13 300a13 100a93 1600433 441413 14469b3 1300533
  //   2200893 73 fe0416e3 415a0a33 fe0a10e3 ffc10113 12b03 ffc10113 12a83 ffc10113 12a03 ffc10113 12983
  //   ffc10113 12403 ffc10113 12503 ffc10113 12883 200073 1112023 410113 a12023 410113 812023 410113
  //   1312023 410113 1412023 410113 1512023 410113 1612023 410113 300b13 300a13 100a93 1600433 441413
  //   14469b3 1300533 2200893 73 fe0416e3 415a0a33 fe0a10e3 ffc10113 12b03 ffc10113 12a83 ffc10113 12a03
  //   ffc10113 12983 ffc10113 12403 ffc10113 12503 ffc10113 12883 200073
  //   指令字
  //   JAL
  //   JALR
  //   URET
  //   Beq
  //   Bne
  //   MemToReg
  //   MemWrite
  //   AluOP
  //   AluSrcB
  //   RegWrite
  //   S_Type
  //   入口
  //   为方便自动评测，需要输出PC，IR，寄存器堆写如数据RDin
  //   返回清零
  //   RAM写使能MemWrite、RAM写入数据MDin等信号
  //   保存现场
  //   数据存储器
  //   中断请求
endmodule
module \多级自测  (
  input  IR1,
  input  IR2,
  input  IR3,
  output RegWrite,
  output MemWrite,
  output [31:0] PC,
  output [31:0] IR,
  output [31:0] RDin,
  output [31:0] MDin,
  output [31:0] LedData
);

  wire _1, _2, _3, and_1_out, and_2_out, and_3_out, and_4_out, and_5_out, and_7_out, and_8_out, and_9_out,
       and_15_out, and_16_out, and_17_out, and_18_out, and_19_out, and_20_out, Beq, BGE, Bne, Branch, CLK,
       Clr1, Clr2, Clr3, comparator_1_eq, comparator_2_eq, comparator_3_eq, comparator_4_eq, comparator_5_eq,
       comparator_6_eq, comparator_8_eq, CSRRCI, CSRRSI, d_ff_1_q, d_ff_2_q, d_ff_3_q, d_ff_4_qn, d_ff_5_q,
       d_ff_6_q, d_ff_7_q, decoder_1_out1, decoder_1_out2, ecall, Go, halt, IE, IE0, IE1, IE2, IE3, INT,
       IR1_t, IR2_t, IR3_t, IRA, IRB, IRC, JAL, JALR, LB, MemToReg, multiplexer_3_out, multiplexer_13_out,
       \new , not_1_out, not_2_out, not_3_out, or_1_out, or_2_out, or_8_out, or_9_out, or_10_out, or_13_out,
       or_14_out, or_15_out, or_16_out, or_17_out, register_3_q, register_4_q, register_5_q, RST, tunnel,
       tunnel_t, tunnel_t_t, URET, W1, W2, W3, \中断信号 , \单周期硬布线控制器_1_alu_src , \单周期硬布线控制器_1_s_type ;
  wire [1:0] Addr, last, multiplexer_6_out, multiplexer_9_out, multiplexer_11_out, now,
       priority_encoder_1_out, priority_encoder_2_out, priority_encoder_4_out, register_1_q, register_2_q,
       subtractor_1_out, \中断号 , \级数 ;
  wire [3:0] \单周期硬布线控制器_1_alu_op ;
  wire [4:0] multiplexer_4_out, multiplexer_5_out;
  wire [15:0] \总周期数 ;
  wire [31:0] b, bit_extender_1_out, bit_extender_2_out, bit_extender_3_out, bit_extender_4_out,
       bit_extender_5_out, bit_extender_6_out, bit_extender_7_out, bit_extender_8_out, \byte , INT_PC, j,
       mEPC1_q, mEPC2_q, mEPC_q, multiplexer_7_out, multiplexer_10_out, PC_4, R1, ram_1_data, RET_PC,
       shifter_1_out, shifter_2_out, word, \下 , \现场 ;
  wire [31:2] R;

  Clock #(.highDuration(1), .lowDuration(1)) clock_1 (.out(CLK));
  Button u__1 ();  // open: out
  Button u__2 ();  // open: out
  Button u__3 ();  // open: out
  Button \u_继续运行  (.out(Go));
  LED #(.active("true")) led_1 (.in(W1));
  LED #(.active("true")) led_2 (.in(W2));
  LED #(.active("true")) led_3 (.in(W3));
  Hex_Digit_Display hex_digit_display_1 (.value(LedData[31:28]));  // open: dp
  Comparator #(.width(16), .mode("twosComplement")) comparator_1 (
    .a(16'h258), .b(\总周期数 ), .eq(comparator_1_eq));  // open: gt, lt
  Comparator #(.width(16), .mode("twosComplement")) comparator_2 (
    .a(\总周期数 ), .b(16'h1), .eq(comparator_2_eq));  // open: gt, lt
  Comparator #(.width(16), .mode("twosComplement")) comparator_3 (
    .a(\总周期数 ), .b(16'h4), .eq(comparator_3_eq));  // open: gt, lt
  Comparator #(.width(16), .mode("twosComplement")) comparator_4 (
    .a(\总周期数 ), .b(16'h7), .eq(comparator_4_eq));  // open: gt, lt
  Comparator #(.width(16), .mode("twosComplement")) comparator_5 (
    .a(\总周期数 ), .b(16'h241), .eq(comparator_5_eq));  // open: gt, lt
  Comparator #(.width(32), .mode("twosComplement")) comparator_6 (
    .a(R1), .b(32'ha), .eq(comparator_6_eq));  // open: gt, lt
  Hex_Digit_Display hex_digit_display_2 (.value(LedData[27:24]));  // open: dp
  Hex_Digit_Display hex_digit_display_3 (.value(LedData[23:20]));  // open: dp
  or or_1 (or_1_out, comparator_1_eq, comparator_2_eq);
  assign IRA = or_1_out ? ~CLK : 1'bz;  // Controlled_Inverter controlled_inverter_1
  assign IRB = comparator_3_eq ? ~CLK : 1'bz;  // Controlled_Inverter controlled_inverter_2
  or or_2 (or_2_out, comparator_4_eq, comparator_5_eq);
  assign IRC = or_2_out ? ~CLK : 1'bz;  // Controlled_Inverter controlled_inverter_3
  and and_1 (and_1_out, Beq, tunnel_t);
  and and_2 (and_2_out, ~tunnel_t, Bne);  // AND_Gate
  or or_3 (Branch, and_1_out, and_2_out, and_3_out);
  and and_3 (and_3_out, tunnel_t_t, BGE);
  Priority_Encoder #(.select(2), .disabled("Z")) priority_encoder_1 (
    .in0(1'b1), .in1(Branch), .in2(JAL), .in3(JALR), .out(priority_encoder_1_out));  // open: gs, en_out, en_in
  Multiplexer #(.select(2), .width(32), .disabled("Z"), .enable("false")) multiplexer_1 (
    .in0(PC_4), .in1(b), .in2(j), .in3({R, Addr}), .out(\现场 ), .sel(priority_encoder_1_out));
  and and_4 (and_4_out, ecall, ~comparator_6_eq);  // AND_Gate
  and and_5 (and_5_out, ecall, comparator_6_eq);
  Hex_Digit_Display hex_digit_display_4 (.value(LedData[19:16]));  // open: dp
  Hex_Digit_Display hex_digit_display_5 (.value(LedData[15:12]));  // open: dp
  Pull_Resistor #(.pull(0)) pull_resistor_1 (.node(IRA));
  Pull_Resistor #(.pull(0)) pull_resistor_2 (.node(IRB));
  Pull_Resistor #(.pull(0)) pull_resistor_3 (.node(IRC));
  Multiplexer #(.select(2), .width(32), .disabled("Z"), .enable("false")) multiplexer_2 (
    .in0(\现场 ), .in1(RET_PC), .in2(INT_PC), .out(\下 ), .sel(priority_encoder_2_out));  // open: in3
  Priority_Encoder #(.select(2), .disabled("Z")) priority_encoder_2 (
    .in0(1'b1), .in1(URET), .in2(INT), .out(priority_encoder_2_out));  // open: in3, gs, en_out, en_in
  Register #(.width(32), .trigger("rising"), .Select("low")) u_PC (
    .D(MDin), .en(and_4_out), .Q(LedData), .clk(CLK));  // open: clr
  and and_6 (halt, and_5_out, ~Go);  // AND_Gate
  Hex_Digit_Display hex_digit_display_6 (.value(LedData[11:8]));  // open: dp
  Hex_Digit_Display hex_digit_display_7 (.value(LedData[7:4]));  // open: dp
  // Probe on \总周期数 
  Register #(.width(32), .trigger("rising"), .Select("low")) PC_2 (
    .D(\下 ), .en(not_1_out), .Q(PC), .clk(CLK), .clr(RST));
  not not_1 (not_1_out, halt);
  Hex_Digit_Display hex_digit_display_8 (.value(LedData[3:0]));  // open: dp
  or or_4 (W1, d_ff_5_q, d_ff_1_q);
  or or_5 (W2, d_ff_6_q, d_ff_2_q);
  or or_6 (W3, d_ff_7_q, d_ff_3_q);
  not not_2 (not_2_out, halt);
  // Probe on PC
  D_Flip_Flop #(.trigger("rising"), .Pre_Clr_Positions("LEGACY"), .NegatePresetClear("false"), .enable("false"), .NewFFLayout("false")) d_ff_1 (
    .clk(IR1_t), .D(1'b1), .Q(d_ff_1_q), .reset(d_ff_5_q));  // open: Qn, preset
  D_Flip_Flop #(.trigger("rising"), .Pre_Clr_Positions("LEGACY"), .NegatePresetClear("false"), .enable("false"), .NewFFLayout("false")) d_ff_2 (
    .clk(IR2_t), .D(1'b1), .Q(d_ff_2_q), .reset(d_ff_6_q));  // open: Qn, preset
  D_Flip_Flop #(.trigger("rising"), .Pre_Clr_Positions("LEGACY"), .NegatePresetClear("false"), .enable("false"), .NewFFLayout("false")) d_ff_3 (
    .clk(IR3_t), .D(1'b1), .Q(d_ff_3_q), .reset(d_ff_7_q));  // open: Qn, preset
  Counter #(.width(2), .max('h3), .ongoal("wrap"), .trigger("falling"), .behavior("old")) counter_1 (
    .load(URET), .Q(\级数 ), .clk(multiplexer_3_out), .clr(RST));  // open: D, count, carry, preset
  Multiplexer #(.select(1), .width(1), .disabled("Z"), .enable("false")) multiplexer_3 (
    .in0(\new ), .in1(d_ff_4_qn), .out(multiplexer_3_out), .sel(URET));
  D_Flip_Flop #(.trigger("falling"), .Pre_Clr_Positions("LEGACY"), .NegatePresetClear("false"), .enable("false"), .NewFFLayout("false")) d_ff_4 (
    .clk(CLK), .D(URET), .Qn(d_ff_4_qn));  // open: Q, preset, reset
  // RiscV_Probe riscv_probe_1: pin names not known; wires that end beside it: IR
  Adder #(.width(32)) adder_1 (.a(PC), .b(32'h4), .out(PC_4));  // open: cin, cout
  Counter #(.width(16), .max('hffff), .ongoal("stay"), .trigger("rising"), .behavior("old")) counter_2 (
    .count(not_2_out), .Q(\总周期数 ), .clk(CLK), .clr(RST));  // open: load, D, carry, preset
  or or_7 (IR1_t, IR1, IRA);
  or or_8 (or_8_out, d_ff_1_q, d_ff_5_q);
  or or_9 (or_9_out, d_ff_2_q, d_ff_6_q);
  or or_10 (or_10_out, d_ff_3_q, d_ff_7_q);
  Decoder #(.select(2), .tristate("false"), .disabled("Z"), .enable("false")) decoder_1 (
    .out1(decoder_1_out1), .out2(decoder_1_out2), .sel(\级数 ));  // open: out0, out3
  ROM #(.addrWidth(10), .dataWidth(32), .Select("high")) rom_1 (.addr(PC[11:2]), .data(IR));
  or or_11 (IR2_t, IR2, IRB);
  // Probe on \下 
  and and_7 (and_7_out, or_8_out, ~Clr1);  // AND_Gate
  and and_8 (and_8_out, or_9_out, ~Clr2);  // AND_Gate
  and and_9 (and_9_out, or_10_out, ~Clr3);  // AND_Gate
  Register #(.width(2), .trigger("falling"), .Select("low")) register_1 (
    .D(now), .en(decoder_1_out1), .Q(register_1_q), .clk(CLK), .clr(RST));
  Register #(.width(2), .trigger("falling"), .Select("low")) register_2 (
    .D(now), .en(decoder_1_out2), .Q(register_2_q), .clk(CLK), .clr(RST));
  D_Flip_Flop #(.trigger("rising"), .Pre_Clr_Positions("LEGACY"), .NegatePresetClear("false"), .enable("false"), .NewFFLayout("false")) d_ff_5 (
    .clk(CLK), .D(and_7_out), .Q(d_ff_5_q), .reset(RST));  // open: Qn, preset
  D_Flip_Flop #(.trigger("rising"), .Pre_Clr_Positions("LEGACY"), .NegatePresetClear("false"), .enable("false"), .NewFFLayout("false")) d_ff_6 (
    .clk(CLK), .D(and_8_out), .Q(d_ff_6_q), .reset(RST));  // open: Qn, preset
  D_Flip_Flop #(.trigger("rising"), .Pre_Clr_Positions("LEGACY"), .NegatePresetClear("false"), .enable("false"), .NewFFLayout("false")) d_ff_7 (
    .clk(CLK), .D(and_9_out), .Q(d_ff_7_q), .reset(RST));  // open: Qn, preset
  Subtractor #(.width(2)) subtractor_1 (.a(\级数 ), .b(2'b01), .out(subtractor_1_out));  // open: bin, bout
  \单周期硬布线控制器  \u_单周期硬布线控制器_1  (
    .Funct({IR[30], IR[25], IR[14:12]}), .OP(IR[6:2]), .ALU_OP(\单周期硬布线控制器_1_alu_op ), .MemToReg(MemToReg),
    .MemWrite(MemWrite), .ALU_SRC(\单周期硬布线控制器_1_alu_src ), .RegWrite(RegWrite), .ecall(ecall),
    .S_type(\单周期硬布线控制器_1_s_type ), .Jalr(JALR), .Beq(Beq), .JAL(JAL), .Bne(Bne), .in_3(IR[21]), .uret(URET),
    .LB(LB), .BGE(BGE), .CSRRSI(CSRRSI), .CSRRCI(CSRRCI));
  Multiplexer #(.select(1), .width(5), .disabled("Z"), .enable("false")) multiplexer_4 (
    .in0(IR[19:15]), .in1(5'b10001), .out(multiplexer_4_out), .sel(ecall));
  Multiplexer #(.select(1), .width(5), .disabled("Z"), .enable("false")) multiplexer_5 (
    .in0(IR[24:20]), .in1(5'b01010), .out(multiplexer_5_out), .sel(ecall));
  assign bit_extender_1_out = {{20{IR[31]}}, IR[31:20]};  // Bit_Extender bit_extender_1
  assign bit_extender_2_out = {{20{IR[31]}}, {IR[31:25], IR[11:7]}};  // Bit_Extender bit_extender_2
  assign bit_extender_3_out = {{20{IR[31]}}, {IR[31], IR[7], IR[30:25], IR[11:8]}};  // Bit_Extender bit_extender_3
  assign bit_extender_4_out = {{12{IR[31]}}, {IR[31], IR[19:12], IR[20], IR[30:21]}};  // Bit_Extender bit_extender_4
  or or_12 (IR3_t, IR3, IRC);
  Priority_Encoder #(.select(2), .disabled("Z")) priority_encoder_3 (
    .in1(d_ff_5_q), .in2(d_ff_6_q), .in3(d_ff_7_q), .out(\中断号 ), .gs(\中断信号 ));  // open: in0, en_out, en_in
  Multiplexer #(.select(2), .width(2), .disabled("Z"), .enable("false")) multiplexer_6 (
    .in0(2'b00), .in1(register_1_q), .in2(register_2_q), .out(multiplexer_6_out), .sel(subtractor_1_out));  // open: in3
  Register #(.width(2), .trigger("rising"), .Select("low")) u_last (
    .D(multiplexer_6_out), .Q(last), .clk(CLK), .clr(RST));  // open: en
  Multiplexer #(.select(1), .width(32), .disabled("Z"), .enable("false")) multiplexer_7 (
    .in0(bit_extender_1_out), .in1(bit_extender_2_out), .out(multiplexer_7_out), .sel(\单周期硬布线控制器_1_s_type ));
  Shifter #(.width(32), .shift("ll")) shifter_1 (.in(bit_extender_3_out), .\dist (5'b00001), .out(shifter_1_out));
  Shifter #(.width(32), .shift("ll")) shifter_2 (.in(bit_extender_4_out), .\dist (5'b00001), .out(shifter_2_out));
  Button \u_总复位  (.out(RST));
  Multiplexer #(.select(2), .width(32), .disabled("Z"), .enable("false")) multiplexer_8 (
    .in1(32'h30ac), .in2(32'h3158), .in3(32'h3204), .out(INT_PC), .sel(\中断号 ));  // open: in0
  Regifile regifile_1 (
    .Din(RDin), .Clk(CLK), .R1(R1), .R2(MDin), .WE(RegWrite), .W_num(IR[11:7]), .R1_num(multiplexer_4_out),
    .R2_num(multiplexer_5_out));
  Adder #(.width(32)) adder_2 (.a(shifter_1_out), .b(PC), .out(b));  // open: cin, cout
  Adder #(.width(32)) adder_3 (.a(shifter_2_out), .b(PC), .out(j));  // open: cin, cout
  Comparator #(.width(2), .mode("unsigned")) comparator_7 (.a(\中断号 ), .b(now), .gt(\new ));  // open: eq, lt
  Multiplexer #(.select(1), .width(2), .disabled("Z"), .enable("false")) multiplexer_9 (
    .in0(now), .in1(\中断号 ), .out(multiplexer_9_out), .sel(\new ));
  Multiplexer #(.select(1), .width(32), .disabled("Z"), .enable("false")) multiplexer_10 (
    .in0(MDin), .in1(multiplexer_7_out), .out(multiplexer_10_out), .sel(\单周期硬布线控制器_1_alu_src ));
  Multiplexer #(.select(1), .width(2), .disabled("Z"), .enable("false")) multiplexer_11 (
    .in0(multiplexer_9_out), .in1(last), .out(multiplexer_11_out), .sel(URET));
  or or_13 (or_13_out, URET, INT);
  Register #(.width(32), .trigger("falling"), .Select("low")) mEPC (
    .D(\现场 ), .en(_1), .Q(mEPC_q), .clk(INT), .clr(RST));
  Register #(.width(32), .trigger("falling"), .Select("low")) mEPC1 (
    .D(\现场 ), .en(_2), .Q(mEPC1_q), .clk(INT), .clr(RST));
  Register #(.width(32), .trigger("falling"), .Select("low")) mEPC2 (
    .D(\现场 ), .en(_3), .Q(mEPC2_q), .clk(INT), .clr(RST));
  ALU alu_1 (
    .X(R1), .Y(multiplexer_10_out), .AluOP(\单周期硬布线控制器_1_alu_op ), .Equal(tunnel_t), .Result({R, Addr}),
    .out_4(tunnel_t_t), .out_6(tunnel));  // open: Result_2
  Register #(.width(2), .trigger("rising"), .Select("low")) u_now (
    .D(multiplexer_11_out), .en(or_13_out), .Q(now), .clk(CLK), .clr(RST));
  Multiplexer #(.select(2), .width(32), .disabled("Z"), .enable("false")) multiplexer_12 (
    .in1(mEPC_q), .in2(mEPC1_q), .in3(mEPC2_q), .out(RET_PC), .sel(now));  // open: in0
  Decoder #(.select(2), .tristate("false"), .disabled("Z"), .enable("false")) decoder_2 (
    .out1(_1), .out2(_2), .out3(_3), .sel(now));  // open: out0
  or or_14 (or_14_out, JAL, JALR);
  RAM #(.addrWidth(10), .dataWidth(32), .bus("separate"), .Select("high")) ram_1 (
    .addr(R[11:2]), .din(MDin), .data(ram_1_data), .str(MemWrite), .sel(1'b1), .clk(CLK), .ld(1'b1), .clr(RST));
  Multiplexer #(.select(2), .width(1), .disabled("Z"), .enable("false")) multiplexer_13 (
    .in0(IE0), .in1(IE1), .in2(IE2), .in3(IE3), .out(multiplexer_13_out), .sel(now));
  Comparator #(.width(2), .mode("unsigned")) comparator_8 (.a(\中断号 ), .b(now), .eq(comparator_8_eq));  // open: gt, lt
  and and_10 (INT, IE, \中断信号 );
  Priority_Encoder #(.select(2), .disabled("Z")) priority_encoder_4 (
    .in0(1'b1), .in1(MemToReg), .in2(or_14_out), .out(priority_encoder_4_out));  // open: in3, gs, en_out, en_in
  Multiplexer #(.select(2), .width(32), .disabled("Z"), .enable("false")) multiplexer_14 (
    .in0({R, Addr}), .in1(ram_1_data), .in2(PC_4), .out(word), .sel(priority_encoder_4_out));  // open: in3
  and and_11 (Clr1, _1, URET);
  and and_12 (Clr2, _2, URET);
  and and_13 (Clr3, _3, URET);
  and and_14 (IE, multiplexer_13_out, ~comparator_8_eq);  // AND_Gate
  assign bit_extender_5_out = {{24{word[7]}}, word[7:0]};  // Bit_Extender bit_extender_5
  assign bit_extender_6_out = {{24{word[15]}}, word[15:8]};  // Bit_Extender bit_extender_6
  assign bit_extender_7_out = {{24{word[23]}}, word[23:16]};  // Bit_Extender bit_extender_7
  assign bit_extender_8_out = {{24{word[31]}}, word[31:24]};  // Bit_Extender bit_extender_8
  Multiplexer #(.select(1), .width(32), .disabled("Z"), .enable("false")) multiplexer_15 (
    .in0(word), .in1(\byte ), .out(RDin), .sel(LB));
  Multiplexer #(.select(2), .width(32), .disabled("Z"), .enable("false")) multiplexer_16 (
    .in0(bit_extender_5_out), .in1(bit_extender_6_out), .in2(bit_extender_7_out), .in3(bit_extender_8_out),
    .out(\byte ), .sel(Addr));
  Register #(.width(1), .trigger("rising"), .Select("low")) register_3 (
    .D(CSRRSI), .Q(register_3_q), .clk(CLK));  // open: en, clr
  Register #(.width(1), .trigger("rising"), .Select("low")) register_4 (
    .D(CSRRCI), .Q(register_4_q), .clk(CLK));  // open: en, clr
  not not_3 (not_3_out, URET);
  Register #(.width(1), .trigger("rising"), .Select("low")) register_5 (
    .D(INT), .Q(register_5_q), .clk(CLK), .clr(RST));  // open: en
  and and_15 (and_15_out, register_3_q, _1);
  and and_16 (and_16_out, register_4_q, _1);
  and and_17 (and_17_out, register_3_q, _2);
  and and_18 (and_18_out, register_4_q, _2);
  and and_19 (and_19_out, register_3_q, _3);
  and and_20 (and_20_out, register_4_q, _3);
  D_Flip_Flop #(.trigger("rising"), .Pre_Clr_Positions("LEGACY"), .NegatePresetClear("false"), .enable("false"), .NewFFLayout("false")) d_ff_8 (
    .clk(not_3_out), .D(1'b0), .Qn(IE0), .preset(register_5_q), .reset(RST));  // open: Q
  D_Flip_Flop #(.trigger("rising"), .Pre_Clr_Positions("LEGACY"), .NegatePresetClear("false"), .enable("false"), .NewFFLayout("false")) d_ff_9 (
    .Q(IE1), .preset(and_15_out), .reset(or_15_out));  // open: clk, D, Qn
  or or_15 (or_15_out, and_16_out, RST);
  D_Flip_Flop #(.trigger("rising"), .Pre_Clr_Positions("LEGACY"), .NegatePresetClear("false"), .enable("false"), .NewFFLayout("false")) d_ff_10 (
    .Q(IE2), .preset(and_17_out), .reset(or_16_out));  // open: clk, D, Qn
  or or_16 (or_16_out, and_18_out, RST);
  D_Flip_Flop #(.trigger("rising"), .Pre_Clr_Positions("LEGACY"), .NegatePresetClear("false"), .enable("false"), .NewFFLayout("false")) d_ff_11 (
    .Q(IE3), .preset(and_19_out), .reset(or_17_out));  // open: clk, D, Qn
  or or_17 (or_17_out, and_20_out, RST);

  // Other names for the same wires on the sheet: R[1:0] = Addr

  // Notes on the sheet:
  //   中断源
  //   中断等待指示
  //   总复位信号应将除ROM以外所有存储组件全部清零
  //   多级中断测试信号模拟器
  //   数码管输出
  //   数码管输出应该用寄存器锁存，否则显示数据只能一闪而过
  //   指令探针
  //   指令存储器
  //   指令字
  //   contents of rom_1 (hex, n*v repeats v):
  //   7d000113 100413 1f41993 41f9d993 433 c00913 800b13 140413 f47413 800293 100313 499993 89e9b3 1300533
  //   2200893 73 406282b3 fe0294e3 140413 f00f93 1f47433 1c41413 800293 100313 49d993 89e9b3 1300533
  //   2200893 73 406282b3 fe0294e3 1c45413 406b0b33 b0463 f95ff06f 2b3 fff2c293 1029293 fff2e293 500533
  //   2200893 73 f5dff06f 1112023 410113 a12023 410113 812023 410113 1312023 410113 1412023 410113 1512023
  //   410113 1612023 410113 40e073 100b13 300a13 100a93 1600433 441413 14469b3 1300533 2200893 73 fe0416e3
  //   415a0a33 fe0a10e3 40f073 ffc10113 12b03 ffc10113 12a83 ffc10113 12a03 ffc10113 12983 ffc10113 12403
  //   ffc10113 12503 ffc10113 12883 200073 1112023 410113 a12023 410113 812023 410113 1312023 410113
  //   1412023 410113 1512023 410113 1612023 410113 40e073 200b13 300a13 100a93 1600433 441413 14469b3
  //   1300533 2200893 73 fe0416e3 415a0a33 fe0a10e3 40f073 ffc10113 12b03 ffc10113 12a83 ffc10113 12a03
  //   ffc10113 12983 ffc10113 12403 ffc10113 12503 ffc10113 12883 200073 1112023 410113 a12023 410113
  //   812023 410113 1312023 410113 1412023 410113 1512023 410113 1612023 410113 40e073 300b13 300a13
  //   100a93 1600433 441413 14469b3 1300533 2200893 73 fe0416e3 415a0a33 fe0a10e3 40f073 ffc10113 12b03
  //   ffc10113 12a83 ffc10113 12a03 ffc10113 12983 ffc10113 12403 ffc10113 12503 ffc10113 12883 200073
  //   保存上一级中断号
  //   JAL
  //   JALR
  //   URET
  //   Beq
  //   Bne
  //   MemToReg
  //   MemWrite
  //   AluOP
  //   AluSrcB
  //   RegWrite
  //   S_Type
  //   入口
  //   为方便自动评测，需要输出PC，IR，寄存器堆写如数据RDin
  //   保存现场
  //   RAM写使能MemWrite、RAM写入数据MDin等信号
  //   中断请求
  //   数据存储器
  //   返回清零
endmodule

module \重定向流水线_单级中断  (
  input  IR1,
  input  IR2,
  input  IR3,
  output RegWrite,
  output MemWrite,
  output [31:0] IF_PC,
  output [31:0] ID_PC,
  output [31:0] EX_PC,
  output [31:0] M_PC,
  output [31:0] WB_PC,
  output [31:0] RDin,
  output [31:0] MDin,
  output [31:0] LedData
);

  wire _1_out, _2_out, _3_out, and_1_out, and_2_out, and_3_out, and_5_out, and_6_out, and_7_out, and_8_out,
       and_9_out, and_10_out, and_11_out, and_15_out, Beq, BGE, Bne, Branch, BranchTaken, CLK, clock_1_out,
       clock_2_out, Clr1, Clr2, Clr3, comparator_1_eq, comparator_2_eq, comparator_3_eq, comparator_4_eq,
       comparator_5_eq, comparator_6_eq, comparator_7_eq, comparator_7_lt, comparator_8_eq, comparator_9_eq,
       comparator_10_eq, counter_6_q, d_ff_1_q, d_ff_2_q, d_ff_3_q, d_ff_4_q, d_ff_5_q, d_ff_6_q, d_ff_7_q,
       decoder_1_out1, decoder_1_out2, decoder_1_out3, EX_ecall, ex_mem_1_jal_2, ex_mem_1_jalr_2,
       ex_mem_1_lb_2, ex_mem_1_memtoreg_2, EX_MemToReg, EX_RegWrite, EX_RST, EX_URET, flush, Go, halt,
       ID_ecall, id_ex_1_alusrcb_2, id_ex_1_lb_2, id_ex_1_memwrite_2, ID_URET, IE, IF_URET, INT, IR1_t,
       IR2_t, IR3_t, IRA, IRB, IRC, JAL, JALR, LB, MEM_ecall, MEM_RegWrite, MemToReg, nand_1_out, not_2_out,
       not_3_out, not_4_out, not_5_out, not_6_out, or_3_out, or_9_out, or_10_out, or_11_out, or_12_out,
       or_13_out, or_14_out, register_2_q, RST, stall, tunnel, tunnel_t, tunnel_t_t, W1, W2, W3, WB_ecall,
       WB_JAL, WB_JALR, \中断信号 , \单周期硬布线控制器_1_alu_src , \单周期硬布线控制器_1_beq , \单周期硬布线控制器_1_bge ,
       \单周期硬布线控制器_1_bne , \单周期硬布线控制器_1_jal , \单周期硬布线控制器_1_jalr , \单周期硬布线控制器_1_lb , \单周期硬布线控制器_1_memtoreg ,
       \单周期硬布线控制器_1_memwrite , \单周期硬布线控制器_1_regwrite , \单周期硬布线控制器_1_s_type ;
  wire [1:0] Addr, id_ex_1_rs1forward_2, id_ex_1_rs2forward_2, priority_encoder_1_out,
       priority_encoder_2_out, priority_encoder_4_out, register_1_q, rs1Fwd, rs2Fwd, \中断号 ;
  wire [3:0] id_ex_1_aluop_2, \单周期硬布线控制器_1_alu_op ;
  wire [4:0] EX_rd, MEM_rd, multiplexer_3_out, multiplexer_4_out, WB_rd;
  wire [12:0] CNT_num;
  wire [15:0] \LoadUse次数 , \总周期数 , \插入气泡数 , \无条件分支数 , \条件分支成功数 ;
  wire [31:0] b, bit_extender_1_out, bit_extender_2_out, bit_extender_3_out, bit_extender_4_out,
       bit_extender_5_out, bit_extender_6_out, bit_extender_7_out, bit_extender_8_out, \byte , EX_IR,
       ex_mem_1_pc_4_2, EX_R1, EX_R2, id_ex_1_imm_2, id_ex_1_imm_b_2, id_ex_1_imm_j_2, id_ex_1_pc_4_2,
       id_ex_1_r1_2, id_ex_1_r2_2, ID_IR, if_id_1_pc_4_2, IF_IR, IF_PC_4, INT_PC, j, MEM_IR, MEM_R, MEM_R1,
       mem_wb_1_dataout_2, mem_wb_1_r_2, multiplexer_1_out, multiplexer_2_out, multiplexer_6_out,
       multiplexer_9_out, R, ram_1_data, regifile_falling_edge_1_r1, regifile_falling_edge_1_r2, RET_PC,
       shifter_1_out, shifter_2_out, WB_IR, WB_PC_4, WB_R1, WB_R2, word;

  Button \u_总复位  (.out(RST));
  Button _1 (.out(_1_out));
  Button _2 (.out(_2_out));
  Button _3 (.out(_3_out));
  // Probe on \总周期数 
  // Probe on \总周期数 
  Button \u_继续运行  (.out(Go));
  LED #(.active("true")) led_1 (.in(W1));
  LED #(.active("true")) led_2 (.in(W2));
  LED #(.active("true")) led_3 (.in(W3));
  or or_1 (IR1_t, IR1, IRA);
  Hex_Digit_Display hex_digit_display_1 (.value(LedData[31:28]));  // open: dp
  // Probe on IF_PC[19:0]
  // RiscV_Probe riscv_probe_1: pin names not known; wires that end beside it: _1_out, _2_out, _3_out, IR1_t, IR2_t, IR3_t, IF_IR
  or or_2 (IR2_t, IR2, IRB);
  Comparator #(.width(16), .mode("twosComplement")) comparator_1 (
    .a(16'h23b), .b(\总周期数 ), .eq(comparator_1_eq));  // open: gt, lt
  Comparator #(.width(16), .mode("twosComplement")) comparator_2 (
    .a(\总周期数 ), .b(16'h1), .eq(comparator_2_eq));  // open: gt, lt
  Comparator #(.width(16), .mode("twosComplement")) comparator_3 (
    .a(\总周期数 ), .b(16'h4), .eq(comparator_3_eq));  // open: gt, lt
  Comparator #(.width(16), .mode("twosComplement")) comparator_4 (
    .a(\总周期数 ), .b(16'h7), .eq(comparator_4_eq));  // open: gt, lt
  Comparator #(.width(32), .mode("twosComplement")) comparator_5 (
    .a(WB_R1), .b(32'ha), .eq(comparator_5_eq));  // open: gt, lt
  Priority_Encoder #(.select(2), .disabled("Z")) priority_encoder_1 (
    .in0(1'b1), .in1(Branch), .in2(JAL), .in3(JALR), .out(priority_encoder_1_out));  // open: gs, en_out, en_in
  Hex_Digit_Display hex_digit_display_2 (.value(LedData[27:24]));  // open: dp
  Hex_Digit_Display hex_digit_display_3 (.value(LedData[23:20]));  // open: dp
  // Probe on ID_PC[19:0]
  // RiscV_Probe riscv_probe_2: pin names not known; wires that end beside it: ID_IR
  or or_3 (or_3_out, comparator_1_eq, comparator_2_eq);
  assign IRA = or_3_out ? ~CLK : 1'bz;  // Controlled_Inverter controlled_inverter_1
  assign IRB = comparator_3_eq ? ~CLK : 1'bz;  // Controlled_Inverter controlled_inverter_2
  assign IRC = comparator_4_eq ? ~CLK : 1'bz;  // Controlled_Inverter controlled_inverter_3
  \重定向  \u_重定向_1  (
    .in_1(EX_rd), .in_3(MEM_rd), .in_4(EX_RegWrite), .in_5(MEM_RegWrite), .in_7(ID_ecall), .out_9(rs1Fwd),
    .out_10(rs2Fwd), .stall(stall), .BranchTaken(BranchTaken), .in_2(ID_IR), .in_6(EX_MemToReg), .flush(flush));
  and and_1 (and_1_out, WB_ecall, ~comparator_5_eq);  // AND_Gate
  and and_2 (and_2_out, WB_ecall, comparator_5_eq);
  Comparator #(.width(2), .mode("twosComplement")) comparator_6 (
    .a(2'b00), .b(priority_encoder_1_out), .eq(comparator_6_eq));  // open: gt, lt
  Multiplexer #(.select(2), .width(32), .disabled("Z"), .enable("false")) multiplexer_1 (
    .in0(IF_PC_4), .in1(b), .in2(j), .in3(R), .out(multiplexer_1_out), .sel(priority_encoder_1_out));
  Priority_Encoder #(.select(2), .disabled("Z")) priority_encoder_2 (
    .in0(1'b1), .in1(IF_URET), .in2(INT), .out(priority_encoder_2_out));  // open: in3, gs, en_out, en_in
  Hex_Digit_Display hex_digit_display_4 (.value(LedData[19:16]));  // open: dp
  Hex_Digit_Display hex_digit_display_5 (.value(LedData[15:12]));  // open: dp
  or or_4 (IR3_t, IR3, IRC);
  Pull_Resistor #(.pull(0)) pull_resistor_1 (.node(IRA));
  Pull_Resistor #(.pull(0)) pull_resistor_2 (.node(IRB));
  Pull_Resistor #(.pull(0)) pull_resistor_3 (.node(IRC));
  Register #(.width(32), .trigger("rising"), .Select("low")) PC (
    .D(WB_R2), .en(and_1_out), .Q(LedData), .clk(CLK));  // open: clr
  not not_1 (BranchTaken, comparator_6_eq);
  Multiplexer #(.select(2), .width(32), .disabled("Z"), .enable("false")) multiplexer_2 (
    .in0(multiplexer_1_out), .in1(RET_PC), .in2(INT_PC), .out(multiplexer_2_out), .sel(priority_encoder_2_out));  // open: in3
  and and_3 (and_3_out, ~stall, not_2_out);  // AND_Gate
  not not_2 (not_2_out, halt);
  Hex_Digit_Display hex_digit_display_6 (.value(LedData[7:4]));  // open: dp
  Hex_Digit_Display hex_digit_display_7 (.value(LedData[11:8]));  // open: dp
  Clock #(.highDuration(1), .lowDuration(1)) clock_1 (.out(clock_1_out));
  // Probe on EX_PC[19:0]
  // RiscV_Probe riscv_probe_3: pin names not known; wires that end beside it: clock_1_out, EX_IR, CLK
  and and_4 (halt, and_2_out, ~Go);  // AND_Gate
  Register #(.width(32), .trigger("rising"), .Select("low")) PC_2 (
    .D(multiplexer_2_out), .en(and_3_out), .Q(IF_PC), .clk(CLK), .clr(RST));
  Hex_Digit_Display hex_digit_display_8 (.value(LedData[3:0]));  // open: dp
  or or_5 (W1, d_ff_4_q, d_ff_1_q);
  or or_6 (W2, d_ff_5_q, d_ff_2_q);
  or or_7 (W3, d_ff_6_q, d_ff_3_q);
  not not_3 (not_3_out, halt);
  // Probe on \总周期数 
  // Probe on M_PC[19:0]
  // RiscV_Probe riscv_probe_4: pin names not known; wires that end beside it: MEM_IR
  D_Flip_Flop #(.trigger("rising"), .Pre_Clr_Positions("LEGACY"), .NegatePresetClear("false"), .enable("false"), .NewFFLayout("false")) d_ff_1 (
    .clk(IR1_t), .D(1'b1), .Q(d_ff_1_q), .reset(d_ff_4_q));  // open: Qn, preset
  D_Flip_Flop #(.trigger("rising"), .Pre_Clr_Positions("LEGACY"), .NegatePresetClear("false"), .enable("false"), .NewFFLayout("false")) d_ff_2 (
    .clk(IR2_t), .D(1'b1), .Q(d_ff_2_q), .reset(d_ff_5_q));  // open: Qn, preset
  D_Flip_Flop #(.trigger("rising"), .Pre_Clr_Positions("LEGACY"), .NegatePresetClear("false"), .enable("false"), .NewFFLayout("false")) d_ff_3 (
    .clk(IR3_t), .D(1'b1), .Q(d_ff_3_q), .reset(d_ff_6_q));  // open: Qn, preset
  and and_5 (and_5_out, Beq, tunnel_t);
  and and_6 (and_6_out, ~tunnel_t, Bne);  // AND_Gate
  or or_8 (Branch, and_5_out, and_6_out, and_7_out);
  and and_7 (and_7_out, tunnel_t_t, BGE);
  Counter #(.width(16), .max('hffff), .ongoal("stay"), .trigger("rising"), .behavior("old")) counter_1 (
    .count(not_3_out), .Q(\总周期数 ), .clk(CLK), .clr(RST));  // open: load, D, carry, preset
  Adder #(.width(32)) adder_1 (.a(IF_PC), .b(32'h4), .out(IF_PC_4));  // open: cin, cout
  // Probe on \总周期数 
  // Probe on \无条件分支数 
  // Probe on \条件分支成功数 
  // Probe on \插入气泡数 
  // Probe on \LoadUse次数 
  or or_9 (or_9_out, d_ff_1_q, d_ff_4_q);
  or or_10 (or_10_out, d_ff_2_q, d_ff_5_q);
  or or_11 (or_11_out, d_ff_3_q, d_ff_6_q);
  ROM #(.addrWidth(10), .dataWidth(32), .Select("high")) rom_1 (.addr(IF_PC[11:2]), .data(IF_IR));
  // Probe on IF_PC[11:0]
  // Probe on WB_PC[19:0]
  // RiscV_Probe riscv_probe_5: pin names not known; wires that end beside it: WB_IR
  and and_8 (and_8_out, or_9_out, ~Clr1);  // AND_Gate
  and and_9 (and_9_out, or_10_out, ~Clr2);  // AND_Gate
  and and_10 (and_10_out, or_11_out, ~Clr3);  // AND_Gate
  // RiscV_Probe riscv_probe_6: pin names not known; wires that end beside it: IF_IR
  IF__ID if_id_1 (
    .IR(IF_IR), .PC(IF_PC), .PC_4(IF_PC_4), .IR_2(ID_IR), .PC_2(ID_PC), .PC_4_2(if_id_1_pc_4_2), .RST(RST),
    .CLK(CLK), .en(and_11_out), .BranchTaken(BranchTaken));  // open: PredictJump, PredictJump_2
  and and_11 (and_11_out, ~stall, not_4_out);  // AND_Gate
  not not_4 (not_4_out, halt);
  // Probe on ID_PC[11:0]
  // Probe on EX_PC[11:0]
  D_Flip_Flop #(.trigger("rising"), .Pre_Clr_Positions("LEGACY"), .NegatePresetClear("false"), .enable("false"), .NewFFLayout("false")) d_ff_4 (
    .clk(CLK), .D(and_8_out), .Q(d_ff_4_q), .reset(RST));  // open: Qn, preset
  D_Flip_Flop #(.trigger("rising"), .Pre_Clr_Positions("LEGACY"), .NegatePresetClear("false"), .enable("false"), .NewFFLayout("false")) d_ff_5 (
    .clk(CLK), .D(and_9_out), .Q(d_ff_5_q), .reset(RST));  // open: Qn, preset
  D_Flip_Flop #(.trigger("rising"), .Pre_Clr_Positions("LEGACY"), .NegatePresetClear("false"), .enable("false"), .NewFFLayout("false")) d_ff_6 (
    .clk(CLK), .D(and_10_out), .Q(d_ff_6_q), .reset(RST));  // open: Qn, preset
  // Probe on M_PC[11:0]
  D_Flip_Flop #(.trigger("high"), .Pre_Clr_Positions("LEGACY"), .NegatePresetClear("false"), .enable("true"), .NewFFLayout("false")) d_ff_7 (.Q(d_ff_7_q));  // open: clk, D, Qn, preset, en, reset
  // Probe on 13'hc
  Priority_Encoder #(.select(2), .disabled("Z")) priority_encoder_3 (
    .in1(d_ff_4_q), .in2(d_ff_5_q), .in3(d_ff_6_q), .out(\中断号 ), .gs(\中断信号 ));  // open: in0, en_out, en_in
  \单周期硬布线控制器  \u_单周期硬布线控制器_1  (
    .Funct({ID_IR[30], ID_IR[25], ID_IR[14:12]}), .OP(ID_IR[6:2]), .ALU_OP(\单周期硬布线控制器_1_alu_op ),
    .MemToReg(\单周期硬布线控制器_1_memtoreg ), .MemWrite(\单周期硬布线控制器_1_memwrite ), .ALU_SRC(\单周期硬布线控制器_1_alu_src ),
    .RegWrite(\单周期硬布线控制器_1_regwrite ), .ecall(ID_ecall), .S_type(\单周期硬布线控制器_1_s_type ),
    .Jalr(\单周期硬布线控制器_1_jalr ), .Beq(\单周期硬布线控制器_1_beq ), .JAL(\单周期硬布线控制器_1_jal ), .Bne(\单周期硬布线控制器_1_bne ),
    .in_3(ID_IR[21]), .uret(ID_URET), .LB(\单周期硬布线控制器_1_lb ), .BGE(\单周期硬布线控制器_1_bge ));  // open: CSRRSI, CSRRCI
  Multiplexer #(.select(1), .width(5), .disabled("Z"), .enable("false")) multiplexer_3 (
    .in0(ID_IR[19:15]), .in1(5'b10001), .out(multiplexer_3_out), .sel(ID_ecall));
  Multiplexer #(.select(1), .width(5), .disabled("Z"), .enable("false")) multiplexer_4 (
    .in0(ID_IR[24:20]), .in1(5'b01010), .out(multiplexer_4_out), .sel(ID_ecall));
  assign bit_extender_1_out = {{20{ID_IR[31]}}, ID_IR[31:20]};  // Bit_Extender bit_extender_1
  assign bit_extender_2_out = {{20{ID_IR[31]}}, {ID_IR[31:25], ID_IR[11:7]}};  // Bit_Extender bit_extender_2
  // Probe on WB_PC[11:0]
  Comparator #(.width(13), .mode("twosComplement")) comparator_7 (
    .a(CNT_num), .b(13'hc), .eq(comparator_7_eq), .lt(comparator_7_lt));  // open: gt
  Clock #(.highDuration(1), .lowDuration(1)) clock_2 (.out(clock_2_out));
  Register #(.width(2), .trigger("rising"), .Select("low")) register_1 (
    .D(\中断号 ), .Q(register_1_q), .clk(INT), .clr(RST));  // open: en
  Multiplexer #(.select(2), .width(32), .disabled("Z"), .enable("false")) multiplexer_5 (
    .in1(32'h30ac), .in2(32'h3150), .in3(32'h31f4), .out(INT_PC), .sel(\中断号 ));  // open: in0
  Multiplexer #(.select(1), .width(32), .disabled("Z"), .enable("false")) multiplexer_6 (
    .in0(bit_extender_1_out), .in1(bit_extender_2_out), .out(multiplexer_6_out), .sel(\单周期硬布线控制器_1_s_type ));
  assign bit_extender_3_out = {{20{ID_IR[31]}}, {ID_IR[31], ID_IR[7], ID_IR[30:25], ID_IR[11:8]}};  // Bit_Extender bit_extender_3
  assign bit_extender_4_out = {{12{ID_IR[31]}}, {ID_IR[31], ID_IR[19:12], ID_IR[20], ID_IR[30:21]}};  // Bit_Extender bit_extender_4
  // Probe on IF_PC
  nand nand_1 (nand_1_out, d_ff_7_q, comparator_7_eq);
  Counter #(.width(13), .max('h1fff), .ongoal("stay"), .trigger("rising"), .behavior("old")) counter_2 (
    .count(comparator_7_lt), .Q(CNT_num), .clk(clock_2_out));  // open: load, D, carry, clr, preset
  Decoder #(.select(2), .tristate("false"), .disabled("Z"), .enable("false")) decoder_1 (
    .out1(decoder_1_out1), .out2(decoder_1_out2), .out3(decoder_1_out3), .sel(register_1_q));  // open: out0
  assign CLK = nand_1_out ? clock_2_out : 1'bz;  // Controlled_Buffer controlled_buffer_1
  and and_12 (Clr1, decoder_1_out1, IF_URET);
  and and_13 (Clr2, decoder_1_out2, IF_URET);
  and and_14 (Clr3, decoder_1_out3, IF_URET);
  ID__EX id_ex_1 (
    .R1(regifile_falling_edge_1_r1), .R2(regifile_falling_edge_1_r2), .imm(multiplexer_6_out),
    .imm_b(bit_extender_3_out), .PC(ID_PC), .PC_4(if_id_1_pc_4_2), .IR(ID_IR), .rs1Forward(rs1Fwd),
    .rs2Forward(rs2Fwd), .R1_2(id_ex_1_r1_2), .R2_2(id_ex_1_r2_2), .imm_2(id_ex_1_imm_2),
    .imm_b_2(id_ex_1_imm_b_2), .PC_2(EX_PC), .PC_4_2(id_ex_1_pc_4_2), .IR_2(EX_IR),
    .rs1Forward_2(id_ex_1_rs1forward_2), .rs2Forward_2(id_ex_1_rs2forward_2), .RST_2(RST),
    .imm_j(bit_extender_4_out), .imm_j_2(id_ex_1_imm_j_2), .BGE_2(\单周期硬布线控制器_1_bge ), .LB(\单周期硬布线控制器_1_lb ),
    .JALR(\单周期硬布线控制器_1_jalr ), .JAL(\单周期硬布线控制器_1_jal ), .Beq(\单周期硬布线控制器_1_beq ), .Bne(\单周期硬布线控制器_1_bne ),
    .MemToReg(\单周期硬布线控制器_1_memtoreg ), .MemWrite(\单周期硬布线控制器_1_memwrite ), .AluSrcB(\单周期硬布线控制器_1_alu_src ),
    .RegWrite(\单周期硬布线控制器_1_regwrite ), .ecall(ID_ecall), .AluOP(\单周期硬布线控制器_1_alu_op ), .rd(ID_IR[11:7]),
    .BGE_4(BGE), .LB_2(id_ex_1_lb_2), .JALR_2(JALR), .JAL_2(JAL), .Beq_2(Beq), .Bne_2(Bne),
    .MemToReg_2(EX_MemToReg), .MemWrite_2(id_ex_1_memwrite_2), .AluSrcB_2(id_ex_1_alusrcb_2),
    .RegWrite_2(EX_RegWrite), .ecall_2(EX_ecall), .AluOP_2(id_ex_1_aluop_2), .rd_2(EX_rd), .CLK(CLK),
    .en(not_4_out), .flush(flush), .BGE(ID_URET), .BGE_3(EX_URET), .RST(EX_RST));
  Regifile_Falling_Edge regifile_falling_edge_1 (
    .Din(RDin), .Clk(CLK), .R1(regifile_falling_edge_1_r1), .R2(regifile_falling_edge_1_r2), .WE(RegWrite),
    .W_num(WB_rd), .R1_num(multiplexer_3_out), .R2_num(multiplexer_4_out));
  Pull_Resistor #(.pull(1)) pull_resistor_4 (.node(CLK));
  not not_5 (not_5_out, EX_URET);
  Multiplexer #(.select(2), .width(32), .disabled("Z"), .enable("false")) multiplexer_7 (
    .in0(id_ex_1_r1_2), .in1(MEM_R), .in2(RDin), .out(EX_R1), .sel(id_ex_1_rs1forward_2));  // open: in3
  Multiplexer #(.select(2), .width(32), .disabled("Z"), .enable("false")) multiplexer_8 (
    .in0(id_ex_1_r2_2), .in1(MEM_R), .in2(RDin), .out(EX_R2), .sel(id_ex_1_rs2forward_2));  // open: in3
  Shifter #(.width(32), .shift("ll")) shifter_1 (.in(id_ex_1_imm_b_2), .\dist (5'b00001), .out(shifter_1_out));
  Shifter #(.width(32), .shift("ll")) shifter_2 (.in(id_ex_1_imm_j_2), .\dist (5'b00001), .out(shifter_2_out));
  or or_12 (or_12_out, JAL, JALR);
  and and_15 (and_15_out, stall, ~halt);  // AND_Gate
  Register #(.width(32), .trigger("falling"), .Select("low")) mEPC (
    .D(EX_PC), .en(not_5_out), .Q(RET_PC), .clk(INT), .clr(RST));
  D_Flip_Flop #(.trigger("rising"), .Pre_Clr_Positions("LEGACY"), .NegatePresetClear("false"), .enable("false"), .NewFFLayout("false")) d_ff_8 (
    .clk(not_6_out), .D(1'b0), .Qn(IE), .preset(register_2_q), .reset(RST));  // open: Q
  not not_6 (not_6_out, IF_URET);
  Register #(.width(1), .trigger("rising"), .Select("low")) register_2 (
    .D(INT), .Q(register_2_q), .clk(CLK), .clr(RST));  // open: en
  and and_16 (INT, IE, \中断信号 );
  Adder #(.width(32)) adder_2 (.a(shifter_1_out), .b(EX_PC), .out(b));  // open: cin, cout
  Adder #(.width(32)) adder_3 (.a(shifter_2_out), .b(EX_PC), .out(j));  // open: cin, cout
  Counter #(.width(16), .max('hffff), .ongoal("wrap"), .trigger("rising"), .behavior("old")) counter_3 (
    .count(or_12_out), .Q(\无条件分支数 ), .clk(CLK), .clr(RST));  // open: load, D, carry, preset
  Counter #(.width(16), .max('hffff), .ongoal("wrap"), .trigger("rising"), .behavior("old")) counter_4 (
    .count(Branch), .Q(\条件分支成功数 ), .clk(CLK), .clr(RST));  // open: load, D, carry, preset
  Counter #(.width(16), .max('hffff), .ongoal("wrap"), .trigger("rising"), .behavior("old")) counter_5 (
    .count(and_15_out), .Q(\LoadUse次数 ), .clk(CLK), .clr(RST));  // open: load, D, carry, preset
  Multiplexer #(.select(1), .width(32), .disabled("Z"), .enable("false")) multiplexer_9 (
    .in0(EX_R2), .in1(id_ex_1_imm_2), .out(multiplexer_9_out), .sel(id_ex_1_alusrcb_2));
  ALU alu_1 (
    .X(EX_R1), .Y(multiplexer_9_out), .AluOP(id_ex_1_aluop_2), .Equal(tunnel_t), .Result(R),
    .out_4(tunnel_t_t), .out_6(tunnel));  // open: Result_2
  D_Flip_Flop #(.trigger("falling"), .Pre_Clr_Positions("LEGACY"), .NegatePresetClear("false"), .enable("false"), .NewFFLayout("false")) d_ff_9 (
    .clk(INT), .D(1'b1), .Q(EX_RST), .reset(or_13_out));  // open: Qn, preset
  Comparator #(.width(5), .mode("twosComplement")) comparator_8 (
    .a(IF_IR[6:2]), .b(5'b11100), .eq(comparator_8_eq));  // open: gt, lt
  Comparator #(.width(5), .mode("twosComplement")) comparator_9 (
    .a({IF_IR[30], IF_IR[25], IF_IR[14:12]}), .b({5{1'b0}}), .eq(comparator_9_eq));  // open: gt, lt
  Comparator #(.width(12), .mode("twosComplement")) comparator_10 (
    .a(IF_IR[31:20]), .b(12'h2), .eq(comparator_10_eq));  // open: gt, lt
  EX__MEM ex_mem_1 (
    .LB(id_ex_1_lb_2), .JALR(JALR), .MemToReg(EX_MemToReg), .MemWrite(id_ex_1_memwrite_2),
    .RegWrite(EX_RegWrite), .R1(EX_R1), .rd(EX_rd), .R(R), .MD(EX_R2), .IR(EX_IR), .PC(EX_PC),
    .PC_4(id_ex_1_pc_4_2), .LB_2(ex_mem_1_lb_2), .JALR_2(ex_mem_1_jalr_2), .MemToReg_2(ex_mem_1_memtoreg_2),
    .MemWrite_2(MemWrite), .RegWrite_2(MEM_RegWrite), .R1_2(MEM_R1), .rd_2(MEM_rd), .R_2(MEM_R), .MD_2(MDin),
    .IR_2(MEM_IR), .PC_2(M_PC), .PC_4_2(ex_mem_1_pc_4_2), .RST(RST), .CLK(CLK), .JAL(JAL),
    .JAL_2(ex_mem_1_jal_2), .ecall(EX_ecall), .RegWrite_3(MEM_ecall), .en(not_4_out));
  Counter #(.width(1), .max('h1), .ongoal("stay"), .trigger("rising"), .behavior("old")) counter_6 (
    .count(EX_RST), .Q(counter_6_q), .clk(CLK), .clr(or_13_out));  // open: load, D, carry, preset
  or or_13 (or_13_out, counter_6_q, RST);
  and and_17 (IF_URET, comparator_8_eq, comparator_9_eq, comparator_10_eq);
  RAM #(.addrWidth(10), .dataWidth(32), .bus("separate"), .Select("high")) ram_1 (
    .addr(MEM_R[11:2]), .din(MDin), .data(ram_1_data), .str(MemWrite), .sel(1'b1), .clk(CLK), .ld(1'b1),
    .clr(RST));
  MEM__WB mem_wb_1 (
    .JALR(ex_mem_1_jalr_2), .JAL(ex_mem_1_jal_2), .MenToReg(ex_mem_1_memtoreg_2), .RegWrite(MEM_RegWrite),
    .rd(MEM_rd), .R(MEM_R), .Dataout(ram_1_data), .IR(MEM_IR), .PC(M_PC), .PC_4(ex_mem_1_pc_4_2),
    .JALR_2(WB_JALR), .JAL_2(WB_JAL), .MemToReg(MemToReg), .RegWrite_2(RegWrite), .rd_2(WB_rd),
    .R_2(mem_wb_1_r_2), .Dataout_2(mem_wb_1_dataout_2), .IR_2(WB_IR), .PC_2(WB_PC), .PC_4_2(WB_PC_4),
    .RST(RST), .CLK(CLK), .LB(ex_mem_1_lb_2), .LB_2(LB), .Addr_2(Addr), .addr(MEM_R[1:0]), .R1(MEM_R1),
    .R1_2(WB_R1), .R2(MDin), .R2_2(WB_R2), .ecall(MEM_ecall), .ecall_2(WB_ecall), .en(not_4_out));
  Priority_Encoder #(.select(2), .disabled("Z")) priority_encoder_4 (
    .in0(1'b1), .in1(MemToReg), .in2(or_14_out), .out(priority_encoder_4_out));  // open: in3, gs, en_out, en_in
  or or_14 (or_14_out, WB_JAL, WB_JALR);
  Multiplexer #(.select(2), .width(32), .disabled("Z"), .enable("false")) multiplexer_10 (
    .in0(mem_wb_1_r_2), .in1(mem_wb_1_dataout_2), .in2(WB_PC_4), .out(word), .sel(priority_encoder_4_out));  // open: in3
  assign bit_extender_5_out = {{24{word[7]}}, word[7:0]};  // Bit_Extender bit_extender_5
  assign bit_extender_6_out = {{24{word[15]}}, word[15:8]};  // Bit_Extender bit_extender_6
  assign bit_extender_7_out = {{24{word[23]}}, word[23:16]};  // Bit_Extender bit_extender_7
  assign bit_extender_8_out = {{24{word[31]}}, word[31:24]};  // Bit_Extender bit_extender_8
  Multiplexer #(.select(1), .width(32), .disabled("Z"), .enable("false")) multiplexer_11 (
    .in0(word), .in1(\byte ), .out(RDin), .sel(LB));
  Multiplexer #(.select(2), .width(32), .disabled("Z"), .enable("false")) multiplexer_12 (
    .in0(bit_extender_5_out), .in1(bit_extender_6_out), .in2(bit_extender_7_out), .in3(bit_extender_8_out),
    .out(\byte ), .sel(Addr));

  // Other names for the same wires on the sheet: ID_rd[4:0] = ID_IR[11:7]; MEM_PC[31:0] = M_PC

  // Notes on the sheet:
  //   中断源
  //   时空图监测，可删除
  //   中断等待指示
  //   单级中断测试信号模拟器
  //   数码管输出
  //   指令存储器
  //   contents of rom_1 (hex, n*v repeats v):
  //   7d000113 100413 1f41993 41f9d993 433 c00913 800b13 140413 f47413 800293 100313 499993 89e9b3 1300533
  //   2200893 73 406282b3 fe0294e3 140413 f00f93 1f47433 1c41413 800293 100313 49d993 89e9b3 1300533
  //   2200893 73 406282b3 fe0294e3 1c45413 406b0b33 b0463 f95ff06f 2b3 fff2c293 1029293 fff2e293 500533
  //   2200893 73 f5dff06f 1112023 410113 a12023 410113 812023 410113 1312023 410113 1412023 410113 1512023
  //   410113 1612023 410113 100b13 300a13 100a93 1600433 441413 14469b3 1300533 2200893 73 fe0416e3
  //   415a0a33 fe0a10e3 ffc10113 12b03 ffc10113 12a83 ffc10113 12a03 ffc10113 12983 ffc10113 12403
  //   ffc10113 12503 ffc10113 12883 200073 1112023 410113 a12023 410113 812023 410113 1312023 410113
  //   1412023 410113 1512023 410113 1612023 410113 200b13 300a13 100a93 1600433 441413 14469b3 1300533
  //   2200893 73 fe0416e3 415a0a33 fe0a10e3 ffc10113 12b03 ffc10113 12a83 ffc10113 12a03 ffc10113 12983
  //   ffc10113 12403 ffc10113 12503 ffc10113 12883 200073 1112023 410113 a12023 410113 812023 410113
  //   1312023 410113 1412023 410113 1512023 410113 1612023 410113 300b13 300a13 100a93 1600433 441413
  //   14469b3 1300533 2200893 73 fe0416e3 415a0a33 fe0a10e3 ffc10113 12b03 ffc10113 12a83 ffc10113 12a03
  //   ffc10113 12983 ffc10113 12403 ffc10113 12503 ffc10113 12883 200073
  //   控制位
  //   JAL
  //   JALR
  //   LB
  //   BGE
  //   流水调试日志用
  //   暂停节拍，不能为0
  //   Beq
  //   Bne
  //   MemToReg
  //   MemWrite
  //   AluOP
  //   AluSrcB
  //   RegWrite
  //   S_Type
  //   戳工具置1进入计数暂停模式，ctrl+k时钟自动运行到对应节拍暂停
  //   ctrl+k关闭时钟连续运行，将控制位置零，进入单步调试模式调试
  //   入口
  //   可计数暂停的时钟源
  //   返回清零
  //   LB
  //   JALR
  //   JAL
  //   MemWrite
  //   AluOP
  //   AluSrcB
  //   为方便自动评测，需要输出流水线各段保存的PC值，注意是PC不是PC+4，另外ID段寄存器写入信息，Mem段内存写入信息也要输出
  //   保存现场
  //   中断请求
  //   LB
  //   JALR
  //   JAL
  //   MemToReg
  //   数据存储器
endmodule

module BTB (
  input  [31:0] in_1,
  input  [31:0] in_2,
  input  [31:0] in_3,
  input  in_4,
  input  in_5,
  input  in_6,
  input  in_7,
  output [31:0] out_8,
  output out_9
);

  wire and_17_out, and_26_out, and_27_out, and_28_out, and_29_out, and_30_out, and_31_out, and_32_out,
       and_33_out, comparator_1_eq, comparator_2_eq, comparator_3_eq, comparator_4_eq, comparator_5_eq,
       comparator_6_eq, comparator_7_eq, comparator_8_eq, comparator_9_eq, comparator_10_eq,
       comparator_11_eq, comparator_12_eq, comparator_13_eq, comparator_14_eq, comparator_15_eq,
       comparator_16_eq, d_ff_1_q, d_ff_2_q, d_ff_3_q, d_ff_4_q, d_ff_5_q, d_ff_6_q, d_ff_7_q, d_ff_8_q,
       decoder_1_out0, decoder_1_out1, decoder_1_out2, decoder_1_out3, decoder_1_out4, decoder_1_out5,
       decoder_1_out6, decoder_1_out7, decoder_2_out0, decoder_2_out1, decoder_2_out2, decoder_2_out3,
       decoder_2_out4, decoder_2_out5, decoder_2_out6, decoder_2_out7, EX_miss, H0, H1, H2, H3, H4, H5, H6,
       H7, L0, L1, L2, L3, L4, L5, L6, L7, not_1_out, not_2_out, not_3_out, not_4_out, not_5_out, not_6_out,
       not_7_out, not_8_out, not_9_out, or_1_out, or_2_out, or_3_out, or_4_out, or_5_out, or_6_out, or_7_out,
       or_8_out, or_9_out, or_10_out, or_11_out, or_12_out, or_13_out, or_14_out, or_15_out, or_16_out,
       priority_encoder_1_gs, v0, v1, v2, v3, v4, v5, v6, v7, w0, w1, w2, w3, w4, w5, w6, w7;
  wire [1:0] fsm_1_n0, fsm_2_n0, fsm_3_n0, fsm_4_n0, fsm_5_n0, fsm_6_n0, fsm_7_n0, fsm_8_n0, register_1_q,
       register_2_q, register_3_q, register_4_q, register_5_q, register_6_q, register_7_q, register_8_q;
  wire [2:0] max_1_max_num, max_2_max_num, max_3_max_num, max_4_max_num, max_5_max_num, max_6_max_num,
       max_7_max_num, priority_encoder_1_out;
  wire [15:0] c0, c1, c2, c3, c4, c5, c6, c7, max_1_max, max_2_max, max_3_max, max_4_max, max_5_max,
       max_6_max;
  wire [31:0] Addr_2_q, Addr_3_q, Addr_4_q, Addr_5_q, Addr_6_q, Addr_7_q, Addr_8_q, Addr_q, PC0, PC1, PC2,
       PC3, PC4, PC5, PC6, PC7;

  Register #(.width(1), .trigger("rising"), .Select("low")) valid (.D(1'b1), .en(w0), .Q(v0), .clk(in_4));  // open: clr
  Register #(.width(1), .trigger("rising"), .Select("low")) valid_2 (
    .D(1'b1), .en(w1), .Q(v1), .clk(in_4));  // open: clr
  Register #(.width(1), .trigger("rising"), .Select("low")) valid_3 (
    .D(1'b1), .en(w2), .Q(v2), .clk(in_4));  // open: clr
  Register #(.width(1), .trigger("rising"), .Select("low")) valid_4 (
    .D(1'b1), .en(w3), .Q(v3), .clk(in_4));  // open: clr
  Register #(.width(1), .trigger("rising"), .Select("low")) valid_5 (
    .D(1'b1), .en(w4), .Q(v4), .clk(in_4));  // open: clr
  Register #(.width(1), .trigger("rising"), .Select("low")) valid_6 (
    .D(1'b1), .en(w5), .Q(v5), .clk(in_4));  // open: clr
  Register #(.width(1), .trigger("rising"), .Select("low")) valid_7 (
    .D(1'b1), .en(w6), .Q(v6), .clk(in_4));  // open: clr
  Register #(.width(1), .trigger("rising"), .Select("low")) valid_8 (
    .D(1'b1), .en(w7), .Q(v7), .clk(in_4));  // open: clr
  Register #(.width(32), .trigger("rising"), .Select("low")) PC (.D(in_2), .en(w0), .Q(PC0), .clk(in_4));  // open: clr
  Register #(.width(32), .trigger("rising"), .Select("low")) PC_2 (
    .D(in_2), .en(w1), .Q(PC1), .clk(in_4));  // open: clr
  Register #(.width(32), .trigger("rising"), .Select("low")) PC_3 (
    .D(in_2), .en(w2), .Q(PC2), .clk(in_4));  // open: clr
  Register #(.width(32), .trigger("rising"), .Select("low")) PC_4 (
    .D(in_2), .en(w3), .Q(PC3), .clk(in_4));  // open: clr
  Register #(.width(32), .trigger("rising"), .Select("low")) PC_5 (
    .D(in_2), .en(w4), .Q(PC4), .clk(in_4));  // open: clr
  Register #(.width(32), .trigger("rising"), .Select("low")) PC_6 (
    .D(in_2), .en(w5), .Q(PC5), .clk(in_4));  // open: clr
  Register #(.width(32), .trigger("rising"), .Select("low")) PC_7 (
    .D(in_2), .en(w6), .Q(PC6), .clk(in_4));  // open: clr
  Register #(.width(32), .trigger("rising"), .Select("low")) PC_8 (
    .D(in_2), .en(w7), .Q(PC7), .clk(in_4));  // open: clr
  Register #(.width(32), .trigger("rising"), .Select("low")) Addr (
    .D(in_3), .en(w0), .Q(Addr_q), .clk(in_4));  // open: clr
  Register #(.width(32), .trigger("rising"), .Select("low")) Addr_2 (
    .D(in_3), .en(w1), .Q(Addr_2_q), .clk(in_4));  // open: clr
  Register #(.width(32), .trigger("rising"), .Select("low")) Addr_3 (
    .D(in_3), .en(w2), .Q(Addr_3_q), .clk(in_4));  // open: clr
  Register #(.width(32), .trigger("rising"), .Select("low")) Addr_4 (
    .D(in_3), .en(w3), .Q(Addr_4_q), .clk(in_4));  // open: clr
  Register #(.width(32), .trigger("rising"), .Select("low")) Addr_5 (
    .D(in_3), .en(w4), .Q(Addr_5_q), .clk(in_4));  // open: clr
  Register #(.width(32), .trigger("rising"), .Select("low")) Addr_6 (
    .D(in_3), .en(w5), .Q(Addr_6_q), .clk(in_4));  // open: clr
  Register #(.width(32), .trigger("rising"), .Select("low")) Addr_7 (
    .D(in_3), .en(w6), .Q(Addr_7_q), .clk(in_4));  // open: clr
  Register #(.width(32), .trigger("rising"), .Select("low")) Addr_8 (
    .D(in_3), .en(w7), .Q(Addr_8_q), .clk(in_4));  // open: clr
  assign out_8 = L0 ? Addr_q : 32'bz;  // Controlled_Buffer controlled_buffer_1
  assign out_8 = L1 ? Addr_2_q : 32'bz;  // Controlled_Buffer controlled_buffer_2
  assign out_8 = L2 ? Addr_3_q : 32'bz;  // Controlled_Buffer controlled_buffer_3
  assign out_8 = L3 ? Addr_4_q : 32'bz;  // Controlled_Buffer controlled_buffer_4
  assign out_8 = L4 ? Addr_5_q : 32'bz;  // Controlled_Buffer controlled_buffer_5
  assign out_8 = L5 ? Addr_6_q : 32'bz;  // Controlled_Buffer controlled_buffer_6
  assign out_8 = L6 ? Addr_7_q : 32'bz;  // Controlled_Buffer controlled_buffer_7
  assign out_8 = L7 ? Addr_8_q : 32'bz;  // Controlled_Buffer controlled_buffer_8
  D_Flip_Flop #(.trigger("rising"), .Pre_Clr_Positions("ABOVE_BELOW"), .NegatePresetClear("false"), .enable("false"), .NewFFLayout("false")) d_ff_1 (
    .clk(in_4), .D(or_1_out), .Q(d_ff_1_q));  // open: Qn, preset, reset
  or or_1 (or_1_out, w0, L0);
  D_Flip_Flop #(.trigger("rising"), .Pre_Clr_Positions("ABOVE_BELOW"), .NegatePresetClear("false"), .enable("false"), .NewFFLayout("false")) d_ff_2 (
    .clk(in_4), .D(or_2_out), .Q(d_ff_2_q));  // open: Qn, preset, reset
  or or_2 (or_2_out, w1, L1);
  D_Flip_Flop #(.trigger("rising"), .Pre_Clr_Positions("ABOVE_BELOW"), .NegatePresetClear("false"), .enable("false"), .NewFFLayout("false")) d_ff_3 (
    .clk(in_4), .D(or_3_out), .Q(d_ff_3_q));  // open: Qn, preset, reset
  or or_3 (or_3_out, w2, L2);
  D_Flip_Flop #(.trigger("rising"), .Pre_Clr_Positions("ABOVE_BELOW"), .NegatePresetClear("false"), .enable("false"), .NewFFLayout("false")) d_ff_4 (
    .clk(in_4), .D(or_4_out), .Q(d_ff_4_q));  // open: Qn, preset, reset
  or or_4 (or_4_out, w3, L3);
  D_Flip_Flop #(.trigger("rising"), .Pre_Clr_Positions("ABOVE_BELOW"), .NegatePresetClear("false"), .enable("false"), .NewFFLayout("false")) d_ff_5 (
    .clk(in_4), .D(or_5_out), .Q(d_ff_5_q));  // open: Qn, preset, reset
  or or_5 (or_5_out, w4, L4);
  D_Flip_Flop #(.trigger("rising"), .Pre_Clr_Positions("ABOVE_BELOW"), .NegatePresetClear("false"), .enable("false"), .NewFFLayout("false")) d_ff_6 (
    .clk(in_4), .D(or_6_out), .Q(d_ff_6_q));  // open: Qn, preset, reset
  or or_6 (or_6_out, w5, L5);
  D_Flip_Flop #(.trigger("rising"), .Pre_Clr_Positions("LEGACY"), .NegatePresetClear("false"), .enable("true"), .NewFFLayout("false")) d_ff_7 (
    .clk(in_4), .D(or_7_out), .Q(d_ff_7_q));  // open: Qn, preset, en, reset
  or or_7 (or_7_out, w6, L6);
  D_Flip_Flop #(.trigger("rising"), .Pre_Clr_Positions("LEGACY"), .NegatePresetClear("false"), .enable("true"), .NewFFLayout("false")) d_ff_8 (
    .clk(in_4), .D(or_8_out), .Q(d_ff_8_q));  // open: Qn, preset, en, reset
  or or_8 (or_8_out, w7, L7);
  Counter #(.width(16), .max('hffff), .ongoal("wrap"), .trigger("rising"), .behavior("new")) count (
    .Q(c0), .clk(in_4), .clr(d_ff_1_q));  // open: load, D, count, carry, preset, down
  Counter #(.width(16), .max('hffff), .ongoal("wrap"), .trigger("rising"), .behavior("new")) count_2 (
    .Q(c1), .clk(in_4), .clr(d_ff_2_q));  // open: load, D, count, carry, preset, down
  Counter #(.width(16), .max('hffff), .ongoal("wrap"), .trigger("rising"), .behavior("new")) count_3 (
    .Q(c2), .clk(in_4), .clr(d_ff_3_q));  // open: load, D, count, carry, preset, down
  Counter #(.width(16), .max('hffff), .ongoal("wrap"), .trigger("rising"), .behavior("new")) count_4 (
    .Q(c3), .clk(in_4), .clr(d_ff_4_q));  // open: load, D, count, carry, preset, down
  Counter #(.width(16), .max('hffff), .ongoal("wrap"), .trigger("rising"), .behavior("new")) count_5 (
    .Q(c4), .clk(in_4), .clr(d_ff_5_q));  // open: load, D, count, carry, preset, down
  Counter #(.width(16), .max('hffff), .ongoal("wrap"), .trigger("rising"), .behavior("new")) count_6 (
    .Q(c5), .clk(in_4), .clr(d_ff_6_q));  // open: load, D, count, carry, preset, down
  Counter #(.width(16), .max('hffff), .ongoal("wrap"), .trigger("rising"), .behavior("new")) count_7 (
    .Q(c6), .clk(in_4), .clr(d_ff_7_q));  // open: load, D, count, carry, preset, down
  Counter #(.width(16), .max('hffff), .ongoal("wrap"), .trigger("rising"), .behavior("new")) count_8 (
    .Q(c7), .clk(in_4), .clr(d_ff_8_q));  // open: load, D, count, carry, preset, down
  Comparator #(.width(32), .mode("twosComplement")) comparator_1 (
    .a(PC0), .b(in_1), .eq(comparator_1_eq));  // open: gt, lt
  Comparator #(.width(32), .mode("twosComplement")) comparator_2 (
    .a(PC1), .b(in_1), .eq(comparator_2_eq));  // open: gt, lt
  Comparator #(.width(32), .mode("twosComplement")) comparator_3 (
    .a(PC2), .b(in_1), .eq(comparator_3_eq));  // open: gt, lt
  Comparator #(.width(32), .mode("twosComplement")) comparator_4 (
    .a(PC3), .b(in_1), .eq(comparator_4_eq));  // open: gt, lt
  Comparator #(.width(32), .mode("twosComplement")) comparator_5 (
    .a(PC4), .b(in_1), .eq(comparator_5_eq));  // open: gt, lt
  Comparator #(.width(32), .mode("twosComplement")) comparator_6 (
    .a(PC5), .b(in_1), .eq(comparator_6_eq));  // open: gt, lt
  Comparator #(.width(32), .mode("twosComplement")) comparator_7 (
    .a(PC6), .b(in_1), .eq(comparator_7_eq));  // open: gt, lt
  Comparator #(.width(32), .mode("twosComplement")) comparator_8 (
    .a(PC7), .b(in_1), .eq(comparator_8_eq));  // open: gt, lt
  not not_1 (not_1_out, v0);
  not not_2 (not_2_out, v1);
  not not_3 (not_3_out, v2);
  not not_4 (not_4_out, v3);
  not not_5 (not_5_out, v4);
  not not_6 (not_6_out, v5);
  not not_7 (not_7_out, v6);
  not not_8 (not_8_out, v7);
  MAX max_1 (.Y(c0), .X(c1), .Y_num(3'b000), .X_num(3'b001), .MAX(max_1_max), .MAX_num(max_1_max_num));
  MAX max_2 (
    .Y(max_1_max), .X(max_3_max), .Y_num(max_1_max_num), .X_num(max_3_max_num), .MAX(max_2_max),
    .MAX_num(max_2_max_num));
  MAX max_3 (.Y(c2), .X(c3), .Y_num(3'b010), .X_num(3'b011), .MAX(max_3_max), .MAX_num(max_3_max_num));
  MAX max_4 (.Y(c4), .X(c5), .Y_num(3'b100), .X_num(3'b101), .MAX(max_4_max), .MAX_num(max_4_max_num));
  MAX max_5 (
    .Y(max_4_max), .X(max_6_max), .Y_num(max_4_max_num), .X_num(max_6_max_num), .MAX(max_5_max),
    .MAX_num(max_5_max_num));
  MAX max_6 (.Y(c6), .X(c7), .Y_num(3'b110), .X_num(3'b111), .MAX(max_6_max), .MAX_num(max_6_max_num));
  and and_1 (L0, v0, comparator_1_eq);
  and and_2 (L1, v1, comparator_2_eq);
  and and_3 (L2, v2, comparator_3_eq);
  and and_4 (L3, v3, comparator_4_eq);
  and and_5 (L4, v4, comparator_5_eq);
  and and_6 (L5, v5, comparator_6_eq);
  and and_7 (L6, v6, comparator_7_eq);
  and and_8 (L7, v7, comparator_8_eq);
  Priority_Encoder #(.select(3), .disabled("Z")) priority_encoder_1 (
    .in0(not_1_out), .in1(not_2_out), .in2(not_3_out), .in3(not_4_out), .in4(not_5_out), .in5(not_6_out),
    .in6(not_7_out), .in7(not_8_out), .out(priority_encoder_1_out), .gs(priority_encoder_1_gs));  // open: en_out, en_in
  MAX max_7 (
    .Y(max_2_max), .X(max_5_max), .Y_num(max_2_max_num), .X_num(max_5_max_num), .MAX_num(max_7_max_num));  // open: MAX
  Decoder #(.select(3), .tristate("false"), .disabled(0), .enable("true")) decoder_1 (
    .out0(decoder_1_out0), .out1(decoder_1_out1), .out2(decoder_1_out2), .out3(decoder_1_out3),
    .out4(decoder_1_out4), .out5(decoder_1_out5), .out6(decoder_1_out6), .out7(decoder_1_out7),
    .sel(priority_encoder_1_out), .en(priority_encoder_1_gs));
  not not_9 (not_9_out, priority_encoder_1_gs);
  Decoder #(.select(3), .tristate("false"), .disabled(0), .enable("true")) decoder_2 (
    .out0(decoder_2_out0), .out1(decoder_2_out1), .out2(decoder_2_out2), .out3(decoder_2_out3),
    .out4(decoder_2_out4), .out5(decoder_2_out5), .out6(decoder_2_out6), .out7(decoder_2_out7),
    .sel(max_7_max_num), .en(not_9_out));
  Comparator #(.width(32), .mode("twosComplement")) comparator_9 (
    .a(PC0), .b(in_2), .eq(comparator_9_eq));  // open: gt, lt
  Comparator #(.width(32), .mode("twosComplement")) comparator_10 (
    .a(PC1), .b(in_2), .eq(comparator_10_eq));  // open: gt, lt
  Comparator #(.width(32), .mode("twosComplement")) comparator_11 (
    .a(PC2), .b(in_2), .eq(comparator_11_eq));  // open: gt, lt
  Comparator #(.width(32), .mode("twosComplement")) comparator_12 (
    .a(PC3), .b(in_2), .eq(comparator_12_eq));  // open: gt, lt
  Comparator #(.width(32), .mode("twosComplement")) comparator_13 (
    .a(PC4), .b(in_2), .eq(comparator_13_eq));  // open: gt, lt
  Comparator #(.width(32), .mode("twosComplement")) comparator_14 (
    .a(PC5), .b(in_2), .eq(comparator_14_eq));  // open: gt, lt
  Comparator #(.width(32), .mode("twosComplement")) comparator_15 (
    .a(PC6), .b(in_2), .eq(comparator_15_eq));  // open: gt, lt
  Comparator #(.width(32), .mode("twosComplement")) comparator_16 (
    .a(PC7), .b(in_2), .eq(comparator_16_eq));  // open: gt, lt
  and and_9 (H0, v0, comparator_9_eq);
  and and_10 (H1, v1, comparator_10_eq);
  and and_11 (H2, v2, comparator_11_eq);
  and and_12 (H3, v3, comparator_12_eq);
  and and_13 (H4, v4, comparator_13_eq);
  and and_14 (H5, v5, comparator_14_eq);
  and and_15 (H6, v6, comparator_15_eq);
  and and_16 (H7, v7, comparator_16_eq);
  and and_17 (and_17_out, EX_miss, in_6);
  or or_9 (or_9_out, decoder_1_out0, decoder_2_out0);
  or or_10 (or_10_out, decoder_1_out1, decoder_2_out1);
  or or_11 (or_11_out, decoder_1_out2, decoder_2_out2);
  or or_12 (or_12_out, decoder_1_out3, decoder_2_out3);
  or or_13 (or_13_out, decoder_1_out4, decoder_2_out4);
  or or_14 (or_14_out, decoder_1_out5, decoder_2_out5);
  or or_15 (or_15_out, decoder_1_out6, decoder_2_out6);
  or or_16 (or_16_out, decoder_1_out7, decoder_2_out7);
  nor nor_1 (EX_miss, H0, H1, H2, H3, H4, H5, H6, H7);
  and and_18 (w0, and_17_out, or_9_out);
  and and_19 (w1, and_17_out, or_10_out);
  and and_20 (w2, and_17_out, or_11_out);
  and and_21 (w3, and_17_out, or_12_out);
  and and_22 (w4, and_17_out, or_13_out);
  and and_23 (w5, and_17_out, or_14_out);
  and and_24 (w6, and_17_out, or_15_out);
  and and_25 (w7, and_17_out, or_16_out);
  FSM fsm_1 (.S0(register_1_q[0]), .S1(register_1_q[1]), .BranchTaken(in_7), .N0(fsm_1_n0[0]), .N1(fsm_1_n0[1]));
  and and_26 (and_26_out, in_6, H0);
  FSM fsm_2 (.S0(register_2_q[0]), .S1(register_2_q[1]), .BranchTaken(in_7), .N0(fsm_2_n0[0]), .N1(fsm_2_n0[1]));
  and and_27 (and_27_out, in_6, H1);
  FSM fsm_3 (.S0(register_3_q[0]), .S1(register_3_q[1]), .BranchTaken(in_7), .N0(fsm_3_n0[0]), .N1(fsm_3_n0[1]));
  and and_28 (and_28_out, in_6, H2);
  FSM fsm_4 (.S0(register_4_q[0]), .S1(register_4_q[1]), .BranchTaken(in_7), .N0(fsm_4_n0[0]), .N1(fsm_4_n0[1]));
  and and_29 (and_29_out, in_6, H3);
  FSM fsm_5 (.S0(register_5_q[0]), .S1(register_5_q[1]), .BranchTaken(in_7), .N0(fsm_5_n0[0]), .N1(fsm_5_n0[1]));
  and and_30 (and_30_out, in_6, H4);
  FSM fsm_6 (.S0(register_6_q[0]), .S1(register_6_q[1]), .BranchTaken(in_7), .N0(fsm_6_n0[0]), .N1(fsm_6_n0[1]));
  and and_31 (and_31_out, in_6, H5);
  FSM fsm_7 (.S0(register_7_q[0]), .S1(register_7_q[1]), .BranchTaken(in_7), .N0(fsm_7_n0[0]), .N1(fsm_7_n0[1]));
  and and_32 (and_32_out, in_6, H6);
  FSM fsm_8 (.S0(register_8_q[0]), .S1(register_8_q[1]), .BranchTaken(in_7), .N0(fsm_8_n0[0]), .N1(fsm_8_n0[1]));
  and and_33 (and_33_out, in_6, H7);
  Register #(.width(2), .trigger("rising"), .Select("low")) register_1 (
    .D(fsm_1_n0), .en(and_26_out), .Q(register_1_q), .clk(in_4), .clr(in_5));
  Register #(.width(2), .trigger("rising"), .Select("low")) register_2 (
    .D(fsm_2_n0), .en(and_27_out), .Q(register_2_q), .clk(in_4), .clr(in_5));
  Register #(.width(2), .trigger("rising"), .Select("low")) register_3 (
    .D(fsm_3_n0), .en(and_28_out), .Q(register_3_q), .clk(in_4), .clr(in_5));
  Register #(.width(2), .trigger("rising"), .Select("low")) register_4 (
    .D(fsm_4_n0), .en(and_29_out), .Q(register_4_q), .clk(in_4), .clr(in_5));
  Register #(.width(2), .trigger("rising"), .Select("low")) register_5 (
    .D(fsm_5_n0), .en(and_30_out), .Q(register_5_q), .clk(in_4), .clr(in_5));
  Register #(.width(2), .trigger("rising"), .Select("low")) register_6 (
    .D(fsm_6_n0), .en(and_31_out), .Q(register_6_q), .clk(in_4), .clr(in_5));
  Register #(.width(2), .trigger("rising"), .Select("low")) register_7 (
    .D(fsm_7_n0), .en(and_32_out), .Q(register_7_q), .clk(in_4), .clr(in_5));
  Register #(.width(2), .trigger("rising"), .Select("low")) register_8 (
    .D(fsm_8_n0), .en(and_33_out), .Q(register_8_q), .clk(in_4), .clr(in_5));
  assign out_9 = L0 ? register_1_q[1] : 1'bz;  // Controlled_Buffer controlled_buffer_9
  assign out_9 = L1 ? register_2_q[1] : 1'bz;  // Controlled_Buffer controlled_buffer_10
  assign out_9 = L2 ? register_3_q[1] : 1'bz;  // Controlled_Buffer controlled_buffer_11
  assign out_9 = L3 ? register_4_q[1] : 1'bz;  // Controlled_Buffer controlled_buffer_12
  assign out_9 = L4 ? register_5_q[1] : 1'bz;  // Controlled_Buffer controlled_buffer_13
  assign out_9 = L5 ? register_6_q[1] : 1'bz;  // Controlled_Buffer controlled_buffer_14
  assign out_9 = L6 ? register_7_q[1] : 1'bz;  // Controlled_Buffer controlled_buffer_15
  assign out_9 = L7 ? register_8_q[1] : 1'bz;  // Controlled_Buffer controlled_buffer_16

  // Other names for the same wires on the sheet: Branch = in_6; BranchAddr[31:0] = in_3; BranchTaken = in_7;
  //   CLK = in_4; EX_PC[31:0] = in_2; IF_PC[31:0] = in_1; JumpAddr[31:0] = out_8; PredictJump = out_9; RST = in_5
endmodule

module \重定向流水线_动态分支预测  (
  output RegWrite,
  output MemWrite,
  output [31:0] IF_PC,
  output [31:0] ID_PC,
  output [31:0] EX_PC,
  output [31:0] M_PC,
  output [31:0] WB_PC,
  output [31:0] RDin,
  output [31:0] MDin,
  output [31:0] LedData
);

  wire and_1_out, and_2_out, and_4_out, and_5_out, and_6_out, and_7_out, and_8_out, and_9_out, B, Beq, BGE,
       Bne, Branch, BranchTaken, button_1_out, CLK, clock_1_out, clock_2_out, comparator_1_eq,
       comparator_2_eq, comparator_3_eq, comparator_3_lt, d_ff_1_q, error, EX_ecall, ex_mem_1_jal_2,
       ex_mem_1_jalr_2, ex_mem_1_lb_2, ex_mem_1_memtoreg_2, EX_MemToReg, EX_PredictJump, EX_RegWrite, flush,
       Go, halt, ID_ecall, id_ex_1_alusrcb_2, id_ex_1_lb_2, id_ex_1_memwrite_2, if_id_1_predictjump_2, IR1,
       IR2, IR3, JAL, JALR, LB, MEM_ecall, MEM_RegWrite, MemToReg, nand_1_out, not_2_out, not_3_out,
       not_4_out, or_1_out, or_4_out, or_5_out, or_6_out, PredictJump, RST, stall, tunnel, tunnel_t,
       tunnel_t_t, W1, W2, W3, WB_ecall, WB_JAL, WB_JALR, \单周期硬布线控制器_1_alu_src , \单周期硬布线控制器_1_beq ,
       \单周期硬布线控制器_1_bge , \单周期硬布线控制器_1_bne , \单周期硬布线控制器_1_jal , \单周期硬布线控制器_1_jalr , \单周期硬布线控制器_1_lb ,
       \单周期硬布线控制器_1_memtoreg , \单周期硬布线控制器_1_memwrite , \单周期硬布线控制器_1_regwrite , \单周期硬布线控制器_1_s_type ;
  wire [1:0] Addr, id_ex_1_rs1forward_2, id_ex_1_rs2forward_2, priority_encoder_1_out,
       priority_encoder_2_out, priority_encoder_3_out, rs1Forward, rs2Forward;
  wire [3:0] id_ex_1_aluop_2, \单周期硬布线控制器_1_alu_op ;
  wire [4:0] EX_rd, MEM_rd, multiplexer_5_out, multiplexer_6_out, WB_rd;
  wire [12:0] CNT_num;
  wire [15:0] \LoadUse次数 , \总周期数 , \插入气泡数 , \无条件分支数 , \条件分支成功数 ;
  wire [31:0] B_Addr, bit_extender_1_out, bit_extender_2_out, bit_extender_3_out, bit_extender_4_out,
       bit_extender_5_out, bit_extender_6_out, bit_extender_7_out, bit_extender_8_out, BranchAddr,
       btb_1_out_8, \byte , EX_IR, ex_mem_1_pc_4_2, EX_PC_4, EX_R1, EX_R2, id_ex_1_imm_2, id_ex_1_imm_b_2,
       id_ex_1_imm_j_2, id_ex_1_r1_2, id_ex_1_r2_2, ID_IR, if_id_1_pc_4_2, IF_IR, IF_PC_4, J_Addr, MEM_IR,
       MEM_R, MEM_R1, mem_wb_1_dataout_2, mem_wb_1_r_2, multiplexer_1_out, multiplexer_3_out,
       multiplexer_7_out, multiplexer_10_out, PredictAddr, R, ram_1_data, regifile_falling_edge_1_r1,
       regifile_falling_edge_1_r2, shifter_1_out, shifter_2_out, WB_IR, WB_PC_4, WB_R1, WB_R2, word;

  Button \u_总复位  (.out(RST));
  Button _1 (.out(IR1));
  Button _2 (.out(IR2));
  Button _3 (.out(IR3));
  // Probe on \总周期数 
  // Probe on \总周期数 
  Button \u_继续运行  (.out(Go));
  LED #(.active("true")) led_1 (.in(W1));
  LED #(.active("true")) led_2 (.in(W2));
  LED #(.active("true")) led_3 (.in(W3));
  or or_1 (or_1_out, B, JAL, JALR);
  Hex_Digit_Display hex_digit_display_1 (.value(LedData[31:28]));  // open: dp
  // Probe on IF_PC[19:0]
  // RiscV_Probe riscv_probe_1: pin names not known; wires that end beside it: IF_IR
  or or_2 (B, Beq, Bne, BGE);
  Button button_1 (.out(button_1_out));
  Comparator #(.width(32), .mode("twosComplement")) comparator_1 (
    .a(WB_R1), .b(32'ha), .eq(comparator_1_eq));  // open: gt, lt
  Priority_Encoder #(.select(2), .disabled("Z")) priority_encoder_1 (
    .in0(1'b1), .in1(Branch), .in2(JAL), .in3(JALR), .out(priority_encoder_1_out));  // open: gs, en_out, en_in
  Multiplexer #(.select(2), .width(32), .disabled("Z"), .enable("false")) multiplexer_1 (
    .in0(EX_PC_4), .in1(B_Addr), .in2(J_Addr), .in3(R), .out(multiplexer_1_out), .sel(priority_encoder_1_out));
  Hex_Digit_Display hex_digit_display_2 (.value(LedData[27:24]));  // open: dp
  Hex_Digit_Display hex_digit_display_3 (.value(LedData[23:20]));  // open: dp
  // Probe on ID_PC[19:0]
  // RiscV_Probe riscv_probe_2: pin names not known; wires that end beside it: ID_IR
  BTB btb_1 (
    .in_2(EX_PC), .in_3(BranchAddr), .out_8(btb_1_out_8), .in_7(BranchTaken), .out_9(PredictJump),
    .in_6(or_1_out), .in_1(IF_PC), .in_4(CLK), .in_5(button_1_out));
  \重定向  \u_重定向_1  (
    .in_1(EX_rd), .in_3(MEM_rd), .in_4(EX_RegWrite), .in_5(MEM_RegWrite), .in_7(ID_ecall),
    .out_9(rs1Forward), .out_10(rs2Forward), .stall(stall), .BranchTaken(BranchTaken), .in_2(ID_IR),
    .in_6(EX_MemToReg), .flush(flush));
  Register #(.width(32), .trigger("rising"), .Select("low")) PC (
    .D(WB_R2), .en(and_1_out), .Q(LedData), .clk(CLK));  // open: clr
  and and_1 (and_1_out, WB_ecall, ~comparator_1_eq);  // AND_Gate
  and and_2 (and_2_out, WB_ecall, comparator_1_eq);
  Comparator #(.width(2), .mode("twosComplement")) comparator_2 (
    .a(2'b00), .b(priority_encoder_1_out), .eq(comparator_2_eq));  // open: gt, lt
  not not_1 (BranchTaken, comparator_2_eq);
  Hex_Digit_Display hex_digit_display_4 (.value(LedData[19:16]));  // open: dp
  Hex_Digit_Display hex_digit_display_5 (.value(LedData[15:12]));  // open: dp
  Pull_Resistor #(.pull(0)) pull_resistor_1 (.node(PredictJump));
  Multiplexer #(.select(1), .width(32), .disabled("Z"), .enable("false")) multiplexer_2 (
    .in0(IF_PC_4), .in1(btb_1_out_8), .out(PredictAddr), .sel(PredictJump));
  and and_3 (halt, and_2_out, ~Go);  // AND_Gate
  Multiplexer #(.select(1), .width(32), .disabled("Z"), .enable("false")) multiplexer_3 (
    .in0(PredictAddr), .in1(multiplexer_1_out), .out(multiplexer_3_out), .sel(error));
  Register #(.width(32), .trigger("rising"), .Select("low")) PC_2 (
    .D(multiplexer_3_out), .en(and_4_out), .Q(IF_PC), .clk(CLK), .clr(RST));
  and and_4 (and_4_out, ~stall, not_2_out);  // AND_Gate
  not not_2 (not_2_out, halt);
  Hex_Digit_Display hex_digit_display_6 (.value(LedData[7:4]));  // open: dp
  Hex_Digit_Display hex_digit_display_7 (.value(LedData[11:8]));  // open: dp
  Clock #(.highDuration(1), .lowDuration(1)) clock_1 (.out(clock_1_out));
  // Probe on EX_PC[19:0]
  // RiscV_Probe riscv_probe_3: pin names not known; wires that end beside it: clock_1_out, EX_IR, CLK
  not not_3 (not_3_out, halt);
  Hex_Digit_Display hex_digit_display_8 (.value(LedData[3:0]));  // open: dp
  and and_5 (and_5_out, Beq, tunnel_t);
  and and_6 (and_6_out, ~tunnel_t, Bne);  // AND_Gate
  and and_7 (and_7_out, tunnel_t_t, BGE);
  Counter #(.width(16), .max('hffff), .ongoal("stay"), .trigger("rising"), .behavior("old")) counter_1 (
    .count(not_3_out), .Q(\总周期数 ), .clk(CLK), .clr(RST));  // open: load, D, carry, preset
  Adder #(.width(32)) adder_1 (.a(IF_PC), .b(32'h4), .out(IF_PC_4));  // open: cin, cout
  // Probe on \总周期数 
  // Probe on M_PC[19:0]
  // RiscV_Probe riscv_probe_4: pin names not known; wires that end beside it: MEM_IR
  Priority_Encoder #(.select(2), .disabled("Z")) priority_encoder_2 (
    .in0(1'b1), .in1(B), .in2(JAL), .in3(JALR), .out(priority_encoder_2_out));  // open: gs, en_out, en_in
  Multiplexer #(.select(2), .width(32), .disabled("Z"), .enable("false")) multiplexer_4 (
    .in0(IF_PC), .in1(B_Addr), .in2(J_Addr), .in3(R), .out(BranchAddr), .sel(priority_encoder_2_out));
  or or_3 (Branch, and_5_out, and_6_out, and_7_out);
  ROM #(.addrWidth(10), .dataWidth(32), .Select("high")) rom_1 (.addr(IF_PC[11:2]), .data(IF_IR));
  // Probe on \总周期数 
  // Probe on \无条件分支数 
  // Probe on \条件分支成功数 
  // Probe on \插入气泡数 
  // Probe on \LoadUse次数 
  xor xor_1 (error, BranchTaken, EX_PredictJump);
  IF__ID if_id_1 (
    .IR(IF_IR), .PC(IF_PC), .PC_4(IF_PC_4), .IR_2(ID_IR), .PC_2(ID_PC), .PC_4_2(if_id_1_pc_4_2), .RST(RST),
    .CLK(CLK), .en(and_8_out), .BranchTaken(error), .PredictJump(PredictJump),
    .PredictJump_2(if_id_1_predictjump_2));
  and and_8 (and_8_out, ~stall, not_4_out);  // AND_Gate
  // Probe on IF_PC[11:0]
  // Probe on WB_PC[19:0]
  // RiscV_Probe riscv_probe_5: pin names not known; wires that end beside it: WB_IR
  not not_4 (not_4_out, halt);
  // Probe on EX_PC[11:0]
  // Probe on ID_PC[11:0]
  \单周期硬布线控制器  \u_单周期硬布线控制器_1  (
    .Funct({ID_IR[30], ID_IR[25], ID_IR[14:12]}), .OP(ID_IR[6:2]), .ALU_OP(\单周期硬布线控制器_1_alu_op ),
    .MemToReg(\单周期硬布线控制器_1_memtoreg ), .MemWrite(\单周期硬布线控制器_1_memwrite ), .ALU_SRC(\单周期硬布线控制器_1_alu_src ),
    .RegWrite(\单周期硬布线控制器_1_regwrite ), .ecall(ID_ecall), .S_type(\单周期硬布线控制器_1_s_type ),
    .Jalr(\单周期硬布线控制器_1_jalr ), .Beq(\单周期硬布线控制器_1_beq ), .JAL(\单周期硬布线控制器_1_jal ), .Bne(\单周期硬布线控制器_1_bne ),
    .in_3(ID_IR[21]), .LB(\单周期硬布线控制器_1_lb ), .BGE(\单周期硬布线控制器_1_bge ));  // open: uret, CSRRSI, CSRRCI
  Multiplexer #(.select(1), .width(5), .disabled("Z"), .enable("false")) multiplexer_5 (
    .in0(ID_IR[19:15]), .in1(5'b10001), .out(multiplexer_5_out), .sel(ID_ecall));
  Multiplexer #(.select(1), .width(5), .disabled("Z"), .enable("false")) multiplexer_6 (
    .in0(ID_IR[24:20]), .in1(5'b01010), .out(multiplexer_6_out), .sel(ID_ecall));
  assign bit_extender_1_out = {{20{ID_IR[31]}}, ID_IR[31:20]};  // Bit_Extender bit_extender_1
  assign bit_extender_2_out = {{20{ID_IR[31]}}, {ID_IR[31:25], ID_IR[11:7]}};  // Bit_Extender bit_extender_2
  // Probe on M_PC[11:0]
  D_Flip_Flop #(.trigger("high"), .Pre_Clr_Positions("LEGACY"), .NegatePresetClear("false"), .enable("true"), .NewFFLayout("false")) d_ff_1 (.Q(d_ff_1_q));  // open: clk, D, Qn, preset, en, reset
  // Probe on 13'hc
  Multiplexer #(.select(1), .width(32), .disabled("Z"), .enable("false")) multiplexer_7 (
    .in0(bit_extender_1_out), .in1(bit_extender_2_out), .out(multiplexer_7_out), .sel(\单周期硬布线控制器_1_s_type ));
  assign bit_extender_3_out = {{20{ID_IR[31]}}, {ID_IR[31], ID_IR[7], ID_IR[30:25], ID_IR[11:8]}};  // Bit_Extender bit_extender_3
  assign bit_extender_4_out = {{12{ID_IR[31]}}, {ID_IR[31], ID_IR[19:12], ID_IR[20], ID_IR[30:21]}};  // Bit_Extender bit_extender_4
  // Probe on WB_PC[11:0]
  Comparator #(.width(13), .mode("twosComplement")) comparator_3 (
    .a(CNT_num), .b(13'hc), .eq(comparator_3_eq), .lt(comparator_3_lt));  // open: gt
  Clock #(.highDuration(1), .lowDuration(1)) clock_2 (.out(clock_2_out));
  nand nand_1 (nand_1_out, d_ff_1_q, comparator_3_eq);
  Counter #(.width(13), .max('h1fff), .ongoal("stay"), .trigger("rising"), .behavior("old")) counter_2 (
    .count(comparator_3_lt), .Q(CNT_num), .clk(clock_2_out));  // open: load, D, carry, clr, preset
  Regifile_Falling_Edge regifile_falling_edge_1 (
    .Din(RDin), .Clk(CLK), .R1(regifile_falling_edge_1_r1), .R2(regifile_falling_edge_1_r2), .WE(RegWrite),
    .W_num(WB_rd), .R1_num(multiplexer_5_out), .R2_num(multiplexer_6_out));
  assign CLK = nand_1_out ? clock_2_out : 1'bz;  // Controlled_Buffer controlled_buffer_1
  or or_4 (or_4_out, error, stall);
  ID__EX id_ex_1 (
    .R1(regifile_falling_edge_1_r1), .R2(regifile_falling_edge_1_r2), .imm(multiplexer_7_out),
    .imm_b(bit_extender_3_out), .PC(ID_PC), .PC_4(if_id_1_pc_4_2), .IR(ID_IR), .rs1Forward(rs1Forward),
    .rs2Forward(rs2Forward), .R1_2(id_ex_1_r1_2), .R2_2(id_ex_1_r2_2), .imm_2(id_ex_1_imm_2),
    .imm_b_2(id_ex_1_imm_b_2), .PC_2(EX_PC), .PC_4_2(EX_PC_4), .IR_2(EX_IR),
    .rs1Forward_2(id_ex_1_rs1forward_2), .rs2Forward_2(id_ex_1_rs2forward_2), .RST_2(RST),
    .imm_j(bit_extender_4_out), .imm_j_2(id_ex_1_imm_j_2), .BGE_2(\单周期硬布线控制器_1_bge ), .LB(\单周期硬布线控制器_1_lb ),
    .JALR(\单周期硬布线控制器_1_jalr ), .JAL(\单周期硬布线控制器_1_jal ), .Beq(\单周期硬布线控制器_1_beq ), .Bne(\单周期硬布线控制器_1_bne ),
    .MemToReg(\单周期硬布线控制器_1_memtoreg ), .MemWrite(\单周期硬布线控制器_1_memwrite ), .AluSrcB(\单周期硬布线控制器_1_alu_src ),
    .RegWrite(\单周期硬布线控制器_1_regwrite ), .ecall(ID_ecall), .AluOP(\单周期硬布线控制器_1_alu_op ), .rd(ID_IR[11:7]),
    .BGE_4(BGE), .LB_2(id_ex_1_lb_2), .JALR_2(JALR), .JAL_2(JAL), .Beq_2(Beq), .Bne_2(Bne),
    .MemToReg_2(EX_MemToReg), .MemWrite_2(id_ex_1_memwrite_2), .AluSrcB_2(id_ex_1_alusrcb_2),
    .RegWrite_2(EX_RegWrite), .ecall_2(EX_ecall), .AluOP_2(id_ex_1_aluop_2), .rd_2(EX_rd), .CLK(CLK),
    .en(not_4_out), .flush(or_4_out), .BGE(if_id_1_predictjump_2), .BGE_3(EX_PredictJump));  // open: RST
  Pull_Resistor #(.pull(1)) pull_resistor_2 (.node(CLK));
  Multiplexer #(.select(2), .width(32), .disabled("Z"), .enable("false")) multiplexer_8 (
    .in0(id_ex_1_r1_2), .in1(MEM_R), .in2(RDin), .out(EX_R1), .sel(id_ex_1_rs1forward_2));  // open: in3
  Multiplexer #(.select(2), .width(32), .disabled("Z"), .enable("false")) multiplexer_9 (
    .in0(id_ex_1_r2_2), .in1(MEM_R), .in2(RDin), .out(EX_R2), .sel(id_ex_1_rs2forward_2));  // open: in3
  Shifter #(.width(32), .shift("ll")) shifter_1 (.in(id_ex_1_imm_b_2), .\dist (5'b00001), .out(shifter_1_out));
  Adder #(.width(32)) adder_2 (.a(shifter_1_out), .b(EX_PC), .out(B_Addr));  // open: cin, cout
  Shifter #(.width(32), .shift("ll")) shifter_2 (.in(id_ex_1_imm_j_2), .\dist (5'b00001), .out(shifter_2_out));
  Adder #(.width(32)) adder_3 (.a(shifter_2_out), .b(EX_PC), .out(J_Addr));  // open: cin, cout
  or or_5 (or_5_out, JAL, JALR);
  and and_9 (and_9_out, stall, ~halt);  // AND_Gate
  Multiplexer #(.select(1), .width(32), .disabled("Z"), .enable("false")) multiplexer_10 (
    .in0(EX_R2), .in1(id_ex_1_imm_2), .out(multiplexer_10_out), .sel(id_ex_1_alusrcb_2));
  Counter #(.width(16), .max('hffff), .ongoal("wrap"), .trigger("rising"), .behavior("old")) counter_3 (
    .count(or_5_out), .Q(\无条件分支数 ), .clk(CLK), .clr(RST));  // open: load, D, carry, preset
  Counter #(.width(16), .max('hffff), .ongoal("wrap"), .trigger("rising"), .behavior("old")) counter_4 (
    .count(Branch), .Q(\条件分支成功数 ), .clk(CLK), .clr(RST));  // open: load, D, carry, preset
  Counter #(.width(16), .max('hffff), .ongoal("wrap"), .trigger("rising"), .behavior("old")) counter_5 (
    .count(and_9_out), .Q(\LoadUse次数 ), .clk(CLK), .clr(RST));  // open: load, D, carry, preset
  ALU alu_1 (
    .X(EX_R1), .Y(multiplexer_10_out), .AluOP(id_ex_1_aluop_2), .Equal(tunnel_t), .Result(R),
    .out_4(tunnel_t_t), .out_6(tunnel));  // open: Result_2
  EX__MEM ex_mem_1 (
    .LB(id_ex_1_lb_2), .JALR(JALR), .MemToReg(EX_MemToReg), .MemWrite(id_ex_1_memwrite_2),
    .RegWrite(EX_RegWrite), .R1(EX_R1), .rd(EX_rd), .R(R), .MD(EX_R2), .IR(EX_IR), .PC(EX_PC),
    .PC_4(EX_PC_4), .LB_2(ex_mem_1_lb_2), .JALR_2(ex_mem_1_jalr_2), .MemToReg_2(ex_mem_1_memtoreg_2),
    .MemWrite_2(MemWrite), .RegWrite_2(MEM_RegWrite), .R1_2(MEM_R1), .rd_2(MEM_rd), .R_2(MEM_R), .MD_2(MDin),
    .IR_2(MEM_IR), .PC_2(M_PC), .PC_4_2(ex_mem_1_pc_4_2), .RST(RST), .CLK(CLK), .JAL(JAL),
    .JAL_2(ex_mem_1_jal_2), .ecall(EX_ecall), .RegWrite_3(MEM_ecall), .en(not_4_out));
  RAM #(.addrWidth(10), .dataWidth(32), .bus("separate"), .Select("high")) ram_1 (
    .addr(MEM_R[11:2]), .din(MDin), .data(ram_1_data), .str(MemWrite), .sel(1'b1), .clk(CLK), .ld(1'b1),
    .clr(RST));
  MEM__WB mem_wb_1 (
    .JALR(ex_mem_1_jalr_2), .JAL(ex_mem_1_jal_2), .MenToReg(ex_mem_1_memtoreg_2), .RegWrite(MEM_RegWrite),
    .rd(MEM_rd), .R(MEM_R), .Dataout(ram_1_data), .IR(MEM_IR), .PC(M_PC), .PC_4(ex_mem_1_pc_4_2),
    .JALR_2(WB_JALR), .JAL_2(WB_JAL), .MemToReg(MemToReg), .RegWrite_2(RegWrite), .rd_2(WB_rd),
    .R_2(mem_wb_1_r_2), .Dataout_2(mem_wb_1_dataout_2), .IR_2(WB_IR), .PC_2(WB_PC), .PC_4_2(WB_PC_4),
    .RST(RST), .CLK(CLK), .LB(ex_mem_1_lb_2), .LB_2(LB), .Addr_2(Addr), .addr(MEM_R[1:0]), .R1(MEM_R1),
    .R1_2(WB_R1), .R2(MDin), .R2_2(WB_R2), .ecall(MEM_ecall), .ecall_2(WB_ecall), .en(not_4_out));
  or or_6 (or_6_out, WB_JAL, WB_JALR);
  Priority_Encoder #(.select(2), .disabled("Z")) priority_encoder_3 (
    .in0(1'b1), .in1(MemToReg), .in2(or_6_out), .out(priority_encoder_3_out));  // open: in3, gs, en_out, en_in
  Multiplexer #(.select(2), .width(32), .disabled("Z"), .enable("false")) multiplexer_11 (
    .in0(mem_wb_1_r_2), .in1(mem_wb_1_dataout_2), .in2(WB_PC_4), .out(word), .sel(priority_encoder_3_out));  // open: in3
  assign bit_extender_5_out = {{24{word[7]}}, word[7:0]};  // Bit_Extender bit_extender_5
  assign bit_extender_6_out = {{24{word[15]}}, word[15:8]};  // Bit_Extender bit_extender_6
  assign bit_extender_7_out = {{24{word[23]}}, word[23:16]};  // Bit_Extender bit_extender_7
  assign bit_extender_8_out = {{24{word[31]}}, word[31:24]};  // Bit_Extender bit_extender_8
  Multiplexer #(.select(1), .width(32), .disabled("Z"), .enable("false")) multiplexer_12 (
    .in0(word), .in1(\byte ), .out(RDin), .sel(LB));
  Multiplexer #(.select(2), .width(32), .disabled("Z"), .enable("false")) multiplexer_13 (
    .in0(bit_extender_5_out), .in1(bit_extender_6_out), .in2(bit_extender_7_out), .in3(bit_extender_8_out),
    .out(\byte ), .sel(Addr));

  // Other names for the same wires on the sheet: ID_rd[4:0] = ID_IR[11:7]; MEM_PC[31:0] = M_PC

  // Notes on the sheet:
  //   中断源
  //   时空图监测，可删除
  //   中断等待指示
  //   数码管输出
  //   指令存储器
  //   contents of rom_1 (hex, n*v repeats v):
  //   100493 100006f 100493 200913 300993 100006f 100493 200913 300993 100006f 100493 200913 300993
  //   100006f 100493 200913 300993 3d0000ef 100413 100493 1f49493 900533 2200893 73 24d493 48463 fedff06f
  //   900533 2200893 73 100493 249493 900533 2200893 73 48463 fedff06f 100493 1f49493 900533 2200893 73
  //   4034d493 900533 2200893 73 4044d493 900533 2200893 73 4044d493 900533 2200893 73 4044d493 900533
  //   2200893 73 4044d493 900533 2200893 73 4044d493 900533 2200893 73 4044d493 900533 2200893 73 4044d493
  //   900533 2200893 73 100413 1f41993 41f9d993 433 c00913 300b13 140413 f47413 800293 100313 499993
  //   89e9b3 1300533 2200893 73 406282b3 fe0294e3 140413 f00f93 1f47433 1c41413 800293 100313 49d993
  //   89e9b3 1300533 2200893 73 406282b3 fe0294e3 1c45413 406b0b33 b0463 f95ff06f 2b3 fff2c293 829293
  //   ff2e293 500533 2200893 73 fff00413 493 84a023 140413 448493 84a023 140413 448493 84a023 140413
  //   448493 84a023 140413 448493 84a023 140413 448493 84a023 140413 448493 84a023 140413 448493 84a023
  //   140413 448493 84a023 140413 448493 84a023 140413 448493 84a023 140413 448493 84a023 140413 448493
  //   84a023 140413 448493 84a023 140413 448493 84a023 140413 448493 84a023 140413 448493 140413 433
  //   3c00493 42983 4aa03 149a2b3 28663 134a023 1442023 ffc48493 fe9412e3 800533 2200893 73 440413 3c00493
  //   fc9416e3 a00893 73 100293 300313 800493 849493 7648493 900533 2200893 73 800e13 5494b3 6494b3 900533
  //   2200893 73 fffe0e13 fe0e14e3 a00893 73 100293 300313 800493 849493 7648493 1449493 900533 2200893 73
  //   800e13 54d4b3 64d4b3 900533 2200893 73 fffe0e13 fe0e14e3 a00893 73 313 1000e13 8400493 849493
  //   8348493 400913 891913 490913 849493 8248493 849493 8148493 891913 490913 891913 490913 932023
  //   12484b3 430313 fffe0e13 fe0e18e3 2000e13 313 30483 900533 2200893 73 130313 fffe0e13 fe0e14e3 a00893
  //   73 f00493 900533 2200893 73 fff48493 fe04d8e3 a00893 73 413 140413 800533 2200893 73 240413 800533
  //   2200893 73 340413 800533 2200893 73 440413 800533 2200893 73 540413 800533 2200893 73 640413 800533
  //   2200893 73 740413 800533 2200893 73 840413 800533 2200893 2200893 73 8067
  //   控制位
  //   JAL
  //   JALR
  //   LB
  //   BGE
  //   流水调试日志用
  //   暂停节拍，不能为0
  //   Beq
  //   Bne
  //   MemToReg
  //   MemWrite
  //   AluOP
  //   AluSrcB
  //   RegWrite
  //   S_Type
  //   戳工具置1进入计数暂停模式，ctrl+k时钟自动运行到对应节拍暂停
  //   ctrl+k关闭时钟连续运行，将控制位置零，进入单步调试模式调试
  //   可计数暂停的时钟源
  //   LB
  //   JALR
  //   JAL
  //   MemWrite
  //   AluOP
  //   AluSrcB
  //   为方便自动评测，需要输出流水线各段保存的PC值，注意是PC不是PC+4，另外ID段寄存器写入信息，Mem段内存写入信息也要输出
  //   LB
  //   JALR
  //   JAL
  //   MemToReg
  //   数据存储器
endmodule

module MAX (
  input  [15:0] Y,
  input  [15:0] X,
  input  [2:0] Y_num,
  input  [2:0] X_num,
  output [15:0] MAX,
  output [2:0] MAX_num
);

  wire comparator_1_eq, comparator_1_gt, or_1_out;

  Multiplexer #(.select(1), .width(16), .disabled("Z"), .enable("false")) multiplexer_1 (
    .in0(Y), .in1(X), .out(MAX), .sel(or_1_out));
  Comparator #(.width(16), .mode("unsigned")) comparator_1 (
    .a(X), .b(Y), .gt(comparator_1_gt), .eq(comparator_1_eq));  // open: lt
  or or_1 (or_1_out, comparator_1_gt, comparator_1_eq);
  Multiplexer #(.select(1), .width(3), .disabled("Z"), .enable("false")) multiplexer_2 (
    .in0(Y_num), .in1(X_num), .out(MAX_num), .sel(or_1_out));
endmodule

module FSM (
  input  S0,
  input  S1,
  input  BranchTaken,
  output N0,
  output N1
);

  wire and_1_out, and_2_out, and_3_out, and_4_out, not_1_out, not_2_out, not_3_out, not_4_out, not_5_out;

  not not_1 (not_1_out, S1);
  and and_1 (and_1_out, not_1_out, not_2_out, BranchTaken);
  not not_2 (not_2_out, S0);
  and and_2 (and_2_out, S1, not_3_out, not_4_out);
  not not_3 (not_3_out, S0);
  not not_4 (not_4_out, BranchTaken);
  and and_3 (and_3_out, S0, BranchTaken);
  and and_4 (and_4_out, S1, not_5_out);
  not not_5 (not_5_out, S0);
  or or_1 (N0, and_1_out, and_2_out);
  or or_2 (N1, and_3_out, and_4_out);
endmodule

module Regifile_Falling_Edge (
  input  [31:0] Din,
  input  Clk,
  input  WE,
  input  [4:0] R1_num,
  input  [4:0] W_num,
  input  [4:0] R2_num,
  output [31:0] R1,
  output [31:0] R2
);

  // RegisterFile registerfile_1: pin names not known; wires that end beside it: Din, Clk, WE, W_num, R1_num, R2_num, R1, R2
endmodule
